// Logisim project 658_Computer.circ as structural Verilog
module Motherboard (
  input  RESET_SWITCH,
  input  SNES_CONTROLLER_DATA_0,
  input  PS2_CLOCK_0,
  input  SNES_CONTROLLER_DATA_1,
  input  PS2_DATA_0,
  input  SNES_CONTROLLER_DATA_2,
  input  PS2_CLOCK_2,
  input  SNES_CONTROLLER_DATA_3,
  input  PS2_DATA_2,
  output IOR,
  output IOG,
  output IOB,
  output HSYNC,
  output VSYNC,
  output [7:0] out_15,
  output SNES_CONTROLLER_CLOCCK,
  output SNES_CONTROLLER_LATCH
);

  wire adv7125_1_iob_b, and_5_out, and_6_out, and_7_out, and_8_out, BLIT_0_DONE_IRQ_B, BLIT_1_DONE_IRQ_B,
       BLIT_2_DONE_IRQ_B, BLIT_3_DONE_IRQ_B, CH_0_RWB, CH_0_RWB_B, CH_1_RWB, CH_1_RWB_B, CH_2_RWB,
       CH_2_RWB_B, CH_3_RWB, CH_3_RWB_B, CLEAR_IRQ_BLIT_0, CLEAR_IRQ_BLIT_1, CLEAR_IRQ_BLIT_2,
       CLEAR_IRQ_BLIT_3, CLEAR_IRQ_VERTICAL_RASTER, clock_1_out, clock_generator_1_clock_out,
       device_strobe_1_channel_0_b, device_strobe_1_channel_1_b, device_strobe_1_channel_2_b,
       device_strobe_1_channel_3_b, DONE_IRQ_ENABLE_BLIT_0, DONE_IRQ_ENABLE_BLIT_1, DONE_IRQ_ENABLE_BLIT_2,
       DONE_IRQ_ENABLE_BLIT_3, DONE_RASTERISING_MPU0_BLIT_0_B, DONE_RASTERISING_MPU0_BLIT_1_B,
       DONE_RASTERISING_MPU0_BLIT_2_B, DONE_RASTERISING_MPU0_BLIT_3_B, DONE_RASTERISING_MPU1_BLIT_0_B,
       DONE_RASTERISING_MPU1_BLIT_1_B, DONE_RASTERISING_MPU1_BLIT_2_B, DONE_RASTERISING_MPU1_BLIT_3_B,
       DONE_RASTERISING_MPU2_BLIT_0_B, DONE_RASTERISING_MPU2_BLIT_1_B, DONE_RASTERISING_MPU2_BLIT_2_B,
       DONE_RASTERISING_MPU2_BLIT_3_B, DONE_RASTERISING_MPU3_BLIT_0_B, DONE_RASTERISING_MPU3_BLIT_1_B,
       DONE_RASTERISING_MPU3_BLIT_2_B, DONE_RASTERISING_MPU3_BLIT_3_B, DONE_SHIFTING_B,
       EIGHT_BIT_MODE_BLIT_0, EIGHT_BIT_MODE_BLIT_1, EIGHT_BIT_MODE_BLIT_2, EIGHT_BIT_MODE_BLIT_3,
       FRAME_BUFFER_INDEX, FST, graphics_board_1_main_memory_valid_b, graphics_board_2_main_memory_valid_b,
       graphics_board_3_main_memory_valid_b, graphics_board_4_main_memory_valid_b,
       LINE_WIDTH_HIGH_OE_BLIT_0_B, LINE_WIDTH_HIGH_OE_BLIT_1_B, LINE_WIDTH_HIGH_OE_BLIT_2_B,
       LINE_WIDTH_HIGH_OE_BLIT_3_B, LINE_WIDTH_LE_BLIT_0, LINE_WIDTH_LE_BLIT_1, LINE_WIDTH_LE_BLIT_2,
       LINE_WIDTH_LE_BLIT_3, LINE_WIDTH_LOW_OE_BLIT_0_B, LINE_WIDTH_LOW_OE_BLIT_1_B,
       LINE_WIDTH_LOW_OE_BLIT_2_B, LINE_WIDTH_LOW_OE_BLIT_3_B, main_memory_gateway_1_memory_oeb_out,
       main_memory_gateway_1_memory_web_out, MEMORY_LOCKOUT_CHANNEL_0, MEMORY_LOCKOUT_CHANNEL_1,
       MEMORY_LOCKOUT_CHANNEL_2, MEMORY_LOCKOUT_CHANNEL_3,
       microcontroller_board_kernal_and_user_1_clock_enable_b,
       microcontroller_board_kernal_and_user_1_main_memory_oeb,
       microcontroller_board_kernal_and_user_1_main_memory_valid_b,
       microcontroller_board_kernal_and_user_1_main_memory_web,
       microcontroller_board_kernal_and_user_1_reset, microcontroller_board_kernal_and_user_2_clock_enable_b,
       microcontroller_board_kernal_and_user_2_main_memory_oeb,
       microcontroller_board_kernal_and_user_2_main_memory_valid_b,
       microcontroller_board_kernal_and_user_2_main_memory_web,
       microcontroller_board_kernal_and_user_2_reset, microcontroller_board_kernal_only_1_clock_enable_b,
       microcontroller_board_kernal_only_1_main_memory_oeb,
       microcontroller_board_kernal_only_1_main_memory_valid_b,
       microcontroller_board_kernal_only_1_main_memory_web, microcontroller_board_kernal_only_1_reset,
       microcontroller_board_kernal_only_2_clock_enable_b,
       microcontroller_board_kernal_only_2_main_memory_oeb,
       microcontroller_board_kernal_only_2_main_memory_valid_b,
       microcontroller_board_kernal_only_2_main_memory_web, microcontroller_board_kernal_only_2_reset,
       MPU0_IRQ_B, MPU0_NMI_B, MPU0_RES_B, MPU1_IRQ_B, MPU1_NMI_B, MPU1_RES_B, MPU2_IRQ_B, MPU2_NMI_B,
       MPU2_RES_B, MPU3_IRQ_B, MPU3_NMI_B, MPU3_RES_B, MPU_0_DEVICE_RWB, MPU_0_DEVICE_VALID_B,
       NMIB_LOCKOUT_CHANNEL_0, NMIB_LOCKOUT_CHANNEL_1, NMIB_LOCKOUT_CHANNEL_2, NMIB_LOCKOUT_CHANNEL_3,
       PIXEL_CLOCK_SCK, PIXEL_CLOCK_SDI, PIXEL_CLOCK_SEN, ps2_input_device_1_oe_high_b,
       ps2_input_device_1_oe_low_b, ps2_input_device_1_reset_ps2_b, pull_resistor_37_node,
       pull_resistor_38_node, pull_resistor_39_node, pull_resistor_40_node, pull_resistor_41_node,
       pull_resistor_42_node, pull_resistor_43_node, pull_resistor_44_node, pull_resistor_45_node,
       pull_resistor_46_node, quick_timing_circuit_1_reset_0_b, RESET, SEL0, SEL2, SEL4, SEL6, SLW,
       snes_controller_device_1_counter_reset_b, snes_controller_device_1_oe_controller_0_high_b,
       snes_controller_device_1_oe_controller_0_low_b, snes_controller_device_1_oe_controller_1_high_b,
       snes_controller_device_1_oe_controller_1_low_b, snes_controller_device_1_oe_controller_2_high_b,
       snes_controller_device_1_oe_controller_2_low_b, snes_controller_device_1_oe_controller_3_high_b,
       snes_controller_device_1_oe_controller_3_low_b, START_RASTERISING_BLIT_0, START_RASTERISING_BLIT_1,
       START_RASTERISING_BLIT_2, START_RASTERISING_BLIT_3, TRANSPARENCY_TESTING_BLIT_0_B,
       TRANSPARENCY_TESTING_BLIT_1_B, TRANSPARENCY_TESTING_BLIT_2_B, TRANSPARENCY_TESTING_BLIT_3_B,
       VERTICAL_DONE_IRQ_B, VERTICAL_RASTER_HIGH_OEB, VERTICAL_RASTER_IRQ_ENABLE, VERTICAL_RASTER_LE,
       VERTICAL_RASTER_LOW_OEB, video_board_1_blank_b, video_board_1_video_clock;
  wire [1:0] HORIZONTAL_PIXEL_DOUBLING, MPU0_CHANNEL, MPU1_CHANNEL, MPU2_CHANNEL, MPU3_CHANNEL,
       MPU_0_DEVICE_CHANNEL, MPU_1_DEVICE_CHANNEL, MPU_2_DEVICE_CHANNEL, MPU_3_DEVICE_CHANNEL;
  wire [3:0] CH_0_DEVICE_ADDRESS, CH_1_DEVICE_ADDRESS, CH_2_DEVICE_ADDRESS, CH_3_DEVICE_ADDRESS,
       FOUR_BIT_HIGH_NYBBLE_BLIT_0, FOUR_BIT_HIGH_NYBBLE_BLIT_1, FOUR_BIT_HIGH_NYBBLE_BLIT_2,
       FOUR_BIT_HIGH_NYBBLE_BLIT_3, MPU_0_DEVICE_ADDRESS, undriven;
  wire [3:2] pull_resistor_8_node, pull_resistor_17_node, pull_resistor_26_node, pull_resistor_35_node;
  wire [5:0] CH_0_DEVICE_IDENTIFIER, CH_1_DEVICE_IDENTIFIER, CH_2_DEVICE_IDENTIFIER, CH_3_DEVICE_IDENTIFIER,
       MPU_0_DEVICE_IDENTIFIER;
  wire [7:0] BLIT_0_REMAINING_WIDTH_W0_7, BLIT_1_REMAINING_WIDTH_W0_7, BLIT_2_REMAINING_WIDTH_W0_7,
       BLIT_3_REMAINING_WIDTH_W0_7, CH_0_D, CH_1_D, CH_2_D, CH_3_D, HORIZONTAL_ACTIVE_H4_11,
       HORIZONTAL_BACK_PORCH_H4_11, HORIZONTAL_FRONT_PORCH_H4_11, HORIZONTAL_SYNC_H4_11,
       main_memory_gateway_1_d_out_right, microcontroller_board_kernal_and_user_1_main_memory_d_out,
       microcontroller_board_kernal_and_user_2_main_memory_d_out,
       microcontroller_board_kernal_only_1_main_memory_d_out,
       microcontroller_board_kernal_only_2_main_memory_d_out, MPU_0_ABILITY, MPU_0_DEVICE_D, MPU_1_ABILITY,
       MPU_2_ABILITY, MPU_3_ABILITY, n3_to_8_decoder_lvc138_1_p5, n3_to_8_decoder_lvc138_2_p5,
       n3_to_8_decoder_lvc138_3_p5, PALETTE_INDEX_P0_7, snes_input_board_1_shift_register_out,
       TRANSPARENCU_INDEX_BLIT_0, TRANSPARENCU_INDEX_BLIT_1, TRANSPARENCU_INDEX_BLIT_2,
       TRANSPARENCU_INDEX_BLIT_3, VERTICAL_ACTIVE_V4_11, VERTICAL_BACK_PORCH_V0_7, VERTICAL_FRONT_PORCH_V0_7,
       VERTICAL_RASTER_V0_7, VERTICAL_SYNC_V0_7, video_board_1_blue, video_board_1_green, video_board_1_red;
  wire [7:1] SELECTOR;
  wire [8:1] and_1_out, and_2_out, and_3_out, and_4_out;
  wire [11:0] LINE_WIDTH_BLIT_0, LINE_WIDTH_BLIT_1, LINE_WIDTH_BLIT_2, LINE_WIDTH_BLIT_3;
  wire [23:0] DESTINATION_ADDRESS_BLIT_0, DESTINATION_ADDRESS_BLIT_1, DESTINATION_ADDRESS_BLIT_2,
       DESTINATION_ADDRESS_BLIT_3, main_memory_gateway_1_maddress_out_a0_23,
       microcontroller_board_kernal_and_user_1_main_memory_address,
       microcontroller_board_kernal_and_user_2_main_memory_address,
       microcontroller_board_kernal_only_1_main_memory_address,
       microcontroller_board_kernal_only_2_main_memory_address, SOURCE_ADDRESS_BLIT_0, SOURCE_ADDRESS_BLIT_1,
       SOURCE_ADDRESS_BLIT_2, SOURCE_ADDRESS_BLIT_3, undriven_2;
  wire [39:0] T1, T2;

  and and_1 (and_1_out[1], DONE_RASTERISING_MPU0_BLIT_0_B, DONE_RASTERISING_MPU0_BLIT_1_B, DONE_RASTERISING_MPU0_BLIT_2_B, DONE_RASTERISING_MPU0_BLIT_3_B);
  and and_2 (and_2_out[1], DONE_RASTERISING_MPU1_BLIT_0_B, DONE_RASTERISING_MPU1_BLIT_1_B, DONE_RASTERISING_MPU1_BLIT_2_B, DONE_RASTERISING_MPU1_BLIT_3_B);
  and and_3 (and_3_out[1], DONE_RASTERISING_MPU2_BLIT_0_B, DONE_RASTERISING_MPU2_BLIT_1_B, DONE_RASTERISING_MPU2_BLIT_2_B, DONE_RASTERISING_MPU2_BLIT_3_B);
  and and_4 (and_4_out[1], DONE_RASTERISING_MPU3_BLIT_0_B, DONE_RASTERISING_MPU3_BLIT_1_B, DONE_RASTERISING_MPU3_BLIT_2_B, DONE_RASTERISING_MPU3_BLIT_3_B);
  and and_5 (and_5_out, RESET, MPU0_RES_B);
  Pull_Resistor #(.pull(1)) pull_resistor_1 (.node(and_1_out[2]));
  Pull_Resistor #(.pull(1)) pull_resistor_2 (.node(and_1_out[3]));
  Pull_Resistor #(.pull(1)) pull_resistor_3 (.node(and_1_out[4]));
  Pull_Resistor #(.pull(1)) pull_resistor_4 (.node(and_1_out[5]));
  Pull_Resistor #(.pull(1)) pull_resistor_5 (.node(and_1_out[6]));
  Pull_Resistor #(.pull(1)) pull_resistor_6 (.node(and_1_out[7]));
  Pull_Resistor #(.pull(1)) pull_resistor_7 (.node(and_1_out[8]));
  Pull_Resistor #(.pull(1)) pull_resistor_8 (.node(pull_resistor_8_node[2]));
  Pull_Resistor #(.pull(1)) pull_resistor_9 (.node(pull_resistor_8_node[3]));
  and and_6 (and_6_out, RESET, MPU1_RES_B);
  Pull_Resistor #(.pull(1)) pull_resistor_10 (.node(and_2_out[2]));
  Pull_Resistor #(.pull(1)) pull_resistor_11 (.node(and_2_out[3]));
  Pull_Resistor #(.pull(1)) pull_resistor_12 (.node(and_2_out[4]));
  Pull_Resistor #(.pull(1)) pull_resistor_13 (.node(and_2_out[5]));
  Pull_Resistor #(.pull(1)) pull_resistor_14 (.node(and_2_out[6]));
  Pull_Resistor #(.pull(1)) pull_resistor_15 (.node(and_2_out[7]));
  Pull_Resistor #(.pull(1)) pull_resistor_16 (.node(and_2_out[8]));
  Pull_Resistor #(.pull(1)) pull_resistor_17 (.node(pull_resistor_17_node[2]));
  Pull_Resistor #(.pull(1)) pull_resistor_18 (.node(pull_resistor_17_node[3]));
  and and_7 (and_7_out, RESET, MPU2_RES_B);
  Pull_Resistor #(.pull(1)) pull_resistor_19 (.node(and_3_out[2]));
  Pull_Resistor #(.pull(1)) pull_resistor_20 (.node(and_3_out[3]));
  Pull_Resistor #(.pull(1)) pull_resistor_21 (.node(and_3_out[4]));
  Pull_Resistor #(.pull(1)) pull_resistor_22 (.node(and_3_out[5]));
  Pull_Resistor #(.pull(1)) pull_resistor_23 (.node(and_3_out[6]));
  Pull_Resistor #(.pull(1)) pull_resistor_24 (.node(and_3_out[7]));
  Pull_Resistor #(.pull(1)) pull_resistor_25 (.node(and_3_out[8]));
  Pull_Resistor #(.pull(1)) pull_resistor_26 (.node(pull_resistor_26_node[2]));
  Pull_Resistor #(.pull(1)) pull_resistor_27 (.node(pull_resistor_26_node[3]));
  and and_8 (and_8_out, RESET, MPU3_RES_B);
  Pull_Resistor #(.pull(1)) pull_resistor_28 (.node(and_4_out[2]));
  Pull_Resistor #(.pull(1)) pull_resistor_29 (.node(and_4_out[3]));
  Pull_Resistor #(.pull(1)) pull_resistor_30 (.node(and_4_out[4]));
  Pull_Resistor #(.pull(1)) pull_resistor_31 (.node(and_4_out[5]));
  Pull_Resistor #(.pull(1)) pull_resistor_32 (.node(and_4_out[6]));
  Pull_Resistor #(.pull(1)) pull_resistor_33 (.node(and_4_out[7]));
  Pull_Resistor #(.pull(1)) pull_resistor_34 (.node(and_4_out[8]));
  Pull_Resistor #(.pull(1)) pull_resistor_35 (.node(pull_resistor_35_node[2]));
  Pull_Resistor #(.pull(1)) pull_resistor_36 (.node(pull_resistor_35_node[3]));
  LED led_1 (.in(microcontroller_board_kernal_only_1_reset));
  LED led_2 (.in(microcontroller_board_kernal_and_user_1_reset));
  LED led_3 (.in(microcontroller_board_kernal_only_2_reset));
  LED led_4 (.in(microcontroller_board_kernal_and_user_2_reset));
  Microcontroller_Board_Kernal_Only microcontroller_board_kernal_only_1 (
    .DEVICE_D_OUT(MPU_0_DEVICE_D), .MAIN_MEMORY_WEB(microcontroller_board_kernal_only_1_main_memory_web),
    .IRQ_IN({and_1_out, MPU0_IRQ_B}), .MPU_ABILITY(MPU_0_ABILITY), .DEVICE_ADDRESS(MPU_0_DEVICE_ADDRESS),
    .MAIN_MEMORY_OEB(microcontroller_board_kernal_only_1_main_memory_oeb),
    .MAIN_MEMORY_VALID_B(microcontroller_board_kernal_only_1_main_memory_valid_b), .RESET_1(and_5_out),
    .SELECTOR({SELECTOR[7], SEL6, SELECTOR[5], SEL4, SELECTOR[3], SEL2, SELECTOR[1], SEL0}),
    .NMI_B_IN({pull_resistor_8_node, NMIB_LOCKOUT_CHANNEL_0, MPU0_NMI_B}),
    .MAIN_MEMORY_LOCKOUT(MEMORY_LOCKOUT_CHANNEL_0), .DEVICE_D_IN(MPU_0_DEVICE_D),
    .MAIN_MEMORY_ADDRESS(microcontroller_board_kernal_only_1_main_memory_address), .FST(FST),
    .DEVICE_CHANNEL(MPU_0_DEVICE_CHANNEL), .MPU_CHANNEL_D0_1(MPU0_CHANNEL),
    .DEVICE_IDENTIFIER(MPU_0_DEVICE_IDENTIFIER),
    .MAIN_MEMORY_D_OUT(microcontroller_board_kernal_only_1_main_memory_d_out), .DEVICE_RWB(MPU_0_DEVICE_RWB),
    .RESET(microcontroller_board_kernal_only_1_reset), .T2(T2), .T1(T1),
    .DEVICE_VALID_B(MPU_0_DEVICE_VALID_B),
    .MAIN_MEMORY_D_IN(microcontroller_board_kernal_only_1_main_memory_d_out),
    .CLOCK_ENABLE_B(microcontroller_board_kernal_only_1_clock_enable_b));
  Microcontroller_Board_Kernal_And_User microcontroller_board_kernal_and_user_1 (
    .MAIN_MEMORY_VALID_B(microcontroller_board_kernal_and_user_1_main_memory_valid_b),
    .DEVICE_CHANNEL(MPU_1_DEVICE_CHANNEL), .RESET_1(and_6_out),
    .CLOCK_ENABLE_B(microcontroller_board_kernal_and_user_1_clock_enable_b), .T2(T2), .FST(FST),
    .IRQ_B_IN({and_2_out, MPU1_IRQ_B}), .DEVICE_D_IN(MPU_0_DEVICE_D), .T1(T1),
    .DEVICE_ADDRESS(MPU_0_DEVICE_ADDRESS),
    .MAIN_MEMORY_ADDRESS(microcontroller_board_kernal_and_user_1_main_memory_address),
    .NMI_B_IN({pull_resistor_17_node, NMIB_LOCKOUT_CHANNEL_1, MPU1_NMI_B}),
    .MAIN_MEMORY_LOCKOUT(MEMORY_LOCKOUT_CHANNEL_1), .MPU_CHANNEL_D0_1(MPU1_CHANNEL),
    .DEVICE_IDENTIFIER(MPU_0_DEVICE_IDENTIFIER), .MPU_ABILITY(MPU_1_ABILITY),
    .MAIN_MEMORY_D_IN(microcontroller_board_kernal_and_user_1_main_memory_d_out),
    .SELECTOR({SELECTOR[1], SEL0, SELECTOR[7], SEL6, SELECTOR[5], SEL4, SELECTOR[3], SEL2}),
    .DEVICE_VALID_B(MPU_0_DEVICE_VALID_B), .RESET(microcontroller_board_kernal_and_user_1_reset),
    .DEVICE_RWB(MPU_0_DEVICE_RWB), .MAIN_MEMORY_WEB(microcontroller_board_kernal_and_user_1_main_memory_web),
    .DEVICE_D_OUT(MPU_0_DEVICE_D),
    .MAIN_MEMORY_D_OUT(microcontroller_board_kernal_and_user_1_main_memory_d_out),
    .MAIN_MEMORY_OEB(microcontroller_board_kernal_and_user_1_main_memory_oeb));
  Microcontroller_Board_Kernal_Only microcontroller_board_kernal_only_2 (
    .DEVICE_D_OUT(MPU_0_DEVICE_D), .MAIN_MEMORY_WEB(microcontroller_board_kernal_only_2_main_memory_web),
    .IRQ_IN({and_3_out, MPU2_IRQ_B}), .MPU_ABILITY(MPU_2_ABILITY), .DEVICE_ADDRESS(MPU_0_DEVICE_ADDRESS),
    .MAIN_MEMORY_OEB(microcontroller_board_kernal_only_2_main_memory_oeb),
    .MAIN_MEMORY_VALID_B(microcontroller_board_kernal_only_2_main_memory_valid_b), .RESET_1(and_7_out),
    .SELECTOR({SELECTOR[3], SEL2, SELECTOR[1], SEL0, SELECTOR[7], SEL6, SELECTOR[5], SEL4}),
    .NMI_B_IN({pull_resistor_26_node, NMIB_LOCKOUT_CHANNEL_2, MPU2_NMI_B}),
    .MAIN_MEMORY_LOCKOUT(MEMORY_LOCKOUT_CHANNEL_2), .DEVICE_D_IN(MPU_0_DEVICE_D),
    .MAIN_MEMORY_ADDRESS(microcontroller_board_kernal_only_2_main_memory_address), .FST(FST),
    .DEVICE_CHANNEL(MPU_2_DEVICE_CHANNEL), .MPU_CHANNEL_D0_1(MPU2_CHANNEL),
    .DEVICE_IDENTIFIER(MPU_0_DEVICE_IDENTIFIER),
    .MAIN_MEMORY_D_OUT(microcontroller_board_kernal_only_2_main_memory_d_out), .DEVICE_RWB(MPU_0_DEVICE_RWB),
    .RESET(microcontroller_board_kernal_only_2_reset), .T2(T2), .T1(T1),
    .DEVICE_VALID_B(MPU_0_DEVICE_VALID_B),
    .MAIN_MEMORY_D_IN(microcontroller_board_kernal_only_2_main_memory_d_out),
    .CLOCK_ENABLE_B(microcontroller_board_kernal_only_2_clock_enable_b));
  Microcontroller_Board_Kernal_And_User microcontroller_board_kernal_and_user_2 (
    .MAIN_MEMORY_VALID_B(microcontroller_board_kernal_and_user_2_main_memory_valid_b),
    .DEVICE_CHANNEL(MPU_3_DEVICE_CHANNEL), .RESET_1(and_8_out),
    .CLOCK_ENABLE_B(microcontroller_board_kernal_and_user_2_clock_enable_b), .T2(T2), .FST(FST),
    .IRQ_B_IN({and_4_out, MPU3_IRQ_B}), .DEVICE_D_IN(MPU_0_DEVICE_D), .T1(T1),
    .DEVICE_ADDRESS(MPU_0_DEVICE_ADDRESS),
    .MAIN_MEMORY_ADDRESS(microcontroller_board_kernal_and_user_2_main_memory_address),
    .NMI_B_IN({pull_resistor_35_node, NMIB_LOCKOUT_CHANNEL_3, MPU3_NMI_B}),
    .MAIN_MEMORY_LOCKOUT(MEMORY_LOCKOUT_CHANNEL_3), .MPU_CHANNEL_D0_1(MPU3_CHANNEL),
    .DEVICE_IDENTIFIER(MPU_0_DEVICE_IDENTIFIER), .MPU_ABILITY(MPU_3_ABILITY),
    .MAIN_MEMORY_D_IN(microcontroller_board_kernal_and_user_2_main_memory_d_out),
    .SELECTOR({SELECTOR[5], SEL4, SELECTOR[3], SEL2, SELECTOR[1], SEL0, SELECTOR[7], SEL6}),
    .DEVICE_VALID_B(MPU_0_DEVICE_VALID_B), .RESET(microcontroller_board_kernal_and_user_2_reset),
    .DEVICE_RWB(MPU_0_DEVICE_RWB), .MAIN_MEMORY_WEB(microcontroller_board_kernal_and_user_2_main_memory_web),
    .DEVICE_D_OUT(MPU_0_DEVICE_D),
    .MAIN_MEMORY_D_OUT(microcontroller_board_kernal_and_user_2_main_memory_d_out),
    .MAIN_MEMORY_OEB(microcontroller_board_kernal_and_user_2_main_memory_oeb));
  LED led_5 (.in(microcontroller_board_kernal_only_1_clock_enable_b));
  LED led_6 (.in(microcontroller_board_kernal_and_user_1_clock_enable_b));
  LED led_7 (.in(microcontroller_board_kernal_only_2_clock_enable_b));
  LED led_8 (.in(microcontroller_board_kernal_and_user_2_clock_enable_b));
  Pull_Resistor #(.pull(1)) pull_resistor_37 (.node(pull_resistor_37_node));
  Pull_Resistor #(.pull(1)) pull_resistor_38 (.node(pull_resistor_38_node));
  Pull_Resistor #(.pull(1)) pull_resistor_39 (.node(pull_resistor_39_node));
  Pull_Resistor #(.pull(1)) pull_resistor_40 (.node(pull_resistor_40_node));
  Graphics_Board graphics_board_1 (
    .SOURCE_ADDRESS(SOURCE_ADDRESS_BLIT_0), .TRANSPARENCY_B(TRANSPARENCY_TESTING_BLIT_0_B),
    .DONE_IRQB(BLIT_0_DONE_IRQ_B), .D_OUT(microcontroller_board_kernal_only_1_main_memory_d_out),
    .D_IN(microcontroller_board_kernal_only_1_main_memory_d_out),
    .TRANSPARENCY_COLOUR_INDEX(TRANSPARENCU_INDEX_BLIT_0), .RESET_B(RESET),
    .LINE_WIDTH_REMAINING_W0_7(BLIT_0_REMAINING_WIDTH_W0_7),
    .DESTINATION_ADDRESS(DESTINATION_ADDRESS_BLIT_0),
    .MAIN_MEMORY_VALID_B(graphics_board_1_main_memory_valid_b),
    .REMAINING_WIDTH_LOW_OEB(LINE_WIDTH_LOW_OE_BLIT_0_B),
    .WEB(microcontroller_board_kernal_only_1_main_memory_web),
    .REMAINING_WIDTH_HIGH_OEB(LINE_WIDTH_HIGH_OE_BLIT_0_B), .LINE_WIDTH_0_11(LINE_WIDTH_BLIT_0),
    .ADDRESS_A0_23(microcontroller_board_kernal_only_1_main_memory_address),
    .MEMORY_LOCKOUT(MEMORY_LOCKOUT_CHANNEL_0), .HIGH_NYBBLE(FOUR_BIT_HIGH_NYBBLE_BLIT_0),
    .IRQ_CLEAR(CLEAR_IRQ_BLIT_0), .START_RASTERISING(START_RASTERISING_BLIT_0),
    .EIGHT_BIT(EIGHT_BIT_MODE_BLIT_0), .OEB(microcontroller_board_kernal_only_1_main_memory_oeb),
    .REMAINING_WIDTH_LE(LINE_WIDTH_LE_BLIT_0), .IRQ_ENABLE(DONE_IRQ_ENABLE_BLIT_0),
    .SELECTOR({SELECTOR[7], SEL6, SELECTOR[5], SEL4, SELECTOR[3], SEL2, SELECTOR[1], SEL0}));
  Memory_Lockout_And_Generator memory_lockout_and_generator_1 (
    .NMI_B(NMIB_LOCKOUT_CHANNEL_0), .MAIN_MEMORY_VALID_3_B(pull_resistor_37_node),
    .LOCKOUT(MEMORY_LOCKOUT_CHANNEL_0), .RESET(RESET), .ADDRESS_IN_A0_23(24'h4aaaaa),
    .WE_B(microcontroller_board_kernal_only_1_main_memory_oeb),
    .MAIN_MEMORY_VALID_1_B(microcontroller_board_kernal_only_1_main_memory_valid_b),
    .MAIN_MEMORY_VALID_2_B(graphics_board_1_main_memory_valid_b), .SLOW_SELECTOR(SLW),
    .GATEWAY_ENABLE_B(SEL6), .OE_B(microcontroller_board_kernal_only_1_main_memory_web),
    .ADDRESS_OUT_A0_23(microcontroller_board_kernal_only_1_main_memory_address));
  Graphics_Board graphics_board_2 (
    .SOURCE_ADDRESS(SOURCE_ADDRESS_BLIT_1), .TRANSPARENCY_B(TRANSPARENCY_TESTING_BLIT_1_B),
    .DONE_IRQB(BLIT_1_DONE_IRQ_B), .D_OUT(microcontroller_board_kernal_and_user_1_main_memory_d_out),
    .D_IN(microcontroller_board_kernal_and_user_1_main_memory_d_out),
    .TRANSPARENCY_COLOUR_INDEX(TRANSPARENCU_INDEX_BLIT_1), .RESET_B(RESET),
    .LINE_WIDTH_REMAINING_W0_7(BLIT_1_REMAINING_WIDTH_W0_7),
    .DESTINATION_ADDRESS(DESTINATION_ADDRESS_BLIT_1),
    .MAIN_MEMORY_VALID_B(graphics_board_2_main_memory_valid_b),
    .REMAINING_WIDTH_LOW_OEB(LINE_WIDTH_LOW_OE_BLIT_1_B),
    .WEB(microcontroller_board_kernal_and_user_1_main_memory_web),
    .REMAINING_WIDTH_HIGH_OEB(LINE_WIDTH_HIGH_OE_BLIT_1_B), .LINE_WIDTH_0_11(LINE_WIDTH_BLIT_1),
    .ADDRESS_A0_23(microcontroller_board_kernal_and_user_1_main_memory_address),
    .MEMORY_LOCKOUT(MEMORY_LOCKOUT_CHANNEL_1), .HIGH_NYBBLE(FOUR_BIT_HIGH_NYBBLE_BLIT_1),
    .IRQ_CLEAR(CLEAR_IRQ_BLIT_1), .START_RASTERISING(START_RASTERISING_BLIT_1),
    .EIGHT_BIT(EIGHT_BIT_MODE_BLIT_1), .OEB(microcontroller_board_kernal_and_user_1_main_memory_oeb),
    .REMAINING_WIDTH_LE(LINE_WIDTH_LE_BLIT_1), .IRQ_ENABLE(DONE_IRQ_ENABLE_BLIT_1),
    .SELECTOR({SELECTOR[1], SEL0, SELECTOR[7], SEL6, SELECTOR[5], SEL4, SELECTOR[3], SEL2}));
  Memory_Lockout_And_Generator memory_lockout_and_generator_2 (
    .NMI_B(NMIB_LOCKOUT_CHANNEL_1), .MAIN_MEMORY_VALID_3_B(pull_resistor_38_node),
    .LOCKOUT(MEMORY_LOCKOUT_CHANNEL_1), .RESET(RESET), .ADDRESS_IN_A0_23(24'h6bbbbb),
    .WE_B(microcontroller_board_kernal_and_user_1_main_memory_oeb),
    .MAIN_MEMORY_VALID_1_B(microcontroller_board_kernal_and_user_1_main_memory_valid_b),
    .MAIN_MEMORY_VALID_2_B(graphics_board_2_main_memory_valid_b), .SLOW_SELECTOR(SLW),
    .GATEWAY_ENABLE_B(SEL0), .OE_B(microcontroller_board_kernal_and_user_1_main_memory_web),
    .ADDRESS_OUT_A0_23(microcontroller_board_kernal_and_user_1_main_memory_address));
  Graphics_Board graphics_board_3 (
    .SOURCE_ADDRESS(undriven_2), .TRANSPARENCY_B(TRANSPARENCY_TESTING_BLIT_2_B),
    .DONE_IRQB(BLIT_2_DONE_IRQ_B), .D_OUT(microcontroller_board_kernal_only_2_main_memory_d_out),
    .D_IN(microcontroller_board_kernal_only_2_main_memory_d_out),
    .TRANSPARENCY_COLOUR_INDEX(TRANSPARENCU_INDEX_BLIT_2), .RESET_B(RESET),
    .LINE_WIDTH_REMAINING_W0_7(BLIT_2_REMAINING_WIDTH_W0_7),
    .DESTINATION_ADDRESS(DESTINATION_ADDRESS_BLIT_2),
    .MAIN_MEMORY_VALID_B(graphics_board_3_main_memory_valid_b),
    .REMAINING_WIDTH_LOW_OEB(LINE_WIDTH_LOW_OE_BLIT_2_B),
    .WEB(microcontroller_board_kernal_only_2_main_memory_web),
    .REMAINING_WIDTH_HIGH_OEB(LINE_WIDTH_HIGH_OE_BLIT_2_B), .LINE_WIDTH_0_11(LINE_WIDTH_BLIT_2),
    .ADDRESS_A0_23(microcontroller_board_kernal_only_2_main_memory_address),
    .MEMORY_LOCKOUT(MEMORY_LOCKOUT_CHANNEL_2), .HIGH_NYBBLE(undriven), .IRQ_CLEAR(CLEAR_IRQ_BLIT_2),
    .START_RASTERISING(START_RASTERISING_BLIT_2), .EIGHT_BIT(EIGHT_BIT_MODE_BLIT_2),
    .OEB(microcontroller_board_kernal_only_2_main_memory_oeb), .REMAINING_WIDTH_LE(LINE_WIDTH_LE_BLIT_2),
    .IRQ_ENABLE(DONE_IRQ_ENABLE_BLIT_2),
    .SELECTOR({SELECTOR[3], SEL2, SELECTOR[1], SEL0, SELECTOR[7], SEL6, SELECTOR[5], SEL4}));
  Memory_Lockout_And_Generator memory_lockout_and_generator_3 (
    .NMI_B(NMIB_LOCKOUT_CHANNEL_2), .MAIN_MEMORY_VALID_3_B(pull_resistor_39_node),
    .LOCKOUT(MEMORY_LOCKOUT_CHANNEL_2), .RESET(RESET), .ADDRESS_IN_A0_23(24'h4aaaaa),
    .WE_B(microcontroller_board_kernal_only_2_main_memory_oeb),
    .MAIN_MEMORY_VALID_1_B(microcontroller_board_kernal_only_2_main_memory_valid_b),
    .MAIN_MEMORY_VALID_2_B(graphics_board_3_main_memory_valid_b), .SLOW_SELECTOR(SLW),
    .GATEWAY_ENABLE_B(SEL2), .OE_B(microcontroller_board_kernal_only_2_main_memory_web),
    .ADDRESS_OUT_A0_23(microcontroller_board_kernal_only_2_main_memory_address));
  Graphics_Board graphics_board_4 (
    .SOURCE_ADDRESS(SOURCE_ADDRESS_BLIT_3), .TRANSPARENCY_B(TRANSPARENCY_TESTING_BLIT_3_B),
    .DONE_IRQB(BLIT_3_DONE_IRQ_B), .D_OUT(microcontroller_board_kernal_and_user_2_main_memory_d_out),
    .D_IN(microcontroller_board_kernal_and_user_2_main_memory_d_out),
    .TRANSPARENCY_COLOUR_INDEX(TRANSPARENCU_INDEX_BLIT_3), .RESET_B(RESET),
    .LINE_WIDTH_REMAINING_W0_7(BLIT_3_REMAINING_WIDTH_W0_7),
    .DESTINATION_ADDRESS(DESTINATION_ADDRESS_BLIT_3),
    .MAIN_MEMORY_VALID_B(graphics_board_4_main_memory_valid_b),
    .REMAINING_WIDTH_LOW_OEB(LINE_WIDTH_LOW_OE_BLIT_3_B),
    .WEB(microcontroller_board_kernal_and_user_2_main_memory_web),
    .REMAINING_WIDTH_HIGH_OEB(LINE_WIDTH_HIGH_OE_BLIT_3_B), .LINE_WIDTH_0_11(LINE_WIDTH_BLIT_3),
    .ADDRESS_A0_23(microcontroller_board_kernal_and_user_2_main_memory_address),
    .MEMORY_LOCKOUT(MEMORY_LOCKOUT_CHANNEL_3), .HIGH_NYBBLE(FOUR_BIT_HIGH_NYBBLE_BLIT_3),
    .IRQ_CLEAR(CLEAR_IRQ_BLIT_3), .START_RASTERISING(START_RASTERISING_BLIT_3),
    .EIGHT_BIT(EIGHT_BIT_MODE_BLIT_3), .OEB(microcontroller_board_kernal_and_user_2_main_memory_oeb),
    .REMAINING_WIDTH_LE(LINE_WIDTH_LE_BLIT_3), .IRQ_ENABLE(DONE_IRQ_ENABLE_BLIT_3),
    .SELECTOR({SELECTOR[5], SEL4, SELECTOR[3], SEL2, SELECTOR[1], SEL0, SELECTOR[7], SEL6}));
  Memory_Lockout_And_Generator memory_lockout_and_generator_4 (
    .NMI_B(NMIB_LOCKOUT_CHANNEL_3), .MAIN_MEMORY_VALID_3_B(pull_resistor_40_node),
    .LOCKOUT(MEMORY_LOCKOUT_CHANNEL_3), .RESET(RESET), .ADDRESS_IN_A0_23(24'h6bbbbb),
    .WE_B(microcontroller_board_kernal_and_user_2_main_memory_oeb),
    .MAIN_MEMORY_VALID_1_B(microcontroller_board_kernal_and_user_2_main_memory_valid_b),
    .MAIN_MEMORY_VALID_2_B(graphics_board_4_main_memory_valid_b), .SLOW_SELECTOR(SLW),
    .GATEWAY_ENABLE_B(SEL4), .OE_B(microcontroller_board_kernal_and_user_2_main_memory_web),
    .ADDRESS_OUT_A0_23(microcontroller_board_kernal_and_user_2_main_memory_address));
  // Probe on BLIT_0_REMAINING_WIDTH_W0_7
  // Probe on BLIT_1_REMAINING_WIDTH_W0_7
  // Probe on BLIT_2_REMAINING_WIDTH_W0_7
  // Probe on BLIT_3_REMAINING_WIDTH_W0_7
  Main_Memory_Gateway main_memory_gateway_1 (
    .MEMORY_WEB_IN(microcontroller_board_kernal_only_1_main_memory_web),
    .MADDRESS_OUT_A0_23(main_memory_gateway_1_maddress_out_a0_23),
    .ADDRESS_IN_A0_23(microcontroller_board_kernal_only_1_main_memory_address), .GATEWAY_ENABLE_B(SEL6),
    .D_OUT_RIGHT(main_memory_gateway_1_d_out_right),
    .D_OUT_LEFT(microcontroller_board_kernal_only_1_main_memory_d_out),
    .D_IN_LEFT(microcontroller_board_kernal_only_1_main_memory_d_out),
    .MEMORY_OEB_IN(microcontroller_board_kernal_only_1_main_memory_oeb),
    .D_IN_RIGHT(main_memory_gateway_1_d_out_right), .MEMORY_OEB_OUT(main_memory_gateway_1_memory_oeb_out),
    .MEMORY_WEB_OUT(main_memory_gateway_1_memory_web_out));
  Main_Memory_Gateway main_memory_gateway_2 (
    .MEMORY_WEB_IN(microcontroller_board_kernal_and_user_1_main_memory_web),
    .MADDRESS_OUT_A0_23(main_memory_gateway_1_maddress_out_a0_23),
    .ADDRESS_IN_A0_23(microcontroller_board_kernal_and_user_1_main_memory_address), .GATEWAY_ENABLE_B(SEL0),
    .D_OUT_RIGHT(main_memory_gateway_1_d_out_right),
    .D_OUT_LEFT(microcontroller_board_kernal_and_user_1_main_memory_d_out),
    .D_IN_LEFT(microcontroller_board_kernal_and_user_1_main_memory_d_out),
    .MEMORY_OEB_IN(microcontroller_board_kernal_and_user_1_main_memory_oeb),
    .D_IN_RIGHT(main_memory_gateway_1_d_out_right), .MEMORY_OEB_OUT(main_memory_gateway_1_memory_oeb_out),
    .MEMORY_WEB_OUT(main_memory_gateway_1_memory_web_out));
  Main_Memory_Gateway main_memory_gateway_3 (
    .MEMORY_WEB_IN(microcontroller_board_kernal_only_2_main_memory_web),
    .MADDRESS_OUT_A0_23(main_memory_gateway_1_maddress_out_a0_23),
    .ADDRESS_IN_A0_23(microcontroller_board_kernal_only_2_main_memory_address), .GATEWAY_ENABLE_B(SEL2),
    .D_OUT_RIGHT(main_memory_gateway_1_d_out_right),
    .D_OUT_LEFT(microcontroller_board_kernal_only_2_main_memory_d_out),
    .D_IN_LEFT(microcontroller_board_kernal_only_2_main_memory_d_out),
    .MEMORY_OEB_IN(microcontroller_board_kernal_only_2_main_memory_oeb),
    .D_IN_RIGHT(main_memory_gateway_1_d_out_right), .MEMORY_OEB_OUT(main_memory_gateway_1_memory_oeb_out),
    .MEMORY_WEB_OUT(main_memory_gateway_1_memory_web_out));
  Main_Memory_Gateway main_memory_gateway_4 (
    .MEMORY_WEB_IN(microcontroller_board_kernal_and_user_2_main_memory_web),
    .MADDRESS_OUT_A0_23(main_memory_gateway_1_maddress_out_a0_23),
    .ADDRESS_IN_A0_23(microcontroller_board_kernal_and_user_2_main_memory_address), .GATEWAY_ENABLE_B(SEL4),
    .D_OUT_RIGHT(main_memory_gateway_1_d_out_right),
    .D_OUT_LEFT(microcontroller_board_kernal_and_user_2_main_memory_d_out),
    .D_IN_LEFT(microcontroller_board_kernal_and_user_2_main_memory_d_out),
    .MEMORY_OEB_IN(microcontroller_board_kernal_and_user_2_main_memory_oeb),
    .D_IN_RIGHT(main_memory_gateway_1_d_out_right), .MEMORY_OEB_OUT(main_memory_gateway_1_memory_oeb_out),
    .MEMORY_WEB_OUT(main_memory_gateway_1_memory_web_out));
  Pull_Resistor pull_resistor_41 (.node(pull_resistor_41_node));
  Pull_Resistor #(.pull(1)) pull_resistor_42 (.node(pull_resistor_42_node));
  // _3_to_8_Decoder__LVC138 3_to_8_decoder_lvc138_1: pin names not known; wires that end beside it: pull_resistor_41_node, pull_resistor_41_node, main_memory_gateway_1_maddress_out_a0_23[23:21], pull_resistor_42_node, n3_to_8_decoder_lvc138_1_p5
  Pull_Resistor pull_resistor_43 (.node(pull_resistor_43_node));
  Pull_Resistor #(.pull(1)) pull_resistor_44 (.node(pull_resistor_44_node));
  Pull_Resistor pull_resistor_45 (.node(pull_resistor_45_node));
  Pull_Resistor #(.pull(1)) pull_resistor_46 (.node(pull_resistor_46_node));
  // Probe on main_memory_gateway_1_maddress_out_a0_23[20:0]
  // _3_to_8_Decoder__LVC138 3_to_8_decoder_lvc138_2: pin names not known; wires that end beside it: n3_to_8_decoder_lvc138_1_p5[0], pull_resistor_43_node, main_memory_gateway_1_maddress_out_a0_23[20:18], pull_resistor_44_node, n3_to_8_decoder_lvc138_2_p5
  // _3_to_8_Decoder__LVC138 3_to_8_decoder_lvc138_3: pin names not known; wires that end beside it: n3_to_8_decoder_lvc138_1_p5[1], pull_resistor_45_node, main_memory_gateway_1_maddress_out_a0_23[20:18], pull_resistor_46_node, n3_to_8_decoder_lvc138_3_p5
  RAM #(.databus("bidir"), .trigger("high"), .addrWidth(21), .enables("line"), .\type ("nonvolatile")) ram_1 (
    .addr(main_memory_gateway_1_maddress_out_a0_23[20:0]), .data(main_memory_gateway_1_d_out_right));  // open: we, oe, clk
  SRAM_Chipifier sram_chipifier_1 (
    .WEB(main_memory_gateway_1_memory_web_out), .OEB(main_memory_gateway_1_memory_oeb_out),
    .CEB(n3_to_8_decoder_lvc138_1_p5[2]));  // open: OE, E, WE
  RAM #(.addrWidth(21), .\type ("nonvolatile"), .trigger("high"), .databus("bidir"), .enables("line")) ram_2 (
    .addr(main_memory_gateway_1_maddress_out_a0_23[20:0]), .data(main_memory_gateway_1_d_out_right));  // open: we, oe, clk
  SRAM_Chipifier sram_chipifier_2 (
    .WEB(main_memory_gateway_1_memory_web_out), .OEB(main_memory_gateway_1_memory_oeb_out),
    .CEB(n3_to_8_decoder_lvc138_1_p5[3]));  // open: OE, E, WE
  RAM #(.\type ("nonvolatile"), .enables("line"), .addrWidth(21), .databus("bidir"), .trigger("high")) ram_3 (
    .addr(main_memory_gateway_1_maddress_out_a0_23[20:0]), .data(main_memory_gateway_1_d_out_right));  // open: we, oe, clk
  SRAM_Chipifier sram_chipifier_3 (
    .WEB(main_memory_gateway_1_memory_web_out), .OEB(main_memory_gateway_1_memory_oeb_out),
    .CEB(n3_to_8_decoder_lvc138_1_p5[4]));  // open: OE, E, WE
  RAM #(.\type ("nonvolatile"), .trigger("high"), .databus("bidir"), .enables("line"), .addrWidth(21)) ram_4 (
    .addr(main_memory_gateway_1_maddress_out_a0_23[20:0]), .data(main_memory_gateway_1_d_out_right));  // open: we, oe, clk
  SRAM_Chipifier sram_chipifier_4 (
    .WEB(main_memory_gateway_1_memory_web_out), .OEB(main_memory_gateway_1_memory_oeb_out),
    .CEB(n3_to_8_decoder_lvc138_1_p5[5]));  // open: OE, E, WE
  RAM #(.addrWidth(21), .\type ("nonvolatile"), .trigger("high"), .enables("line"), .databus("bidir")) ram_5 (
    .addr(main_memory_gateway_1_maddress_out_a0_23[20:0]), .data(main_memory_gateway_1_d_out_right));  // open: we, oe, clk
  SRAM_Chipifier sram_chipifier_5 (
    .WEB(main_memory_gateway_1_memory_web_out), .OEB(main_memory_gateway_1_memory_oeb_out),
    .CEB(n3_to_8_decoder_lvc138_1_p5[6]));  // open: OE, E, WE
  RAM #(.trigger("high"), .enables("line"), .databus("bidir"), .addrWidth(21), .\type ("nonvolatile")) ram_6 (
    .addr(main_memory_gateway_1_maddress_out_a0_23[20:0]), .data(main_memory_gateway_1_d_out_right));  // open: we, oe, clk
  SRAM_Chipifier sram_chipifier_6 (
    .WEB(main_memory_gateway_1_memory_web_out), .OEB(main_memory_gateway_1_memory_oeb_out),
    .CEB(n3_to_8_decoder_lvc138_1_p5[7]));  // open: OE, E, WE
  // Probe on main_memory_gateway_1_d_out_right
  Clock clock_1 (.out(clock_1_out));
  Clock_Generator clock_generator_1 (
    .SELECT_LOW_SPEED_S0_3(4'b0000), .SELECT_HIGH_SPEED_S0_3(4'b0000),
    .CLOCK_OUT(clock_generator_1_clock_out), .CLOCK_IN(clock_1_out), .RESET(quick_timing_circuit_1_reset_0_b));
  Quick_Timing_Circuit quick_timing_circuit_1 (
    .RESET_0_B(quick_timing_circuit_1_reset_0_b), .RESET_1_B(RESET), .RESET(RESET_SWITCH),
    .SELECTOR_B({SELECTOR[7], SEL6, SELECTOR[5], SEL4, SELECTOR[3], SEL2, SELECTOR[1], SEL0}), .CLK(FST),
    .SLOW_SELECTOR(SLW), .CLOCK_IN(clock_generator_1_clock_out));  // open: HCLK_B, MULTIPLEXER, COUNTER, HCLK, CLK_B
  Device_Strobe device_strobe_1 (
    .Channel_2_B(device_strobe_1_channel_2_b), .SELECTOR_0_B(SEL4), .CHANNEL_1_NUMBER(MPU_1_DEVICE_CHANNEL),
    .Channel_3_B(device_strobe_1_channel_3_b), .Channel_0_B(device_strobe_1_channel_0_b),
    .Channel_1_B(device_strobe_1_channel_1_b), .RESET(RESET), .CHANNEL_0_NUMBER(MPU_0_DEVICE_CHANNEL),
    .DEVICE_1_VALID_B(MPU_0_DEVICE_VALID_B), .DEVICE_0_VALID_B(MPU_0_DEVICE_VALID_B), .SELECTOR_1_B(SEL6));
  Device_Strobe device_strobe_2 (
    .Channel_2_B(device_strobe_1_channel_2_b), .SELECTOR_0_B(SEL0), .CHANNEL_1_NUMBER(MPU_3_DEVICE_CHANNEL),
    .Channel_3_B(device_strobe_1_channel_3_b), .Channel_0_B(device_strobe_1_channel_0_b),
    .Channel_1_B(device_strobe_1_channel_1_b), .RESET(RESET), .CHANNEL_0_NUMBER(MPU_2_DEVICE_CHANNEL),
    .DEVICE_1_VALID_B(MPU_0_DEVICE_VALID_B), .DEVICE_0_VALID_B(MPU_0_DEVICE_VALID_B), .SELECTOR_1_B(SEL2));
  Video_Board video_board_1 (
    .GREEN(video_board_1_green), .VERTICAL_RASTER_HIGH_OEB(VERTICAL_RASTER_HIGH_OEB),
    .CLOCK_OSCILLATOR_SCK(PIXEL_CLOCK_SCK), .V_D0_7(VERTICAL_RASTER_V0_7), .H_SYNC(HSYNC),
    .RED(video_board_1_red), .CLOCK_OSCILLATOR_SEN(PIXEL_CLOCK_SEN), .BLANK_B(video_board_1_blank_b),
    .HACTIVE_D4_11(HORIZONTAL_ACTIVE_H4_11), .IRQ_ENABLE(VERTICAL_RASTER_IRQ_ENABLE),
    .VIDEO_CLOCK(video_board_1_video_clock), .BLUE(video_board_1_blue), .H_SYNC_D4_11(HORIZONTAL_SYNC_H4_11),
    .MAIN_MEMORY_VIDEO_2_B(n3_to_8_decoder_lvc138_2_p5[2]), .CLOCK_OSCILLATOR_SDI(PIXEL_CLOCK_SDI),
    .H_FRONT_PORCH_D4_11(HORIZONTAL_FRONT_PORCH_H4_11),
    .ADDRESS_A0_17(main_memory_gateway_1_maddress_out_a0_23[17:0]), .FRAME_BUFFER(FRAME_BUFFER_INDEX),
    .CLEAR_IRQ(CLEAR_IRQ_VERTICAL_RASTER), .VERTICAL_RASTER_LE(VERTICAL_RASTER_LE), .V_SYNC(VSYNC),
    .OEB(main_memory_gateway_1_memory_oeb_out), .RESET_B(RESET), .V_SYNC_D0_7(VERTICAL_SYNC_V0_7),
    .H_BACK_PORCH_D4_11(HORIZONTAL_BACK_PORCH_H4_11), .MAIN_MEMORY_VIDEO_0_B(n3_to_8_decoder_lvc138_2_p5[0]),
    .V_FRONT_PORCH_D0_7(VERTICAL_FRONT_PORCH_V0_7), .IRQ_B(VERTICAL_DONE_IRQ_B),
    .V_ACTIVE_D4_11(VERTICAL_ACTIVE_V4_11), .MAIN_MEMORY_VIDEO_1_B(n3_to_8_decoder_lvc138_2_p5[1]),
    .MAIN_MEMORY_PALETTE_B(n3_to_8_decoder_lvc138_2_p5[3]), .V_BACK_PORCH_D0_7(VERTICAL_BACK_PORCH_V0_7),
    .WEB(main_memory_gateway_1_memory_web_out), .VERTICAL_RASTER_LOW_OEB(VERTICAL_RASTER_LOW_OEB),
    .PIXEL_DOUBLING_X(HORIZONTAL_PIXEL_DOUBLING), .PALETTE_INDEX_P0_7(PALETTE_INDEX_P0_7));
  // Probe on MPU_0_DEVICE_D
  // Probe on MPU_0_DEVICE_D
  // Probe on MPU_0_DEVICE_D
  // Probe on MPU_0_DEVICE_D
  Device_Channel_Gateway device_channel_gateway_1 (
    .MPU_DEVICE_ADDRESS(MPU_0_DEVICE_ADDRESS), .MPU_D_IN(MPU_0_DEVICE_D), .CHANNEL_D_IN(CH_0_D),
    .MPU_RWB(MPU_0_DEVICE_RWB), .CHANNEL_RWB(CH_0_RWB), .CHANNEL_DEVICE_IDENTIFIER(CH_0_DEVICE_IDENTIFIER),
    .SELECTOR_B(device_strobe_1_channel_0_b), .CHANNEL_RWB_B(CH_0_RWB_B),
    .CHANNEL_DEVICE_ADDRESS(CH_0_DEVICE_ADDRESS), .FST(FST), .CHANNEL_D_OUT(CH_0_D),
    .MPU_D_OUT(MPU_0_DEVICE_D), .MPU_DEVICE_VALID_B(MPU_0_DEVICE_VALID_B),
    .MPU_DEVICE_IDENTIFIER(MPU_0_DEVICE_IDENTIFIER));
  Device_Channel_Gateway device_channel_gateway_2 (
    .MPU_DEVICE_ADDRESS(MPU_0_DEVICE_ADDRESS), .MPU_D_IN(MPU_0_DEVICE_D), .CHANNEL_D_IN(CH_1_D),
    .MPU_RWB(MPU_0_DEVICE_RWB), .CHANNEL_RWB(CH_1_RWB), .CHANNEL_DEVICE_IDENTIFIER(CH_1_DEVICE_IDENTIFIER),
    .SELECTOR_B(device_strobe_1_channel_1_b), .CHANNEL_RWB_B(CH_1_RWB_B),
    .CHANNEL_DEVICE_ADDRESS(CH_1_DEVICE_ADDRESS), .FST(FST), .CHANNEL_D_OUT(CH_1_D),
    .MPU_D_OUT(MPU_0_DEVICE_D), .MPU_DEVICE_VALID_B(MPU_0_DEVICE_VALID_B),
    .MPU_DEVICE_IDENTIFIER(MPU_0_DEVICE_IDENTIFIER));
  Device_Channel_Gateway device_channel_gateway_3 (
    .MPU_DEVICE_ADDRESS(MPU_0_DEVICE_ADDRESS), .MPU_D_IN(MPU_0_DEVICE_D), .CHANNEL_D_IN(CH_2_D),
    .MPU_RWB(MPU_0_DEVICE_RWB), .CHANNEL_RWB(CH_2_RWB), .CHANNEL_DEVICE_IDENTIFIER(CH_2_DEVICE_IDENTIFIER),
    .SELECTOR_B(device_strobe_1_channel_2_b), .CHANNEL_RWB_B(CH_2_RWB_B),
    .CHANNEL_DEVICE_ADDRESS(CH_2_DEVICE_ADDRESS), .FST(FST), .CHANNEL_D_OUT(CH_2_D),
    .MPU_D_OUT(MPU_0_DEVICE_D), .MPU_DEVICE_VALID_B(MPU_0_DEVICE_VALID_B),
    .MPU_DEVICE_IDENTIFIER(MPU_0_DEVICE_IDENTIFIER));
  Device_Channel_Gateway device_channel_gateway_4 (
    .MPU_DEVICE_ADDRESS(MPU_0_DEVICE_ADDRESS), .MPU_D_IN(MPU_0_DEVICE_D), .CHANNEL_D_IN(CH_3_D),
    .MPU_RWB(MPU_0_DEVICE_RWB), .CHANNEL_RWB(CH_3_RWB), .CHANNEL_DEVICE_IDENTIFIER(CH_3_DEVICE_IDENTIFIER),
    .SELECTOR_B(device_strobe_1_channel_3_b), .CHANNEL_RWB_B(CH_3_RWB_B),
    .CHANNEL_DEVICE_ADDRESS(CH_3_DEVICE_ADDRESS), .FST(FST), .CHANNEL_D_OUT(CH_3_D),
    .MPU_D_OUT(MPU_0_DEVICE_D), .MPU_DEVICE_VALID_B(MPU_0_DEVICE_VALID_B),
    .MPU_DEVICE_IDENTIFIER(MPU_0_DEVICE_IDENTIFIER));
  ADV7125 adv7125_1 (
    .GREEN_D0_7(video_board_1_green), .IOB_B(adv7125_1_iob_b), .BLUE_D0_7(video_board_1_blue), .IOR(IOR),
    .RED_D0_7(video_board_1_red), .IOG(IOG), .IOR_B(adv7125_1_iob_b), .IOB(IOB), .SYNC_B(HSYNC),
    .IOG_B(adv7125_1_iob_b), .BLANK_B(video_board_1_blank_b), .CLOCK(video_board_1_video_clock));
  Pull_Resistor pull_resistor_47 (.node(adv7125_1_iob_b));
  // Probe on CH_0_D
  // Probe on CH_1_D
  // Probe on CH_2_D
  // Helper__W65C816_Timing helper_w65c816_timing_1: pin names not known; wires that end beside it: 4'b0110, 4'b0001, 4'b0110, 4'b0100, 4'b0001, 4'b0101, 4'b0001, 4'b0110, 4'b0010, 4'b0110, T1, 4'b0100, 4'b0000, 4'b0111, 4'b0000, 4'b0011, 4'b0111, 4'b0111, 4'b0000, 4'b0011, 4'b0000, T2
  // Probe on CH_0_D
  // Probe on CH_1_D
  // Probe on CH_2_D
  // Probe on CH_3_D
  Microcontroller_Device microcontroller_device_1 (
    .CHANNEL_DEVICE_ADDRESS(CH_0_DEVICE_ADDRESS), .NMI_B(MPU0_NMI_B), .MPU_CHANNEL_OUT(MPU0_CHANNEL),
    .CHANNEL_RWB(CH_0_RWB), .D_OUT(CH_0_D), .IRQ_B(MPU0_IRQ_B), .CHANNEL_RWB_B(CH_0_RWB_B),
    .MPU_ABILITY(MPU_0_ABILITY), .RESET(RESET), .MPU_CHANNEL_IN(2'b00),
    .CHANNEL_DEVICE_IDENTIFIER(CH_0_DEVICE_IDENTIFIER), .RES_B(MPU0_RES_B), .SLOW_SELECTOR(SLW), .D_IN(CH_0_D));
  Microcontroller_Device microcontroller_device_2 (
    .CHANNEL_DEVICE_ADDRESS(CH_1_DEVICE_ADDRESS), .NMI_B(MPU1_NMI_B), .MPU_CHANNEL_OUT(MPU1_CHANNEL),
    .CHANNEL_RWB(CH_1_RWB), .D_OUT(CH_1_D), .IRQ_B(MPU1_IRQ_B), .CHANNEL_RWB_B(CH_1_RWB_B),
    .MPU_ABILITY(MPU_1_ABILITY), .RESET(RESET), .MPU_CHANNEL_IN(2'b01),
    .CHANNEL_DEVICE_IDENTIFIER(CH_1_DEVICE_IDENTIFIER), .RES_B(MPU1_RES_B), .SLOW_SELECTOR(SLW), .D_IN(CH_1_D));
  Microcontroller_Device microcontroller_device_3 (
    .CHANNEL_DEVICE_ADDRESS(CH_2_DEVICE_ADDRESS), .NMI_B(MPU2_NMI_B), .MPU_CHANNEL_OUT(MPU2_CHANNEL),
    .CHANNEL_RWB(CH_2_RWB), .D_OUT(CH_2_D), .IRQ_B(MPU2_IRQ_B), .CHANNEL_RWB_B(CH_2_RWB_B),
    .MPU_ABILITY(MPU_2_ABILITY), .RESET(RESET), .MPU_CHANNEL_IN(2'b10),
    .CHANNEL_DEVICE_IDENTIFIER(CH_2_DEVICE_IDENTIFIER), .RES_B(MPU2_RES_B), .SLOW_SELECTOR(SLW), .D_IN(CH_2_D));
  Microcontroller_Device microcontroller_device_4 (
    .CHANNEL_DEVICE_ADDRESS(CH_3_DEVICE_ADDRESS), .NMI_B(MPU3_NMI_B), .MPU_CHANNEL_OUT(MPU3_CHANNEL),
    .CHANNEL_RWB(CH_3_RWB), .D_OUT(CH_3_D), .IRQ_B(MPU3_IRQ_B), .CHANNEL_RWB_B(CH_3_RWB_B),
    .MPU_ABILITY(MPU_3_ABILITY), .RESET(RESET), .MPU_CHANNEL_IN(2'b11),
    .CHANNEL_DEVICE_IDENTIFIER(CH_3_DEVICE_IDENTIFIER), .RES_B(MPU3_RES_B), .SLOW_SELECTOR(SLW), .D_IN(CH_3_D));
  // Probe on CH_0_D
  Echo_Device echo_device_1 (
    .D_OUT(CH_0_D), .CHANNEL_RWB(CH_0_RWB), .CHANNEL_DEVICE_ADDRESS(CH_0_DEVICE_ADDRESS),
    .CHANNEL_DEVICE_IDENTIFIER(CH_0_DEVICE_IDENTIFIER), .D_IN(CH_0_D));
  Echo_Device echo_device_2 (
    .D_OUT(CH_1_D), .CHANNEL_RWB(CH_1_RWB), .CHANNEL_DEVICE_ADDRESS(CH_1_DEVICE_ADDRESS),
    .CHANNEL_DEVICE_IDENTIFIER(CH_1_DEVICE_IDENTIFIER), .D_IN(CH_1_D));
  Echo_Device echo_device_3 (
    .D_OUT(CH_2_D), .CHANNEL_RWB(CH_2_RWB), .CHANNEL_DEVICE_ADDRESS(CH_2_DEVICE_ADDRESS),
    .CHANNEL_DEVICE_IDENTIFIER(CH_2_DEVICE_IDENTIFIER), .D_IN(CH_2_D));
  Echo_Device echo_device_4 (
    .D_OUT(CH_3_D), .CHANNEL_RWB(CH_3_RWB), .CHANNEL_DEVICE_ADDRESS(CH_3_DEVICE_ADDRESS),
    .CHANNEL_DEVICE_IDENTIFIER(CH_3_DEVICE_IDENTIFIER), .D_IN(CH_3_D));
  // Probe on CH_1_D
  Graphics_Device graphics_device_1 (
    .CLEAR_IRQ(CLEAR_IRQ_BLIT_1), .REMAINING_WIDTH_HIGH_OEB(LINE_WIDTH_HIGH_OE_BLIT_1_B), .D_IN(CH_1_D),
    .DONE_IRQB_MPU_0_1_2_3({DONE_RASTERISING_MPU3_BLIT_1_B, DONE_RASTERISING_MPU2_BLIT_1_B, DONE_RASTERISING_MPU1_BLIT_1_B, DONE_RASTERISING_MPU0_BLIT_1_B}),
    .REMAINING_WIDTH_LOW_OEB(LINE_WIDTH_LOW_OE_BLIT_1_B), .IRQ_ENABLE(DONE_IRQ_ENABLE_BLIT_1),
    .CHANNEL_RWB_B(CH_1_RWB_B), .CHANNEL_DEVICE_IDENTIFIER(CH_1_DEVICE_IDENTIFIER),
    .DEST_ADDRESS(DESTINATION_ADDRESS_BLIT_1), .CHANNEL_DEVICE_ADDRESS(CH_1_DEVICE_ADDRESS),
    .LINE_WIDTH_W0_11(LINE_WIDTH_BLIT_1), .TRANSPARENCY_B(TRANSPARENCY_TESTING_BLIT_1_B),
    .START_RASTERISING(START_RASTERISING_BLIT_1), .D_OUT(CH_1_D), .DONE_IRQB(BLIT_0_DONE_IRQ_B),
    .TRANSPARENCY_COLOUR(TRANSPARENCU_INDEX_BLIT_1), .PIXEL_HIGH_NYBBLE(FOUR_BIT_HIGH_NYBBLE_BLIT_1),
    .SOURCE_ADDRESS(SOURCE_ADDRESS_BLIT_1), .REMAINING_WIDTH_LE(LINE_WIDTH_LE_BLIT_1),
    .EIGHT_BIT(EIGHT_BIT_MODE_BLIT_1), .CHANNEL_RWB(CH_1_RWB),
    .LINE_WIDTH_REMAINING_IN_W0_7(BLIT_0_REMAINING_WIDTH_W0_7));
  Graphics_Device graphics_device_2 (
    .CLEAR_IRQ(CLEAR_IRQ_BLIT_3), .REMAINING_WIDTH_HIGH_OEB(LINE_WIDTH_HIGH_OE_BLIT_3_B), .D_IN(CH_3_D),
    .DONE_IRQB_MPU_0_1_2_3({DONE_RASTERISING_MPU3_BLIT_3_B, DONE_RASTERISING_MPU2_BLIT_3_B, DONE_RASTERISING_MPU1_BLIT_3_B, DONE_RASTERISING_MPU0_BLIT_3_B}),
    .REMAINING_WIDTH_LOW_OEB(LINE_WIDTH_LOW_OE_BLIT_3_B), .IRQ_ENABLE(DONE_IRQ_ENABLE_BLIT_3),
    .CHANNEL_RWB_B(CH_3_RWB_B), .CHANNEL_DEVICE_IDENTIFIER(CH_3_DEVICE_IDENTIFIER),
    .DEST_ADDRESS(DESTINATION_ADDRESS_BLIT_3), .CHANNEL_DEVICE_ADDRESS(CH_3_DEVICE_ADDRESS),
    .LINE_WIDTH_W0_11(LINE_WIDTH_BLIT_3), .TRANSPARENCY_B(TRANSPARENCY_TESTING_BLIT_3_B),
    .START_RASTERISING(START_RASTERISING_BLIT_3), .D_OUT(CH_3_D), .DONE_IRQB(BLIT_3_DONE_IRQ_B),
    .TRANSPARENCY_COLOUR(TRANSPARENCU_INDEX_BLIT_3), .PIXEL_HIGH_NYBBLE(FOUR_BIT_HIGH_NYBBLE_BLIT_3),
    .SOURCE_ADDRESS(SOURCE_ADDRESS_BLIT_3), .REMAINING_WIDTH_LE(LINE_WIDTH_LE_BLIT_3),
    .EIGHT_BIT(EIGHT_BIT_MODE_BLIT_3), .CHANNEL_RWB(CH_3_RWB),
    .LINE_WIDTH_REMAINING_IN_W0_7(BLIT_3_REMAINING_WIDTH_W0_7));
  // Probe on CH_0_D
  Graphics_Device graphics_device_3 (
    .CLEAR_IRQ(CLEAR_IRQ_BLIT_0), .REMAINING_WIDTH_HIGH_OEB(LINE_WIDTH_HIGH_OE_BLIT_0_B), .D_IN(CH_0_D),
    .DONE_IRQB_MPU_0_1_2_3({DONE_RASTERISING_MPU3_BLIT_0_B, DONE_RASTERISING_MPU2_BLIT_0_B, DONE_RASTERISING_MPU1_BLIT_0_B, DONE_RASTERISING_MPU0_BLIT_0_B}),
    .REMAINING_WIDTH_LOW_OEB(LINE_WIDTH_LOW_OE_BLIT_0_B), .IRQ_ENABLE(DONE_IRQ_ENABLE_BLIT_0),
    .CHANNEL_RWB_B(CH_0_RWB_B), .CHANNEL_DEVICE_IDENTIFIER(CH_0_DEVICE_IDENTIFIER),
    .DEST_ADDRESS(DESTINATION_ADDRESS_BLIT_0), .CHANNEL_DEVICE_ADDRESS(CH_0_DEVICE_ADDRESS),
    .LINE_WIDTH_W0_11(LINE_WIDTH_BLIT_0), .TRANSPARENCY_B(TRANSPARENCY_TESTING_BLIT_0_B),
    .START_RASTERISING(START_RASTERISING_BLIT_0), .D_OUT(CH_0_D), .DONE_IRQB(BLIT_0_DONE_IRQ_B),
    .TRANSPARENCY_COLOUR(TRANSPARENCU_INDEX_BLIT_0), .PIXEL_HIGH_NYBBLE(FOUR_BIT_HIGH_NYBBLE_BLIT_0),
    .SOURCE_ADDRESS(SOURCE_ADDRESS_BLIT_0), .REMAINING_WIDTH_LE(LINE_WIDTH_LE_BLIT_0),
    .EIGHT_BIT(EIGHT_BIT_MODE_BLIT_0), .CHANNEL_RWB(CH_0_RWB),
    .LINE_WIDTH_REMAINING_IN_W0_7(BLIT_0_REMAINING_WIDTH_W0_7));
  Graphics_Device graphics_device_4 (
    .CLEAR_IRQ(CLEAR_IRQ_BLIT_2), .REMAINING_WIDTH_HIGH_OEB(LINE_WIDTH_HIGH_OE_BLIT_2_B), .D_IN(CH_2_D),
    .DONE_IRQB_MPU_0_1_2_3({DONE_RASTERISING_MPU3_BLIT_2_B, DONE_RASTERISING_MPU2_BLIT_2_B, DONE_RASTERISING_MPU1_BLIT_2_B, DONE_RASTERISING_MPU0_BLIT_2_B}),
    .REMAINING_WIDTH_LOW_OEB(LINE_WIDTH_LOW_OE_BLIT_2_B), .IRQ_ENABLE(DONE_IRQ_ENABLE_BLIT_2),
    .CHANNEL_RWB_B(CH_2_RWB_B), .CHANNEL_DEVICE_IDENTIFIER(CH_2_DEVICE_IDENTIFIER),
    .DEST_ADDRESS(DESTINATION_ADDRESS_BLIT_2), .CHANNEL_DEVICE_ADDRESS(CH_2_DEVICE_ADDRESS),
    .LINE_WIDTH_W0_11(LINE_WIDTH_BLIT_2), .TRANSPARENCY_B(TRANSPARENCY_TESTING_BLIT_2_B),
    .START_RASTERISING(START_RASTERISING_BLIT_2), .D_OUT(CH_2_D), .DONE_IRQB(BLIT_2_DONE_IRQ_B),
    .TRANSPARENCY_COLOUR(TRANSPARENCU_INDEX_BLIT_2), .PIXEL_HIGH_NYBBLE(FOUR_BIT_HIGH_NYBBLE_BLIT_2),
    .SOURCE_ADDRESS(SOURCE_ADDRESS_BLIT_2), .REMAINING_WIDTH_LE(LINE_WIDTH_LE_BLIT_2),
    .EIGHT_BIT(EIGHT_BIT_MODE_BLIT_2), .CHANNEL_RWB(CH_2_RWB),
    .LINE_WIDTH_REMAINING_IN_W0_7(BLIT_2_REMAINING_WIDTH_W0_7));
  // Probe on CH_0_D
  Video_Device video_device_1 (
    .H_SYNC_D4_11(HORIZONTAL_SYNC_H4_11),
    .DONE_IRQB_MPU_0_1_2_3({DONE_RASTERISING_MPU3_BLIT_0_B, DONE_RASTERISING_MPU2_BLIT_0_B, DONE_RASTERISING_MPU1_BLIT_0_B, DONE_RASTERISING_MPU0_BLIT_0_B}),
    .D_IN(CH_0_D), .CHANNEL_DEVICE_ADDRESS(CH_0_DEVICE_ADDRESS),
    .H_BACK_PORCH_D4_11(HORIZONTAL_BACK_PORCH_H4_11), .HACTIVE_D4_11(HORIZONTAL_ACTIVE_H4_11),
    .FRAME_BUFFER(FRAME_BUFFER_INDEX), .CHANNEL_RWB(CH_0_RWB), .VERTICAL_RASTER_LE(VERTICAL_RASTER_LE),
    .V_ACTIVE_D4_11(VERTICAL_ACTIVE_V4_11), .VERTICAL_RASTER_LOW_OEB(VERTICAL_RASTER_LOW_OEB),
    .CLOCK_OSCILLATOR_SCK(PIXEL_CLOCK_SCK), .CLOCK_OSCILLATOR_SDI(PIXEL_CLOCK_SDI), .D_OUT(CH_0_D),
    .DONE_IRQB(VERTICAL_DONE_IRQ_B), .CLOCK_OSCILLATOR_SEN(PIXEL_CLOCK_SEN),
    .V_BACK_PORCH_D0_7(VERTICAL_BACK_PORCH_V0_7), .IRQ_ENABLE(VERTICAL_RASTER_IRQ_ENABLE),
    .CHANNEL_RWB_B(CH_0_RWB_B), .V_SYNC_D0_7(VERTICAL_SYNC_V0_7), .CLEAR_IRQ(CLEAR_IRQ_VERTICAL_RASTER),
    .V_FRONT_PORCH_D0_7(VERTICAL_FRONT_PORCH_V0_7), .VERTICAL_RASTER_HIGH_OEB(VERTICAL_RASTER_HIGH_OEB),
    .PIXEL_DOUBLING_X(HORIZONTAL_PIXEL_DOUBLING), .VERTICAL_RASTER_IN_D0_7(VERTICAL_RASTER_V0_7),
    .CHANNEL_DEVICE_IDENTIFIER(CH_0_DEVICE_IDENTIFIER), .PALETTE_INDEX(PALETTE_INDEX_P0_7),
    .H_FRONT_PORCH_D4_11(HORIZONTAL_FRONT_PORCH_H4_11), .RESET_B(RESET));
  // Probe on CH_0_D
  SNES_Controller_Device snes_controller_device_1 (
    .RESET_B(RESET), .OE_CONTROLLER_2_HIGH_B(snes_controller_device_1_oe_controller_2_high_b),
    .COUNTER_RESET_B(snes_controller_device_1_counter_reset_b),
    .CHANNEL_DEVICE_IDENTIFIER(CH_0_DEVICE_IDENTIFIER), .CHANNEL_RWB_B(CH_0_RWB_B),
    .OE_CONTROLLER_3_LOW_B(snes_controller_device_1_oe_controller_3_low_b),
    .CHANNEL_DEVICE_ADDRESS(CH_0_DEVICE_ADDRESS),
    .OE_CONTROLLER_1_HIGH_B(snes_controller_device_1_oe_controller_1_high_b),
    .OE_CONTROLLER_1_LOW_B(snes_controller_device_1_oe_controller_1_low_b),
    .SHIFT_REGISTER_IN(snes_input_board_1_shift_register_out), .CHANNEL_RWB(CH_0_RWB),
    .OE_CONTROLLER_0_HIGH_B(snes_controller_device_1_oe_controller_0_high_b),
    .OE_CONTROLLER_3_HIGH_B(snes_controller_device_1_oe_controller_3_high_b),
    .LATCH_RESET_B(DONE_SHIFTING_B), .OE_CONTROLLER_0_LOW_B(snes_controller_device_1_oe_controller_0_low_b),
    .D_OUT(CH_0_D), .D_IN(CH_0_D), .OE_CONTROLLER_2_LOW_B(snes_controller_device_1_oe_controller_2_low_b));  // open: DEVICE_SELECTED
  SNES_Input_Board snes_input_board_1 (
    .OE_CONTROLLER_2_HIGH_B(snes_controller_device_1_oe_controller_2_high_b),
    .CONTROLLER_LATCH(SNES_CONTROLLER_LATCH),
    .OE_CONTROLLER_0_HIGH_B(snes_controller_device_1_oe_controller_0_high_b),
    .CONTROLLER_CLOCK(SNES_CONTROLLER_CLOCCK), .CONTROLLER_DATA_1(SNES_CONTROLLER_DATA_1),
    .CONTROLLER_DATA_2(SNES_CONTROLLER_DATA_2),
    .OE_CONTROLLER_2_LOW_B(snes_controller_device_1_oe_controller_2_low_b),
    .OE_CONTROLLER_0_LOW_B(snes_controller_device_1_oe_controller_0_low_b),
    .COUNTER_RESET_B(snes_controller_device_1_counter_reset_b), .DONE_SHIFTING_B(DONE_SHIFTING_B),
    .OE_CONTROLLER_3_HIGH_B(snes_controller_device_1_oe_controller_3_high_b),
    .CONTROLLER_DATA_0(SNES_CONTROLLER_DATA_0),
    .OE_CONTROLLER_1_HIGH_B(snes_controller_device_1_oe_controller_1_high_b),
    .OE_CONTROLLER_1_LOW_B(snes_controller_device_1_oe_controller_1_low_b), .RESET_B(RESET),
    .CONTROLLER_DATA_3(SNES_CONTROLLER_DATA_3), .SHIFT_REGISTER_OUT(snes_input_board_1_shift_register_out),
    .OE_CONTROLLER_3_LOW_B(snes_controller_device_1_oe_controller_3_low_b));  // open: SHIFT_IN_CLOCK
  // Probe on snes_input_board_1_shift_register_out
  // Probe on CH_0_D
  PS2_Input_Device ps2_input_device_1 (
    .OE_HIGH_B(ps2_input_device_1_oe_high_b), .CHANNEL_RWB_B(CH_0_RWB_B),
    .RESET_PS2_B(ps2_input_device_1_reset_ps2_b), .CHANNEL_RWB(CH_0_RWB), .FIFO_IN(out_15), .D_OUT(CH_0_D),
    .RESET_B(RESET), .CHANNEL_DEVICE_IDENTIFIER(CH_0_DEVICE_IDENTIFIER),
    .OE_LOW_B(ps2_input_device_1_oe_low_b), .D_IN(CH_0_D), .CHANNEL_DEVICE_ADDRESS(CH_0_DEVICE_ADDRESS));  // open: DEVICE_SELECTED
  PS2_Input_Board ps2_input_board_1 (
    .OE_HIGH_BYTE_B(ps2_input_device_1_oe_high_b), .PS2_DATA_1(PS2_DATA_2), .FIFO_OUT(out_15),
    .PS2_CLOCK_1(PS2_CLOCK_2), .RESET_B(ps2_input_device_1_reset_ps2_b),
    .OE_LOW_BYTE_B(ps2_input_device_1_oe_low_b), .PS2_CLOCK_0(PS2_CLOCK_0), .PS2_DATA_0(PS2_DATA_0));  // open: PS2_ACTIVE_1, PS2_ACTIVE_0

  // Other names for the same wires on the sheet: MPU_1_DEVICE_ADDRESS[3:0] = MPU_0_DEVICE_ADDRESS;
  //   MPU_2_DEVICE_ADDRESS[3:0] = MPU_0_DEVICE_ADDRESS; MPU_3_DEVICE_ADDRESS[3:0] = MPU_0_DEVICE_ADDRESS;
  //   MPU_1_DEVICE_D[7:0] = MPU_0_DEVICE_D; MPU_2_DEVICE_D[7:0] = MPU_0_DEVICE_D;
  //   MPU_3_DEVICE_D[7:0] = MPU_0_DEVICE_D; MPU_1_DEVICE_IDENTIFIER[5:0] = MPU_0_DEVICE_IDENTIFIER;
  //   MPU_2_DEVICE_IDENTIFIER[5:0] = MPU_0_DEVICE_IDENTIFIER; MPU_3_DEVICE_IDENTIFIER[5:0] = MPU_0_DEVICE_IDENTIFIER;
  //   MPU_1_DEVICE_RWB = MPU_0_DEVICE_RWB; MPU_2_DEVICE_RWB = MPU_0_DEVICE_RWB; MPU_3_DEVICE_RWB = MPU_0_DEVICE_RWB;
  //   MPU_1_DEVICE_VALID_B = MPU_0_DEVICE_VALID_B; MPU_2_DEVICE_VALID_B = MPU_0_DEVICE_VALID_B;
  //   MPU_3_DEVICE_VALID_B = MPU_0_DEVICE_VALID_B; SELECTOR (some bits) = {SEL6, SEL4, SEL2, SEL0};
  //   SELECTOR_OFFSET_0[7:0] = {SELECTOR[7], SEL6, SELECTOR[5], SEL4, SELECTOR[3], SEL2, SELECTOR[1], SEL0};
  //   SELECTOR_OFFSET_2[7:0] = {SELECTOR[1], SEL0, SELECTOR[7], SEL6, SELECTOR[5], SEL4, SELECTOR[3], SEL2};
  //   SELECTOR_OFFSET_4[7:0] = {SELECTOR[3], SEL2, SELECTOR[1], SEL0, SELECTOR[7], SEL6, SELECTOR[5], SEL4};
  //   SELECTOR_OFFSET_6[7:0] = {SELECTOR[5], SEL4, SELECTOR[3], SEL2, SELECTOR[1], SEL0, SELECTOR[7], SEL6}
endmodule

module Microcontroller_Board_Kernal_Only (
  input  RESET_1,
  input  [7:0] SELECTOR,
  input  FST,
  input  [39:0] T1,
  input  [39:0] T2,
  input  MAIN_MEMORY_LOCKOUT,
  input  [1:0] MPU_CHANNEL_D0_1,
  input  [8:0] IRQ_IN,
  input  [3:0] NMI_B_IN,
  input  [7:0] MAIN_MEMORY_D_IN,
  input  [7:0] DEVICE_D_IN,
  output RESET,
  output CLOCK_ENABLE_B,
  output [7:0] MPU_ABILITY,
  output [23:0] MAIN_MEMORY_ADDRESS,
  output MAIN_MEMORY_OEB,
  output MAIN_MEMORY_WEB,
  output [7:0] MAIN_MEMORY_D_OUT,
  output MAIN_MEMORY_VALID_B,
  output [1:0] DEVICE_CHANNEL,
  output DEVICE_VALID_B,
  output [5:0] DEVICE_IDENTIFIER,
  output [3:0] DEVICE_ADDRESS,
  output DEVICE_RWB,
  output [7:0] DEVICE_D_OUT
);

  wire BANK_LATCH, DATA_TRANSMIT_B, DEVICE_STROBE_B, DEVICE_VALID_B_t, FST_t, INTERNAL_MEMORY_VALID, IRQ_B,
       KERNAL_ROM_B, microprocessor_w65c816_1_p6, microprocessor_w65c816_1_p13, microprocessor_w65c816_1_p14,
       microprocessor_w65c816_1_p15, MPU_LOCK_IN, nand_1_out, nand_2_out, NATIVE_MODE, NMI_B, not_1_out,
       not_2_out, not_3_out, OPCODE_ADDRESS, or_1_out, PHI2, pull_resistor_1_node, pull_resistor_2_node,
       pull_resistor_3_node, pull_resistor_6_node, RDY, READ_ENABLE, READ_ENABLE_B, READ_SELECTOR,
       ROM_ADDRESS_VALID, RWB, RWB_B, SA_FLAG_REGISTER_B, SA_INSTRUCTION_COUNTER_0, SA_INSTRUCTION_COUNTER_1,
       SA_INSTRUCTION_COUNTER_2, SA_INSTRUCTION_COUNTER_3, selector_state_1_sel0, selector_state_1_sel1,
       selector_state_1_sel2, selector_state_1_sel3, selector_state_1_sel4, selector_state_1_sel5,
       selector_state_1_sel6, selector_state_1_sel7, SPECIAL_ADDRESS_VALID_B, STOP_SELECTOR, VPB,
       WRITE_ENABLE, WRITE_SELECTOR;
  wire [3:0] DEVICE_ADDRESS_t;
  wire [5:0] DEVICE_IDENTIFIER_t;
  wire [7:0] A0_7, A8_15, D, IRAM_A0_7, KERNAL_ROM_data, microprocessor_w65c816_1_p10;
  wire [7:2] flags_register_1_flag_register;
  wire [11:0] address_decode_1_special_memory_selector_b;
  wire [23:16] ADDRESS;

  Pull_Resistor #(.pull(1)) pull_resistor_1 (.node(pull_resistor_1_node));
  Pull_Resistor pull_resistor_2 (.node(pull_resistor_2_node));
  // Probe on {ADDRESS, A8_15, A0_7}
  LED led_1 (.in(selector_state_1_sel0));
  LED led_2 (.in(selector_state_1_sel3));
  LED led_3 (.in(selector_state_1_sel1));
  LED led_4 (.in(selector_state_1_sel2));
  LED led_5 (.in(selector_state_1_sel4));
  Selector_State selector_state_1 (
    .SEL0(selector_state_1_sel0), .SEL5(selector_state_1_sel5), .DEVICE_STROBE_B(DEVICE_STROBE_B),
    .SEL2(selector_state_1_sel2), .READ_SELECTOR(READ_SELECTOR), .WRITE_SELECTOR(WRITE_SELECTOR),
    .RESET(RESET_1), .BOARD_RESET(RESET), .SEL6(selector_state_1_sel6), .SELECTOR(SELECTOR), .PHI2(PHI2),
    .STOP_SELECTOR_B(STOP_SELECTOR), .DATA_TRANSMIT_B(DATA_TRANSMIT_B), .SEL1(selector_state_1_sel1),
    .SEL7(selector_state_1_sel7), .SEL3(selector_state_1_sel3), .CLOCK_ENABLE_B(CLOCK_ENABLE_B),
    .BANK_LATCH(BANK_LATCH), .SEL4(selector_state_1_sel4));  // open: READ_BANK_REMAP_B, MPU_LOCK_IN
  not not_1 (not_1_out, CLOCK_ENABLE_B);
  and and_1 (FST_t, not_1_out, FST);
  Clock_Control clock_control_1 (
    .DEVICE_ADDRESS_VALID_B(DEVICE_VALID_B_t), .RESET(RESET), .RWB_B(RWB_B),
    .UNSTOPPABLE_CLOCK(STOP_SELECTOR), .ROM_ADDRESS_VALID(ROM_ADDRESS_VALID), .CLOCK_ENABLE_B(CLOCK_ENABLE_B));
  Flags_Register flags_register_1 (
    .FLAG_REGISTER({flags_register_1_flag_register, KERNAL_ROM_B, MPU_LOCK_IN}),
    .WRITE_ENABLE_B(READ_ENABLE_B), .D_IN(D), .D_OUT(D), .READ_ENABLE_B(READ_ENABLE_B), .RESET(RESET),
    .SA_FLAG_REGISTER_B(SA_FLAG_REGISTER_B));
  LED led_6 (.in(selector_state_1_sel7));
  LED led_7 (.in(selector_state_1_sel5));
  LED led_8 (.in(selector_state_1_sel6));
  Counter #(.width(32), .max('hffffffff)) counter_1 (.clk(FST_t));  // open: load, D, count, Q, carry, up, clr
  Address_Decode address_decode_1 (
    .DEVICE_CHANNEL(DEVICE_CHANNEL), .ADDRESS_IN_A0_24({ADDRESS, A8_15, A0_7}), .MPU_LOCK_IN(MPU_LOCK_IN),
    .INTERNAL_MEMORY_VALID(INTERNAL_MEMORY_VALID), .RWB(RWB), .DEVICE_ADDRESS(DEVICE_ADDRESS_t),
    .DEVICE_VALID_B(DEVICE_VALID_B_t), .KERNAL_MODE_B(pull_resistor_2_node),
    .DEVICE_IDENTIFIER(DEVICE_IDENTIFIER_t), .ROM_VALID(ROM_ADDRESS_VALID),
    .KERNAL_MODE(pull_resistor_1_node), .KERNAL_ROM_B(KERNAL_ROM_B),
    .MAIN_MEMORY_VALID_B(MAIN_MEMORY_VALID_B),
    .SPECIAL_MEMORY_SELECTOR_B({SA_INSTRUCTION_COUNTER_3, SA_INSTRUCTION_COUNTER_2, SA_INSTRUCTION_COUNTER_1, SA_INSTRUCTION_COUNTER_0, address_decode_1_special_memory_selector_b[11:3], SA_FLAG_REGISTER_B, address_decode_1_special_memory_selector_b[1:0]}),
    .SPECIAL_VALID_B(SPECIAL_ADDRESS_VALID_B));
  Pull_Resistor #(.pull(1)) pull_resistor_3 (.node(pull_resistor_3_node));
  LED led_9 (.in(INTERNAL_MEMORY_VALID));
  LED led_10 (.in(SPECIAL_ADDRESS_VALID_B));
  LED led_11 (.in(DEVICE_VALID_B_t));
  LED led_12 (.in(ROM_ADDRESS_VALID));
  LED led_13 (.in(MAIN_MEMORY_VALID_B));
  // Microprocessor__W65C816 microprocessor_w65c816_1: pin names not known; wires that end beside it: pull_resistor_3_node, IRQ_B, NMI_B, RESET, PHI2, microprocessor_w65c816_1_p6, T1, T2, {A8_15, A0_7}, microprocessor_w65c816_1_p10, RWB, RDY, microprocessor_w65c816_1_p13, microprocessor_w65c816_1_p14, microprocessor_w65c816_1_p15, FST_t, VPB
  Interrupt_Vectoring interrupt_vectoring_1 (
    .IRQ_6_B(IRQ_IN[6]), .IRQ_8_B(IRQ_IN[8]), .IRQ_5_B(IRQ_IN[5]), .IRQ_B(IRQ_B), .NMI_3_B(NMI_B_IN[3]),
    .IRQ_7_B(IRQ_IN[7]), .IRQ_0_B(IRQ_IN[0]), .NMI_0_B(NMI_B_IN[0]), .ADDRESS_IN_A0_7(A0_7), .NMI_B(NMI_B),
    .IRQ_1_B(IRQ_IN[1]), .IRQ_4_B(IRQ_IN[4]), .NMI_1_B(NMI_B_IN[1]), .NMI_2_B(NMI_B_IN[2]),
    .IRQ_3_B(IRQ_IN[3]), .IRQ_2_B(IRQ_IN[2]), .ADDRESS_OUT_A0_7(IRAM_A0_7), .VPB(VPB));
  // Probe on {A8_15, A0_7}
  Pull_Resistor #(.pull(1)) pull_resistor_4 (.node(microprocessor_w65c816_1_p15));
  // Probe on microprocessor_w65c816_1_p10
  Signals signals_1 (
    .VPA(microprocessor_w65c816_1_p14), .D(microprocessor_w65c816_1_p10), .READ_ENABLE(READ_ENABLE),
    .OPCODE_ADDRESS(OPCODE_ADDRESS), .CLOCK_ENABLE_B(CLOCK_ENABLE_B), .BA0_7(ADDRESS), .RWB_B(RWB_B),
    .RWB(RWB), .BANK_LATCH(BANK_LATCH), .E(microprocessor_w65c816_1_p6), .WRITE_ENABLE(WRITE_ENABLE),
    .WRITE_SELECTOR(WRITE_SELECTOR), .READ_SELECTOR(READ_SELECTOR), .VDA(microprocessor_w65c816_1_p13),
    .READ_ENABLE_B(READ_ENABLE_B), .NATIVE_MODE(NATIVE_MODE));  // open: WRITE_ENABLE_B
  // _8_bit_Bus_Transceiver__LVC4245 8_bit_bus_transceiver_lvc4245_1: pin names not known; wires that end beside it: DATA_TRANSMIT_B, microprocessor_w65c816_1_p10, RWB, D
  // Probe on {ADDRESS[16], A8_15, IRAM_A0_7}
  nand nand_1 (nand_1_out, INTERNAL_MEMORY_VALID, READ_ENABLE);
  nand nand_2 (nand_2_out, INTERNAL_MEMORY_VALID, WRITE_ENABLE);
  not not_2 (not_2_out, ROM_ADDRESS_VALID);
  or or_1 (or_1_out, not_2_out, READ_ENABLE_B);
  Pull_Resistor pull_resistor_5 (.node({A8_15, A0_7}));
  RAM #(.\type ("nonvolatile"), .addrWidth(17), .databus("bidir"), .trigger("high"), .enables("line")) INTERNAL_MEMORY (
    .addr({ADDRESS[16], A8_15, IRAM_A0_7}), .data(D));  // open: we, oe, clk
  LED led_14 (.in(nand_1_out));
  SRAM_Chipifier sram_chipifier_1 (.WEB(nand_2_out), .OEB(nand_1_out), .CEB(pull_resistor_6_node));  // open: OE, E, WE
  LED led_15 (.in(nand_2_out));
  Pull_Resistor pull_resistor_6 (.node(pull_resistor_6_node));
  // Probe on {A8_15[6:0], IRAM_A0_7}
  ROM #(.addrWidth(16)) KERNAL_ROM (.addr({1'b1, A8_15[6:0], IRAM_A0_7}), .data(KERNAL_ROM_data));
  LED led_16 (.in(or_1_out));
  not not_3 (not_3_out, or_1_out);
  Pull_Resistor pull_resistor_7 (.node(D));
  // Probe on {ADDRESS, A8_15, A0_7}
  // Probe on D
  // Probe on D
  // Probe on D
  assign D = not_3_out ? KERNAL_ROM_data : 8'bz;  // Controlled_Buffer controlled_buffer_1
  Pull_Resistor pull_resistor_8 (.node(MPU_ABILITY[0]));
  Pull_Resistor pull_resistor_9 (.node(MPU_ABILITY[7]));
  Device_MPU_Gateway device_mpu_gateway_1 (
    .MPU_DEVICE_VALID_B(DEVICE_VALID_B_t), .MPU_0_DEVICE_IDENTIFIER(DEVICE_IDENTIFIER_t),
    .CHANNEL_DEVICE_IDENTIFIER(DEVICE_IDENTIFIER), .MPU_D_OUT(D), .CHANNEL_DEVICE_ADDRESS(DEVICE_ADDRESS),
    .MPU_D_IN(D), .MPU_RWB(RWB), .CHANNEL_D_IN(DEVICE_D_IN), .CHANNEL_DEVICE_VALID_B(DEVICE_VALID_B),
    .CHANNEL_RWB(DEVICE_RWB), .MPU_0_DEVICE_ADDRESS(DEVICE_ADDRESS_t), .CHANNEL_D_OUT(DEVICE_D_OUT),
    .SELECTOR_B(DEVICE_STROBE_B));
  Memory_Transceiver memory_transceiver_1 (
    .WE_B(MAIN_MEMORY_WEB), .MAIN_MEMORY_VALID_B(MAIN_MEMORY_VALID_B),
    .ADDRESS_IN_A0_23({ADDRESS, A8_15, A0_7}), .MAIN_MEMORY_D_OUT(MAIN_MEMORY_D_OUT), .RWB(RWB),
    .MAIN_MEMORY_D_IN(MAIN_MEMORY_D_IN), .MEMORY_LOCKOUT(MAIN_MEMORY_LOCKOUT), .OE_B(MAIN_MEMORY_OEB),
    .MPU_D_IN(D), .MPU_D_OUT(D), .RWB_B(RWB_B), .ADDRESS_OUT_A0_23(MAIN_MEMORY_ADDRESS));

  assign MPU_ABILITY[6:1] = {6{MPU_ABILITY[7]}};

  // Other names for the same wires on the sheet: ADDRESS[15:0] = {A8_15, A0_7}; BA0_7[7:0] = ADDRESS;
  //   ABILITY_USER_MODE = MPU_ABILITY[0]; WRITE_ENABLE_B = READ_ENABLE_B

  // Notes on the sheet:
  //   contents of KERNAL_ROM (hex, n*v repeats v):
  //   16384*0 ad fc ff c9 2b e1 f0 2 0 0 e2 20 a9 a4 8d 12 70 a9 cc ad 12 70 1a 8d 12 70 a9 cc ad 12 70 c9
  //   a5 f0 2 0 0 a2 ef cd 9b ae c 6f ac e 6f a9 ff 8d 0 6f a9 42 8f 0 ff 1 a9 43 8f 1 ff 1 a9 0 48 a9 4
  //   48 a9 1c 48 8 40 41184*ff 18 fb c2 30 a9 ff 1 1b e2 20 a9 0 48 ab c2 20 5c 0 40 0 8b b c2 30 48 da
  //   5a 80 39 8b b c2 30 48 da 5a 80 30 8b b c2 30 48 da 5a 80 27 8b b c2 30 48 da 5a e2 20 a9 0 48 ab ae
  //   c 6f ac e 6f 80 12 8b b c2 30 48 da 5a 80 9 8b b c2 30 48 da 5a 80 0 c2 30 7a fa 68 2b ab 40 7771*ff
  //   5a e1 6f e1 51 e1 48 e1 0 0 3f e1 4*ff 78 e1 0 0 78 e1 78 e1 2b e1 78 e1
  //   32KB_ROM
endmodule

module Microcontroller_Board_Kernal_And_User (
  input  RESET_1,
  input  [7:0] SELECTOR,
  input  FST,
  input  [39:0] T1,
  input  [39:0] T2,
  input  MAIN_MEMORY_LOCKOUT,
  input  [1:0] MPU_CHANNEL_D0_1,
  input  [8:0] IRQ_B_IN,
  input  [3:0] NMI_B_IN,
  input  [7:0] MAIN_MEMORY_D_IN,
  input  [7:0] DEVICE_D_IN,
  output [7:0] MPU_ABILITY,
  output RESET,
  output CLOCK_ENABLE_B,
  output [23:0] MAIN_MEMORY_ADDRESS,
  output MAIN_MEMORY_OEB,
  output MAIN_MEMORY_WEB,
  output [7:0] MAIN_MEMORY_D_OUT,
  output MAIN_MEMORY_VALID_B,
  output [1:0] DEVICE_CHANNEL,
  output DEVICE_VALID_B,
  output [5:0] DEVICE_IDENTIFIER,
  output [3:0] DEVICE_ADDRESS,
  output DEVICE_RWB,
  output [7:0] DEVICE_D_OUT
);

  wire BANK_LATCH, DATA_TRANSMIT_B, DEVICE_STROBE_B, DEVICE_VALID_B_t, ENTER_INTERRUPT, EXIT_INTERRUPT,
       FST_t, INTERNAL_MEMORY_VALID, IRQ_B, KERNAL_MODE, KERNAL_MODE_B, KERNAL_ROM_B, LOCK_IN_B,
       microprocessor_w65c816_1_p6, microprocessor_w65c816_1_p13, microprocessor_w65c816_1_p14,
       microprocessor_w65c816_1_p15, MPU_LOCK_IN, NATIVE_MODE, NMI_B, not_1_out, not_2_out, not_3_out,
       not_4_out, not_5_out, OPCODE_ADDRESS, or_1_out, PHI2, pull_resistor_1_node, RDY, READ_BANK_REMAP_B,
       READ_ENABLE, READ_ENABLE_B, READ_SELECTOR, ROM_ADDRESS_VALID, RWB, RWB_B, SA_FLAG_REGISTER_B,
       SA_INSTRUCTION_COUNTER_0, SA_INSTRUCTION_COUNTER_1, SA_INSTRUCTION_COUNTER_2,
       SA_INSTRUCTION_COUNTER_3, SA_INTERRUPTS_IN_DEPTH_B, SA_USER_PROGRAM_ID_B, selector_state_1_sel0,
       selector_state_1_sel1, selector_state_1_sel2, selector_state_1_sel3, selector_state_1_sel4,
       selector_state_1_sel5, selector_state_1_sel6, selector_state_1_sel7, SPECIAL_ADDRESS_VALID_B,
       STOP_SELECTOR, user_mode_memory_glue_1_ceb, user_mode_memory_glue_1_oeb, user_mode_memory_glue_1_web,
       VPB, WRITE_ENABLE, WRITE_SELECTOR;
  wire [3:0] DEVICE_ADDRESS_t;
  wire [5:0] DEVICE_IDENTIFIER_t;
  wire [7:0] A0_7, A8_15, D, interrupt_detection_1_opcode, IRAM_A0_7, KERNAL_ROM_data,
       kernal_user_mode_1_interrupt_depth, microprocessor_w65c816_1_p10, MRAM_A16_23, USER_PROGRAM_ID;
  wire [7:2] flags_register_1_flag_register;
  wire [11:3] address_decode_1_special_memory_selector_b;
  wire [16:0] user_mode_memory_glue_1_address_out_a0_16;
  wire [23:16] ADDRESS;
  wire [31:0] instruction_counter_1_count;

  // Probe on {ADDRESS, A8_15, A0_7}
  LED led_1 (.in(selector_state_1_sel0));
  LED led_2 (.in(selector_state_1_sel1));
  LED led_3 (.in(selector_state_1_sel4));
  LED led_4 (.in(selector_state_1_sel3));
  LED led_5 (.in(selector_state_1_sel2));
  Selector_State selector_state_1 (
    .SEL0(selector_state_1_sel0), .SEL5(selector_state_1_sel5), .DEVICE_STROBE_B(DEVICE_STROBE_B),
    .SEL2(selector_state_1_sel2), .READ_SELECTOR(READ_SELECTOR), .READ_BANK_REMAP_B(READ_BANK_REMAP_B),
    .WRITE_SELECTOR(WRITE_SELECTOR), .RESET(RESET_1), .BOARD_RESET(RESET), .SEL6(selector_state_1_sel6),
    .SELECTOR(SELECTOR), .PHI2(PHI2), .STOP_SELECTOR_B(STOP_SELECTOR), .DATA_TRANSMIT_B(DATA_TRANSMIT_B),
    .SEL1(selector_state_1_sel1), .SEL7(selector_state_1_sel7), .SEL3(selector_state_1_sel3),
    .CLOCK_ENABLE_B(CLOCK_ENABLE_B), .BANK_LATCH(BANK_LATCH), .SEL4(selector_state_1_sel4));  // open: MPU_LOCK_IN
  not not_1 (not_1_out, CLOCK_ENABLE_B);
  and and_1 (FST_t, not_1_out, FST);
  Interrupt_Vectoring interrupt_vectoring_1 (
    .IRQ_6_B(IRQ_B_IN[6]), .IRQ_8_B(IRQ_B_IN[8]), .IRQ_5_B(IRQ_B_IN[5]), .IRQ_B(IRQ_B),
    .NMI_3_B(NMI_B_IN[3]), .IRQ_7_B(IRQ_B_IN[7]), .IRQ_0_B(IRQ_B_IN[0]), .NMI_0_B(NMI_B_IN[0]),
    .ADDRESS_IN_A0_7(A0_7), .NMI_B(NMI_B), .IRQ_1_B(IRQ_B_IN[1]), .IRQ_4_B(IRQ_B_IN[4]),
    .NMI_1_B(NMI_B_IN[1]), .NMI_2_B(NMI_B_IN[2]), .IRQ_3_B(IRQ_B_IN[3]), .IRQ_2_B(IRQ_B_IN[2]),
    .ADDRESS_OUT_A0_7(IRAM_A0_7), .VPB(VPB));
  Flags_Register flags_register_1 (
    .FLAG_REGISTER({flags_register_1_flag_register, KERNAL_ROM_B, LOCK_IN_B}),
    .WRITE_ENABLE_B(READ_ENABLE_B), .D_IN(D), .D_OUT(D), .READ_ENABLE_B(READ_ENABLE_B), .RESET(RESET),
    .SA_FLAG_REGISTER_B(SA_FLAG_REGISTER_B));
  Address_Decode address_decode_1 (
    .DEVICE_CHANNEL(DEVICE_CHANNEL), .ADDRESS_IN_A0_24({ADDRESS, A8_15, A0_7}), .MPU_LOCK_IN(MPU_LOCK_IN),
    .INTERNAL_MEMORY_VALID(INTERNAL_MEMORY_VALID), .RWB(RWB), .DEVICE_ADDRESS(DEVICE_ADDRESS_t),
    .DEVICE_VALID_B(DEVICE_VALID_B_t), .KERNAL_MODE_B(KERNAL_MODE_B),
    .DEVICE_IDENTIFIER(DEVICE_IDENTIFIER_t), .ROM_VALID(ROM_ADDRESS_VALID), .KERNAL_MODE(KERNAL_MODE),
    .KERNAL_ROM_B(KERNAL_ROM_B), .MAIN_MEMORY_VALID_B(MAIN_MEMORY_VALID_B),
    .SPECIAL_MEMORY_SELECTOR_B({SA_INSTRUCTION_COUNTER_3, SA_INSTRUCTION_COUNTER_2, SA_INSTRUCTION_COUNTER_1, SA_INSTRUCTION_COUNTER_0, address_decode_1_special_memory_selector_b, SA_FLAG_REGISTER_B, SA_INTERRUPTS_IN_DEPTH_B, SA_USER_PROGRAM_ID_B}),
    .SPECIAL_VALID_B(SPECIAL_ADDRESS_VALID_B));
  LED led_6 (.in(selector_state_1_sel7));
  LED led_7 (.in(selector_state_1_sel5));
  LED led_8 (.in(selector_state_1_sel6));
  Counter #(.width(32), .max('hffffffff)) counter_1 (.clk(FST_t));  // open: load, D, count, Q, carry, up, clr
  Pull_Resistor #(.pull(1)) pull_resistor_1 (.node(pull_resistor_1_node));
  LED led_9 (.in(INTERNAL_MEMORY_VALID));
  LED led_10 (.in(SPECIAL_ADDRESS_VALID_B));
  LED led_11 (.in(DEVICE_VALID_B_t));
  LED led_12 (.in(ROM_ADDRESS_VALID));
  LED led_13 (.in(MAIN_MEMORY_VALID_B));
  // Microprocessor__W65C816 microprocessor_w65c816_1: pin names not known; wires that end beside it: pull_resistor_1_node, IRQ_B, NMI_B, RESET, PHI2, microprocessor_w65c816_1_p6, T1, T2, {A8_15, A0_7}, microprocessor_w65c816_1_p10, RWB, RDY, microprocessor_w65c816_1_p13, microprocessor_w65c816_1_p14, microprocessor_w65c816_1_p15, FST_t, VPB
  // Probe on {ADDRESS, A8_15, IRAM_A0_7}
  Clock_Control clock_control_1 (
    .DEVICE_ADDRESS_VALID_B(DEVICE_VALID_B_t), .RESET(RESET), .RWB_B(RWB_B),
    .UNSTOPPABLE_CLOCK(STOP_SELECTOR), .ROM_ADDRESS_VALID(ROM_ADDRESS_VALID), .CLOCK_ENABLE_B(CLOCK_ENABLE_B));
  // Probe on {A8_15, A0_7}
  Pull_Resistor #(.pull(1)) pull_resistor_2 (.node(microprocessor_w65c816_1_p15));
  User_Mode_Memory_Glue user_mode_memory_glue_1 (
    .ADDRESS_IN_A0_23({ADDRESS, A8_15, IRAM_A0_7}), .READ_ENABLE(READ_ENABLE), .WRITE_ENABLE(WRITE_ENABLE),
    .INTERNAL_MEMORY_VALID(INTERNAL_MEMORY_VALID), .USER_BANK(USER_PROGRAM_ID),
    .ADDRESS_OUT_A0_16(user_mode_memory_glue_1_address_out_a0_16), .OEB(user_mode_memory_glue_1_oeb),
    .READ_BANK_REMAP_B(READ_BANK_REMAP_B), .CEB(user_mode_memory_glue_1_ceb),
    .WEB(user_mode_memory_glue_1_web));
  not not_2 (not_2_out, PHI2);
  // Probe on microprocessor_w65c816_1_p10
  not not_3 (not_3_out, PHI2);
  // Probe on D
  // Probe on user_mode_memory_glue_1_address_out_a0_16
  RAM #(.\type ("nonvolatile"), .enables("line"), .addrWidth(17), .trigger("high"), .databus("bidir")) INTERNAL_MEMORY (
    .addr(user_mode_memory_glue_1_address_out_a0_16), .data(D));  // open: we, oe, clk
  LED led_14 (.in(user_mode_memory_glue_1_oeb));
  SRAM_Chipifier sram_chipifier_1 (
    .WEB(user_mode_memory_glue_1_web), .OEB(user_mode_memory_glue_1_oeb), .CEB(user_mode_memory_glue_1_ceb));  // open: OE, E, WE
  LED led_15 (.in(user_mode_memory_glue_1_web));
  LED led_16 (.in(user_mode_memory_glue_1_ceb));
  Interrupt_Detection interrupt_detection_1 (
    .LATCH_D(WRITE_SELECTOR), .OPCODE_ADDRESS(OPCODE_ADDRESS), .OPCODE(interrupt_detection_1_opcode),
    .RESET_B(RESET), .ADDRESS_IN_A0(A0_7[0]), .NATIVE_MODE(NATIVE_MODE),
    .RETURN_FROM_INTERRUPT(EXIT_INTERRUPT), .ENTER_INTERRUPT(ENTER_INTERRUPT), .D(D), .PHI2_B(not_2_out));
  Signals signals_1 (
    .VPA(microprocessor_w65c816_1_p14), .D(microprocessor_w65c816_1_p10), .READ_ENABLE(READ_ENABLE),
    .OPCODE_ADDRESS(OPCODE_ADDRESS), .CLOCK_ENABLE_B(CLOCK_ENABLE_B), .BA0_7(ADDRESS), .RWB_B(RWB_B),
    .RWB(RWB), .BANK_LATCH(BANK_LATCH), .E(microprocessor_w65c816_1_p6), .WRITE_ENABLE(WRITE_ENABLE),
    .WRITE_SELECTOR(WRITE_SELECTOR), .READ_SELECTOR(READ_SELECTOR), .VDA(microprocessor_w65c816_1_p13),
    .READ_ENABLE_B(READ_ENABLE_B), .NATIVE_MODE(NATIVE_MODE));  // open: WRITE_ENABLE_B
  not not_4 (not_4_out, ROM_ADDRESS_VALID);
  Instruction_Counter instruction_counter_1 (
    .COUNT(instruction_counter_1_count), .READ_ENABLE_B(READ_ENABLE_B), .OEB_C8_15(SA_INSTRUCTION_COUNTER_1),
    .D_OUT(D), .A0(A0_7[0]), .OEB_C0_7(SA_INSTRUCTION_COUNTER_0), .RESET(RESET),
    .OPCODE_ADDRESS(OPCODE_ADDRESS), .OEB_C24_31(SA_INSTRUCTION_COUNTER_3),
    .OEB_C16_23(SA_INSTRUCTION_COUNTER_2), .PHI2_B(not_3_out));
  // _8_bit_Bus_Transceiver__LVC4245 8_bit_bus_transceiver_lvc4245_1: pin names not known; wires that end beside it: DATA_TRANSMIT_B, microprocessor_w65c816_1_p10, RWB, D
  // Probe on {A8_15[6:0], IRAM_A0_7}
  LED led_17 (.in(or_1_out));
  or or_1 (or_1_out, not_4_out, READ_ENABLE_B);
  // Probe on interrupt_detection_1_opcode
  Pull_Resistor pull_resistor_3 (.node({A8_15, A0_7}));
  ROM #(.addrWidth(16)) KERNAL_ROM (.addr({1'b1, A8_15[6:0], IRAM_A0_7}), .data(KERNAL_ROM_data));
  not not_5 (not_5_out, or_1_out);
  // Probe on instruction_counter_1_count
  Pull_Resistor pull_resistor_4 (.node(D));
  // Probe on D
  // Probe on {ADDRESS, A8_15, A0_7}
  // Probe on D
  assign D = not_5_out ? KERNAL_ROM_data : 8'bz;  // Controlled_Buffer controlled_buffer_1
  // Probe on D
  Kernal_User_Mode kernal_user_mode_1 (
    .INTERRUPT_DEPTH(kernal_user_mode_1_interrupt_depth), .D_OUT(D), .USER(USER_PROGRAM_ID), .BA0_7(ADDRESS),
    .EXIT_INTERRUPT(EXIT_INTERRUPT), .USER_MODE_ABILITY(MPU_ABILITY[0]), .READ_ENABLE_B(READ_ENABLE_B),
    .MAIN_MEMORY_BA0_7(MRAM_A16_23), .KERNAL_MODE(KERNAL_MODE),
    .SA_INTERRUPTS_IN_DEPTH_B(SA_INTERRUPTS_IN_DEPTH_B), .SA_USER_PROGRAM_ID_B(SA_USER_PROGRAM_ID_B),
    .WRITE_ENABLE_B(READ_ENABLE_B), .RESET(RESET), .KERNAL_MODE_B(KERNAL_MODE_B),
    .ENTER_INTERRUPT(ENTER_INTERRUPT), .READ_BANK_REMAP_B(READ_BANK_REMAP_B), .D_IN(D));
  Pull_Resistor pull_resistor_5 (.node(MPU_ABILITY[7]));
  Device_MPU_Gateway device_mpu_gateway_1 (
    .MPU_DEVICE_VALID_B(DEVICE_VALID_B_t), .MPU_0_DEVICE_IDENTIFIER(DEVICE_IDENTIFIER_t),
    .CHANNEL_DEVICE_IDENTIFIER(DEVICE_IDENTIFIER), .MPU_D_OUT(D), .CHANNEL_DEVICE_ADDRESS(DEVICE_ADDRESS),
    .MPU_D_IN(D), .MPU_RWB(RWB), .CHANNEL_D_IN(DEVICE_D_IN), .CHANNEL_DEVICE_VALID_B(DEVICE_VALID_B),
    .CHANNEL_RWB(DEVICE_RWB), .MPU_0_DEVICE_ADDRESS(DEVICE_ADDRESS_t), .CHANNEL_D_OUT(DEVICE_D_OUT),
    .SELECTOR_B(DEVICE_STROBE_B));
  Memory_Transceiver memory_transceiver_1 (
    .WE_B(MAIN_MEMORY_WEB), .MAIN_MEMORY_VALID_B(MAIN_MEMORY_VALID_B),
    .ADDRESS_IN_A0_23({ADDRESS, A8_15, A0_7}), .MAIN_MEMORY_D_OUT(MAIN_MEMORY_D_OUT), .RWB(RWB),
    .MAIN_MEMORY_D_IN(MAIN_MEMORY_D_IN), .MEMORY_LOCKOUT(MAIN_MEMORY_LOCKOUT), .OE_B(MAIN_MEMORY_OEB),
    .MPU_D_IN(D), .MPU_D_OUT(D), .RWB_B(RWB_B), .ADDRESS_OUT_A0_23(MAIN_MEMORY_ADDRESS));
  // Probe on USER_PROGRAM_ID
  // Probe on MRAM_A16_23
  // Probe on kernal_user_mode_1_interrupt_depth

  assign MPU_ABILITY[6:1] = {6{MPU_ABILITY[7]}};

  // Other names for the same wires on the sheet: ADDRESS[15:0] = {A8_15, A0_7}; BA0_7[7:0] = ADDRESS;
  //   ABILITY_USER_MODE = MPU_ABILITY[0]; WRITE_ENABLE_B = READ_ENABLE_B

  // Notes on the sheet:
  //   contents of KERNAL_ROM (hex, n*v repeats v):
  //   16384*0 ad fc ff c9 2b e1 f0 2 0 0 e2 20 a9 a4 8d 12 70 a9 cc ad 12 70 1a 8d 12 70 a9 cc ad 12 70 c9
  //   a5 f0 2 0 0 a2 ef cd 9b ae c 6f ac e 6f a9 ff 8d 0 6f a9 42 8f 0 ff 1 a9 43 8f 1 ff 1 a9 0 48 a9 4
  //   48 a9 1c 48 8 40 41184*ff 18 fb c2 30 a9 ff 1 1b e2 20 a9 0 48 ab c2 20 5c 0 40 0 8b b c2 30 48 da
  //   5a 80 39 8b b c2 30 48 da 5a 80 30 8b b c2 30 48 da 5a 80 27 8b b c2 30 48 da 5a e2 20 a9 0 48 ab ae
  //   c 6f ac e 6f 80 12 8b b c2 30 48 da 5a 80 9 8b b c2 30 48 da 5a 80 0 c2 30 7a fa 68 2b ab 40 7771*ff
  //   5a e1 6f e1 51 e1 48 e1 0 0 3f e1 4*ff 78 e1 0 0 78 e1 78 e1 2b e1 78 e1
  //   32KB_ROM
endmodule

module Video_Board (
  input  [7:0] PALETTE_INDEX_P0_7,
  input  MAIN_MEMORY_VIDEO_0_B,
  input  MAIN_MEMORY_VIDEO_1_B,
  input  MAIN_MEMORY_VIDEO_2_B,
  input  MAIN_MEMORY_PALETTE_B,
  input  [17:0] ADDRESS_A0_17,
  input  OEB,
  input  WEB,
  input  RESET_B,
  input  [1:0] PIXEL_DOUBLING_X,
  input  FRAME_BUFFER,
  input  IRQ_ENABLE,
  input  [7:0] HACTIVE_D4_11,
  input  [7:0] H_FRONT_PORCH_D4_11,
  input  [7:0] H_SYNC_D4_11,
  input  [7:0] H_BACK_PORCH_D4_11,
  input  [7:0] V_ACTIVE_D4_11,
  input  [7:0] V_FRONT_PORCH_D0_7,
  input  [7:0] V_SYNC_D0_7,
  input  [7:0] V_BACK_PORCH_D0_7,
  input  VERTICAL_RASTER_LE,
  input  VERTICAL_RASTER_HIGH_OEB,
  input  VERTICAL_RASTER_LOW_OEB,
  input  CLEAR_IRQ,
  input  CLOCK_OSCILLATOR_SEN,
  input  CLOCK_OSCILLATOR_SCK,
  input  CLOCK_OSCILLATOR_SDI,
  output [7:0] RED,
  output [7:0] GREEN,
  output [7:0] BLUE,
  output H_SYNC,
  output V_SYNC,
  output BLANK_B,
  output IRQ_B,
  output [7:0] V_D0_7,
  output VIDEO_CLOCK
);

  wire not_1_out, or_1_out, or_2_out, pull_resistor_1_node, video_address_1_frame_memory_0_b,
       video_address_1_frame_memory_1_b, video_address_1_frame_memory_2_b,
       video_horizontal_signal_1_h_pixel_valid, video_horizontal_signal_1_h_pixel_valid_b,
       video_horizontal_signal_1_h_sync_pulse, video_horizontal_signal_1_v_clock,
       video_vertical_signal_1_v_pixel_valid, video_vertical_signal_1_v_sync_pulse;
  wire [7:0] video_memory_1_d_out, video_memory_1_palette_d0_7, video_memory_1_pixel_d0_7,
       video_palette_1_d_out;
  wire [17:0] video_address_1_frame_buffer_a0_17;

  Clock clock_1 (.out(VIDEO_CLOCK));
  Video_Address video_address_1 (
    .RESET_B(RESET_B), .FRAME_BUFFER_A0_17(video_address_1_frame_buffer_a0_17),
    .FRAME_MEMORY_0_B(video_address_1_frame_memory_0_b), .START_FRAME_B(or_1_out),
    .FRAME_MEMORY_1_B(video_address_1_frame_memory_1_b), .PIXEL_DOUBLING_X(PIXEL_DOUBLING_X),
    .CLOCK(VIDEO_CLOCK), .FRAME_MEMORY_2_B(video_address_1_frame_memory_2_b));
  Video_Horizontal_Signal video_horizontal_signal_1 (
    .H_PIXEL_VALID(video_horizontal_signal_1_h_pixel_valid), .H_FRONT_PORCH_D4_11(H_FRONT_PORCH_D4_11),
    .HACTIVE_D4_11(HACTIVE_D4_11), .CLOCK(VIDEO_CLOCK), .H_SYNC_D4_11(H_SYNC_D4_11),
    .H_PIXEL_VALID_B(video_horizontal_signal_1_h_pixel_valid_b), .H_BACK_PORCH_D4_11(H_BACK_PORCH_D4_11),
    .H_SYNC_PULSE(video_horizontal_signal_1_h_sync_pulse), .V_CLOCK(video_horizontal_signal_1_v_clock),
    .RESET_B(RESET_B));
  Video_Vertical_Signal video_vertical_signal_1 (
    .V_LOW_OEB(VERTICAL_RASTER_HIGH_OEB), .CLEAR_IRQ(CLEAR_IRQ),
    .V_SYNC_PULSE(video_vertical_signal_1_v_sync_pulse), .V_BACK_PORCH_D0_7(V_BACK_PORCH_D0_7),
    .V_PULSE_LE(VERTICAL_RASTER_LE), .IRQ_B(IRQ_B), .V_PIXEL_VALID(video_vertical_signal_1_v_pixel_valid),
    .RESET_B(RESET_B), .V_ACTIVE_D4_11(V_ACTIVE_D4_11), .V_CLOCK(video_horizontal_signal_1_v_clock),
    .V_SYNC_D0_7(V_SYNC_D0_7), .V_FRONT_PORCH_D0_7(V_FRONT_PORCH_D0_7), .V_D0_7(V_D0_7),
    .V_PIXEL_VALID_B(BLANK_B), .V_HIGH_OEB(VERTICAL_RASTER_LOW_OEB), .IRQ_ENABLE(IRQ_ENABLE));
  or or_1 (or_1_out, video_horizontal_signal_1_h_pixel_valid, video_vertical_signal_1_v_pixel_valid);
  or or_2 (or_2_out, video_horizontal_signal_1_h_pixel_valid_b, BLANK_B);
  not not_1 (not_1_out, FRAME_BUFFER);
  Video_Memory video_memory_1 (
    .MAIN_MEMORY_2_B(MAIN_MEMORY_VIDEO_2_B), .FRAME_BUFFER_0(FRAME_BUFFER), .OEB(OEB),
    .FRAME_MEMORY_2_B(video_address_1_frame_memory_2_b), .FRAME_MEMORY_1_B(video_address_1_frame_memory_1_b),
    .FRAME_BUFFER_A0_17(video_address_1_frame_buffer_a0_17), .WEB(WEB),
    .PALETTE_D0_7(video_memory_1_palette_d0_7), .MAIN_MEMORY_0_B(MAIN_MEMORY_VIDEO_0_B),
    .PALETTE_INDEX(PALETTE_INDEX_P0_7), .D_IN(video_palette_1_d_out),
    .FRAME_MEMORY_0_B(video_address_1_frame_memory_0_b), .MAIN_MEMORY_1_B(MAIN_MEMORY_VIDEO_1_B),
    .PIXEL_D0_7(video_memory_1_pixel_d0_7), .ADDRESS_A0_17(ADDRESS_A0_17), .FRAME_BUFFER_1(not_1_out),
    .D_OUT(video_memory_1_d_out));
  Pull_Resistor pull_resistor_1 (.node(pull_resistor_1_node));
  Video_Palette video_palette_1 (
    .VIDEO_PALETTE_INDEX(video_memory_1_palette_d0_7), .RGB_OEB(pull_resistor_1_node),
    .D_OUT(video_palette_1_d_out), .BLUE(BLUE), .VIDEO_PIXEL_INDEX(video_memory_1_pixel_d0_7), .WEB(WEB),
    .OEB(OEB), .PIXEL_VALID_B(or_2_out), .RGB_LE(VIDEO_CLOCK), .GREEN(GREEN), .RED(RED),
    .MPU_VALID_B(MAIN_MEMORY_PALETTE_B), .D_IN(video_memory_1_d_out), .Address_A0_17(ADDRESS_A0_17));
  Signal_Dragger_2Bit signal_dragger_2bit_1 (
    .INPUT1(video_horizontal_signal_1_h_sync_pulse), .OUTPUT1(H_SYNC), .RESET_B(RESET_B), .CLK(CLEAR_IRQ),
    .INPUT2(video_vertical_signal_1_v_sync_pulse), .OUTPUT2(V_SYNC));
endmodule

module Video_Memory (
  input  [7:0] PALETTE_INDEX,
  input  MAIN_MEMORY_0_B,
  input  MAIN_MEMORY_1_B,
  input  MAIN_MEMORY_2_B,
  input  OEB,
  input  [7:0] D_IN,
  input  WEB,
  input  FRAME_MEMORY_0_B,
  input  FRAME_MEMORY_1_B,
  input  FRAME_MEMORY_2_B,
  input  FRAME_BUFFER_0,
  input  FRAME_BUFFER_1,
  input  [17:0] ADDRESS_A0_17,
  input  [17:0] FRAME_BUFFER_A0_17,
  output [7:0] PIXEL_D0_7,
  output [7:0] PALETTE_D0_7,
  output [7:0] D_OUT
);

  wire and_1_out, or_1_out, or_2_out, pull_resistor_4_node, pull_resistor_11_node;
  wire [4:0] pull_resistor_6_node, pull_resistor_9_node, pull_resistor_13_node, pull_resistor_16_node;
  wire [7:0] selecting_8bit_data_multiplexer_1_d_out, selecting_8bit_data_multiplexer_2_d_out;
  wire [23:0] enabling_24bit_address_multiplexer_1_address_a0_23,
       enabling_24bit_address_multiplexer_2_address_a0_23;
  wire [23:18] undriven, undriven_2, undriven_3, undriven_4;

  Pull_Resistor pull_resistor_1 (.node(pull_resistor_9_node[3]));
  Pull_Resistor #(.pull(1)) pull_resistor_2 (.node(pull_resistor_9_node[2]));
  and and_1 (and_1_out, MAIN_MEMORY_0_B, MAIN_MEMORY_1_B, MAIN_MEMORY_2_B);
  Pull_Resistor #(.pull(1)) pull_resistor_3 (.node(pull_resistor_6_node[4]));
  Pull_Resistor pull_resistor_4 (.node(pull_resistor_4_node));
  Pull_Resistor #(.pull(1)) pull_resistor_5 (.node(pull_resistor_6_node[1]));
  Pull_Resistor #(.pull(1)) pull_resistor_6 (.node(pull_resistor_6_node[0]));
  Pull_Resistor #(.pull(1)) pull_resistor_7 (.node(pull_resistor_9_node[4]));
  Pull_Resistor #(.pull(1)) pull_resistor_8 (.node(pull_resistor_9_node[1]));
  Pull_Resistor #(.pull(1)) pull_resistor_9 (.node(pull_resistor_9_node[0]));
  Pull_Resistor #(.pull(1)) pull_resistor_10 (.node(pull_resistor_13_node[4]));
  Pull_Resistor pull_resistor_11 (.node(pull_resistor_11_node));
  Pull_Resistor #(.pull(1)) pull_resistor_12 (.node(pull_resistor_13_node[1]));
  Pull_Resistor #(.pull(1)) pull_resistor_13 (.node(pull_resistor_13_node[0]));
  Pull_Resistor #(.pull(1)) pull_resistor_14 (.node(pull_resistor_16_node[4]));
  Pull_Resistor #(.pull(1)) pull_resistor_15 (.node(pull_resistor_16_node[1]));
  Pull_Resistor #(.pull(1)) pull_resistor_16 (.node(pull_resistor_16_node[0]));
  or or_1 (or_1_out, FRAME_BUFFER_0, and_1_out);
  or or_2 (or_2_out, and_1_out, FRAME_BUFFER_1);
  Selecting_8Bit_Data_Multiplexer selecting_8bit_data_multiplexer_1 (
    .OE(pull_resistor_4_node), .D_OUT(selecting_8bit_data_multiplexer_1_d_out), .S(FRAME_BUFFER_0),
    .DATA_0_D0_7({MAIN_MEMORY_0_B, MAIN_MEMORY_1_B, MAIN_MEMORY_2_B, pull_resistor_6_node[4], OEB, WEB, pull_resistor_6_node[1:0]}),
    .DATA_1_D0_8({FRAME_MEMORY_0_B, FRAME_MEMORY_1_B, FRAME_MEMORY_2_B, pull_resistor_9_node}));
  Enabling_24Bit_Address_Multiplexer enabling_24bit_address_multiplexer_1 (
    .OEB_0(FRAME_BUFFER_1), .ADDRESS_0_A0_23({undriven, ADDRESS_A0_17}),
    .ADDRESS_1_A0_23({undriven_2, FRAME_BUFFER_A0_17}), .OEB_1(FRAME_BUFFER_0),
    .ADDRESS_A0_23(enabling_24bit_address_multiplexer_1_address_a0_23));
  Selecting_8Bit_Data_Multiplexer selecting_8bit_data_multiplexer_2 (
    .OE(pull_resistor_11_node), .D_OUT(selecting_8bit_data_multiplexer_2_d_out), .S(FRAME_BUFFER_1),
    .DATA_0_D0_7({MAIN_MEMORY_0_B, MAIN_MEMORY_1_B, MAIN_MEMORY_2_B, pull_resistor_13_node[4], OEB, WEB, pull_resistor_13_node[1:0]}),
    .DATA_1_D0_8({FRAME_MEMORY_0_B, FRAME_MEMORY_1_B, FRAME_MEMORY_2_B, pull_resistor_16_node[4], pull_resistor_9_node[3:2], pull_resistor_16_node[1:0]}));
  Enabling_24Bit_Address_Multiplexer enabling_24bit_address_multiplexer_2 (
    .OEB_0(FRAME_BUFFER_0), .ADDRESS_0_A0_23({undriven_3, ADDRESS_A0_17}),
    .ADDRESS_1_A0_23({undriven_4, FRAME_BUFFER_A0_17}), .OEB_1(FRAME_BUFFER_1),
    .ADDRESS_A0_23(enabling_24bit_address_multiplexer_2_address_a0_23));
  Video_Frame_Buffer video_frame_buffer_1 (
    .MPU_ENABLE_B(or_1_out), .CEB_2(selecting_8bit_data_multiplexer_1_d_out[5]),
    .OEB(selecting_8bit_data_multiplexer_1_d_out[3]), .PALETTE_INDEX_IN(PALETTE_INDEX), .D_IN(D_IN),
    .CEB_1(selecting_8bit_data_multiplexer_1_d_out[6]), .CEB_0(selecting_8bit_data_multiplexer_1_d_out[7]),
    .VIDEO_BUFFER_ENABLE_B(FRAME_BUFFER_1), .PIXEL_OUT_D0_7(PIXEL_D0_7),
    .WEB(selecting_8bit_data_multiplexer_1_d_out[2]), .D_OUT(D_OUT),
    .Address_A0_17(enabling_24bit_address_multiplexer_1_address_a0_23[17:0]), .PALETTE_OUT_D0_7(PALETTE_D0_7));
  Video_Frame_Buffer video_frame_buffer_2 (
    .MPU_ENABLE_B(or_2_out), .CEB_2(selecting_8bit_data_multiplexer_2_d_out[5]),
    .OEB(selecting_8bit_data_multiplexer_2_d_out[3]), .PALETTE_INDEX_IN(PALETTE_INDEX), .D_IN(D_IN),
    .CEB_1(selecting_8bit_data_multiplexer_2_d_out[6]), .CEB_0(selecting_8bit_data_multiplexer_2_d_out[7]),
    .VIDEO_BUFFER_ENABLE_B(FRAME_BUFFER_0), .PIXEL_OUT_D0_7(PIXEL_D0_7),
    .WEB(selecting_8bit_data_multiplexer_2_d_out[2]), .D_OUT(D_OUT),
    .Address_A0_17(enabling_24bit_address_multiplexer_2_address_a0_23[17:0]), .PALETTE_OUT_D0_7(PALETTE_D0_7));
endmodule

module Video_Horizontal_Signal (
  input  RESET_B,
  input  CLOCK,
  input  [7:0] HACTIVE_D4_11,
  input  [7:0] H_FRONT_PORCH_D4_11,
  input  [7:0] H_SYNC_D4_11,
  input  [7:0] H_BACK_PORCH_D4_11,
  output H_PIXEL_VALID,
  output H_PIXEL_VALID_B,
  output H_SYNC_PULSE,
  output V_CLOCK
);

  wire and_2_out, and_3_out, n4_bit_up_counter_lvc163_1_p1, n4_bit_up_counter_lvc163_1_p7,
       n4_bit_up_counter_lvc163_2_p7, n8_bit_comparator_f521_1_p3, n8_bit_comparator_f521_2_p3,
       n8_bit_comparator_f521_3_p3, n8_bit_comparator_f521_4_p3, nand_1_out, or_1_out, pull_resistor_2_node,
       pull_resistor_3_node, pull_resistor_5_node, pull_resistor_7_node;
  wire [3:0] n4_bit_up_counter_lvc163_3_p6;
  wire [7:0] n4_bit_up_counter_lvc163_1_p6;

  Pull_Resistor #(.pull(1)) pull_resistor_1 ();  // open: node
  Pull_Resistor #(.pull(1)) pull_resistor_2 (.node(pull_resistor_2_node));
  Pull_Resistor #(.pull(1)) pull_resistor_3 (.node(pull_resistor_3_node));
  // _4_bit_Up_Counter__LVC163 4_bit_up_counter_lvc163_1: pin names not known; wires that end beside it: n4_bit_up_counter_lvc163_1_p1, pull_resistor_2_node, CLOCK, pull_resistor_3_node, pull_resistor_3_node, n4_bit_up_counter_lvc163_1_p6[3:0], n4_bit_up_counter_lvc163_1_p7
  Pull_Resistor #(.pull(1)) pull_resistor_4 ();  // open: node
  Pull_Resistor #(.pull(1)) pull_resistor_5 (.node(pull_resistor_5_node));
  // _4_bit_Up_Counter__LVC163 4_bit_up_counter_lvc163_2: pin names not known; wires that end beside it: n4_bit_up_counter_lvc163_1_p1, pull_resistor_5_node, CLOCK, n4_bit_up_counter_lvc163_1_p7, pull_resistor_3_node, n4_bit_up_counter_lvc163_1_p6[7:4], n4_bit_up_counter_lvc163_2_p7
  nand nand_1 (nand_1_out, n4_bit_up_counter_lvc163_1_p6[3], n4_bit_up_counter_lvc163_1_p6[2], n4_bit_up_counter_lvc163_1_p6[1], n4_bit_up_counter_lvc163_1_p6[0]);
  Pull_Resistor #(.pull(1)) pull_resistor_6 ();  // open: node
  Pull_Resistor #(.pull(1)) pull_resistor_7 (.node(pull_resistor_7_node));
  // _4_bit_Up_Counter__LVC163 4_bit_up_counter_lvc163_3: pin names not known; wires that end beside it: n4_bit_up_counter_lvc163_1_p1, pull_resistor_7_node, CLOCK, n4_bit_up_counter_lvc163_2_p7, pull_resistor_3_node, n4_bit_up_counter_lvc163_3_p6
  // Probe on {n4_bit_up_counter_lvc163_3_p6, n4_bit_up_counter_lvc163_1_p6}
  // Probe on {HACTIVE_D4_11, 4'b0000}
  // Probe on {H_FRONT_PORCH_D4_11, 4'b0000}
  // Probe on {H_SYNC_D4_11, 4'b0000}
  // Probe on {H_BACK_PORCH_D4_11, 4'b0000}
  Pull_Resistor pull_resistor_8 ();  // open: node
  Pull_Resistor pull_resistor_9 ();  // open: node
  Pull_Resistor pull_resistor_10 ();  // open: node
  Pull_Resistor pull_resistor_11 ();  // open: node
  and and_1 (n4_bit_up_counter_lvc163_1_p1, RESET_B, or_1_out);
  // _8_bit_Comparator__F521 8_bit_comparator_f521_1: pin names not known; wires that end beside it: {n4_bit_up_counter_lvc163_3_p6, n4_bit_up_counter_lvc163_1_p6[7:4]}, HACTIVE_D4_11, n8_bit_comparator_f521_1_p3
  // _8_bit_Comparator__F521 8_bit_comparator_f521_2: pin names not known; wires that end beside it: {n4_bit_up_counter_lvc163_3_p6, n4_bit_up_counter_lvc163_1_p6[7:4]}, H_FRONT_PORCH_D4_11, n8_bit_comparator_f521_2_p3
  // _8_bit_Comparator__F521 8_bit_comparator_f521_3: pin names not known; wires that end beside it: {n4_bit_up_counter_lvc163_3_p6, n4_bit_up_counter_lvc163_1_p6[7:4]}, H_SYNC_D4_11, n8_bit_comparator_f521_3_p3
  // _8_bit_Comparator__F521 8_bit_comparator_f521_4: pin names not known; wires that end beside it: {n4_bit_up_counter_lvc163_3_p6, n4_bit_up_counter_lvc163_1_p6[7:4]}, H_BACK_PORCH_D4_11, n8_bit_comparator_f521_4_p3
  and and_2 (and_2_out, RESET_B, n8_bit_comparator_f521_1_p3);
  and and_3 (and_3_out, RESET_B, n8_bit_comparator_f521_2_p3);
  or or_1 (or_1_out, n8_bit_comparator_f521_4_p3, nand_1_out);
  Pull_Resistor pull_resistor_12 ();  // open: node
  Pull_Resistor #(.pull(1)) pull_resistor_13 ();  // open: node
  Pull_Resistor pull_resistor_14 ();  // open: node
  Pull_Resistor #(.pull(1)) pull_resistor_15 ();  // open: node
  // D_type_Flip_Flop__LVC74 d_type_flip_flop_lvc74_1: pin names not known; wires that end beside it: and_2_out, or_1_out, and_3_out, n8_bit_comparator_f521_3_p3, H_PIXEL_VALID, H_SYNC_PULSE, H_PIXEL_VALID_B
  not not_1 (V_CLOCK, or_1_out);

  // Notes on the sheet:
  //   640x480x60 = $28 $29 $2d $31
endmodule

module Video_Vertical_Signal (
  input  RESET_B,
  input  V_CLOCK,
  input  [7:0] V_ACTIVE_D4_11,
  input  [7:0] V_FRONT_PORCH_D0_7,
  input  [7:0] V_SYNC_D0_7,
  input  [7:0] V_BACK_PORCH_D0_7,
  input  CLEAR_IRQ,
  input  IRQ_ENABLE,
  input  V_PULSE_LE,
  input  V_LOW_OEB,
  input  V_HIGH_OEB,
  output V_PIXEL_VALID,
  output V_PIXEL_VALID_B,
  output V_SYNC_PULSE,
  output IRQ_B,
  output [7:0] V_D0_7
);

  wire and_1_out, and_2_out, and_3_out, d_type_flip_flop_lvc74_1_p8, n4_bit_up_counter_lvc161_1_p7,
       n8_bit_comparator_f521_1_p3, n8_bit_comparator_f521_2_p3, n8_bit_comparator_f521_3_p3,
       n8_bit_comparator_f521_4_p3, nand_1_out, not_1_out, not_2_out, not_3_out, not_4_out, not_5_out,
       not_6_out, not_7_out, or_1_out, pull_resistor_2_node, pull_resistor_3_node, pull_resistor_6_node,
       pull_resistor_8_node;
  wire [3:0] n4_bit_up_counter_lvc161_1_p6, n4_bit_up_counter_lvc161_2_p6, n12_bit_up_counter_hc4040_1_p3_2,
       pull_resistor_12_node;
  wire [7:0] n12_bit_up_counter_hc4040_1_p3;

  and and_1 (and_1_out, n8_bit_comparator_f521_4_p3, RESET_B);
  not not_1 (not_1_out, and_1_out);
  // _12_bit_Up_Counter__HC4040 12_bit_up_counter_hc4040_1: pin names not known; wires that end beside it: not_1_out, V_CLOCK, {n12_bit_up_counter_hc4040_1_p3_2, n12_bit_up_counter_hc4040_1_p3}
  // Probe on {V_ACTIVE_D4_11, 4'b0000}
  // Probe on {n12_bit_up_counter_hc4040_1_p3_2, n12_bit_up_counter_hc4040_1_p3[7:4]}
  Pull_Resistor pull_resistor_1 ();  // open: node
  not not_2 (not_2_out, n12_bit_up_counter_hc4040_1_p3[3]);
  not not_3 (not_3_out, n12_bit_up_counter_hc4040_1_p3[2]);
  nand nand_1 (nand_1_out, not_2_out, not_3_out, not_4_out, not_5_out);
  not not_4 (not_4_out, n12_bit_up_counter_hc4040_1_p3[1]);
  not not_5 (not_5_out, n12_bit_up_counter_hc4040_1_p3[0]);
  // _8_bit_Comparator__F521 8_bit_comparator_f521_1: pin names not known; wires that end beside it: {n12_bit_up_counter_hc4040_1_p3_2, n12_bit_up_counter_hc4040_1_p3[7:4]}, V_ACTIVE_D4_11, n8_bit_comparator_f521_1_p3
  and and_2 (and_2_out, RESET_B, or_1_out);
  or or_1 (or_1_out, n8_bit_comparator_f521_1_p3, nand_1_out);
  and and_3 (and_3_out, RESET_B, not_6_out);
  not not_6 (not_6_out, CLEAR_IRQ);
  Pull_Resistor pull_resistor_2 (.node(pull_resistor_2_node));
  Pull_Resistor #(.pull(1)) pull_resistor_3 (.node(pull_resistor_3_node));
  not not_7 (not_7_out, and_2_out);
  Pull_Resistor #(.pull(1)) pull_resistor_4 ();  // open: node
  Pull_Resistor #(.pull(1)) pull_resistor_5 ();  // open: node
  Pull_Resistor #(.pull(1)) pull_resistor_6 (.node(pull_resistor_6_node));
  // D_type_Flip_Flop__LVC74 d_type_flip_flop_lvc74_1: pin names not known; wires that end beside it: and_1_out, and_2_out, and_3_out, pull_resistor_2_node, pull_resistor_3_node, not_7_out, IRQ_ENABLE, d_type_flip_flop_lvc74_1_p8, IRQ_B
  // _4_bit_Up_Counter__LVC161 4_bit_up_counter_lvc161_1: pin names not known; wires that end beside it: and_2_out, pull_resistor_6_node, V_CLOCK, d_type_flip_flop_lvc74_1_p8, d_type_flip_flop_lvc74_1_p8, n4_bit_up_counter_lvc161_1_p6, n4_bit_up_counter_lvc161_1_p7
  Pull_Resistor #(.pull(1)) pull_resistor_7 ();  // open: node
  Pull_Resistor #(.pull(1)) pull_resistor_8 (.node(pull_resistor_8_node));
  // _4_bit_Up_Counter__LVC161 4_bit_up_counter_lvc161_2: pin names not known; wires that end beside it: and_2_out, pull_resistor_8_node, V_CLOCK, n4_bit_up_counter_lvc161_1_p7, d_type_flip_flop_lvc74_1_p8, n4_bit_up_counter_lvc161_2_p6
  // Probe on {n4_bit_up_counter_lvc161_2_p6, n4_bit_up_counter_lvc161_1_p6}
  Pull_Resistor pull_resistor_9 ();  // open: node
  Pull_Resistor pull_resistor_10 ();  // open: node
  Pull_Resistor pull_resistor_11 ();  // open: node
  // _8_bit_Comparator__F521 8_bit_comparator_f521_2: pin names not known; wires that end beside it: {n4_bit_up_counter_lvc161_2_p6, n4_bit_up_counter_lvc161_1_p6}, V_FRONT_PORCH_D0_7, n8_bit_comparator_f521_2_p3
  // _8_bit_Comparator__F521 8_bit_comparator_f521_3: pin names not known; wires that end beside it: {n4_bit_up_counter_lvc161_2_p6, n4_bit_up_counter_lvc161_1_p6}, V_SYNC_D0_7, n8_bit_comparator_f521_3_p3
  // _8_bit_Comparator__F521 8_bit_comparator_f521_4: pin names not known; wires that end beside it: {n4_bit_up_counter_lvc161_2_p6, n4_bit_up_counter_lvc161_1_p6}, V_BACK_PORCH_D0_7, n8_bit_comparator_f521_4_p3
  Pull_Resistor pull_resistor_12 (.node(pull_resistor_12_node));
  Pull_Resistor pull_resistor_13 ();  // open: node
  Pull_Resistor #(.pull(1)) pull_resistor_14 ();  // open: node
  Pull_Resistor pull_resistor_15 ();  // open: node
  Pull_Resistor #(.pull(1)) pull_resistor_16 ();  // open: node
  // D_type_Flip_Flop__LVC74 d_type_flip_flop_lvc74_2: pin names not known; wires that end beside it: and_2_out, n8_bit_comparator_f521_4_p3, n8_bit_comparator_f521_2_p3, n8_bit_comparator_f521_3_p3, V_PIXEL_VALID, V_PIXEL_VALID_B, V_SYNC_PULSE
  // _8_bit_Latch__LVC574 8_bit_latch_lvc574_1: pin names not known; wires that end beside it: V_HIGH_OEB, {pull_resistor_12_node, n12_bit_up_counter_hc4040_1_p3_2}, V_PULSE_LE, V_D0_7
  // _8_bit_Latch__LVC574 8_bit_latch_lvc574_2: pin names not known; wires that end beside it: V_LOW_OEB, n12_bit_up_counter_hc4040_1_p3, V_PULSE_LE, V_D0_7

  // Notes on the sheet:
  //   640x480x60 = $1d $03 $07 $14
endmodule

module Video_Address (
  input  START_FRAME_B,
  input  RESET_B,
  input  CLOCK,
  input  [1:0] PIXEL_DOUBLING_X,
  output FRAME_MEMORY_0_B,
  output FRAME_MEMORY_1_B,
  output FRAME_MEMORY_2_B,
  output [17:0] FRAME_BUFFER_A0_17
);

  wire and_1_out, d_ff_1_qn, d_ff_2_qn, n4_bit_up_counter_lvc163_1_p3, n4_bit_up_counter_lvc163_1_p7,
       n4_bit_up_counter_lvc163_2_p7, n4_bit_up_counter_lvc163_3_p7, n4_bit_up_counter_lvc163_4_p7,
       not_1_out, not_2_out, pull_resistor_2_node, pull_resistor_3_node, pull_resistor_4_node,
       pull_resistor_6_node, pull_resistor_7_node, pull_resistor_8_node, pull_resistor_10_node,
       pull_resistor_11_node, pull_resistor_13_node, pull_resistor_14_node, pull_resistor_16_node,
       pull_resistor_17_node, pull_resistor_19_node, pull_resistor_20_node, pull_resistor_23_node;
  wire [3:1] d_ff_1_q;
  wire [3:2] n4_bit_up_counter_lvc163_5_p6;
  wire [3:3] n2_to_4_decoder_lvc139_1_p3;

  and and_1 (and_1_out, START_FRAME_B, RESET_B);
  Pull_Resistor #(.pull(1)) pull_resistor_1 ();  // open: node
  Pull_Resistor #(.pull(1)) pull_resistor_2 (.node(pull_resistor_2_node));
  Pull_Resistor #(.pull(1)) pull_resistor_3 (.node(pull_resistor_3_node));
  Pull_Resistor #(.pull(1)) pull_resistor_4 (.node(pull_resistor_4_node));
  D_Flip_Flop d_ff_1 (.clk(CLOCK), .D(d_ff_1_qn), .Q(d_ff_1_q[1]), .Qn(d_ff_1_qn), .reset(not_1_out));  // open: preset
  Pull_Resistor pull_resistor_5 (.node(d_ff_1_q[3]));
  not not_1 (not_1_out, RESET_B);
  D_Flip_Flop d_ff_2 (
    .clk(d_ff_1_qn), .D(d_ff_2_qn), .Q(d_ff_1_q[2]), .Qn(d_ff_2_qn), .reset(not_2_out));  // open: preset
  Pull_Resistor #(.pull(1)) pull_resistor_6 (.node(pull_resistor_6_node));
  not not_2 (not_2_out, RESET_B);
  // _4_bit_Up_Counter__LVC163 4_bit_up_counter_lvc163_1: pin names not known; wires that end beside it: and_1_out, pull_resistor_2_node, n4_bit_up_counter_lvc163_1_p3, pull_resistor_3_node, pull_resistor_4_node, FRAME_BUFFER_A0_17[3:0], n4_bit_up_counter_lvc163_1_p7
  Pull_Resistor #(.pull(1)) pull_resistor_7 (.node(pull_resistor_7_node));
  Pull_Resistor pull_resistor_8 (.node(pull_resistor_8_node));
  // _4_to_1_Multiplexer__QS3253 4_to_1_multiplexer_qs3253_1: pin names not known; wires that end beside it: pull_resistor_8_node, pull_resistor_7_node, PIXEL_DOUBLING_X, {d_ff_1_q, CLOCK}, pull_resistor_6_node, n4_bit_up_counter_lvc163_1_p3
  Pull_Resistor #(.pull(1)) pull_resistor_9 ();  // open: node
  Pull_Resistor #(.pull(1)) pull_resistor_10 (.node(pull_resistor_10_node));
  Pull_Resistor #(.pull(1)) pull_resistor_11 (.node(pull_resistor_11_node));
  // _4_bit_Up_Counter__LVC163 4_bit_up_counter_lvc163_2: pin names not known; wires that end beside it: and_1_out, pull_resistor_10_node, n4_bit_up_counter_lvc163_1_p3, n4_bit_up_counter_lvc163_1_p7, pull_resistor_11_node, FRAME_BUFFER_A0_17[7:4], n4_bit_up_counter_lvc163_2_p7
  Pull_Resistor #(.pull(1)) pull_resistor_12 ();  // open: node
  Pull_Resistor #(.pull(1)) pull_resistor_13 (.node(pull_resistor_13_node));
  Pull_Resistor #(.pull(1)) pull_resistor_14 (.node(pull_resistor_14_node));
  // _4_bit_Up_Counter__LVC163 4_bit_up_counter_lvc163_3: pin names not known; wires that end beside it: and_1_out, pull_resistor_13_node, n4_bit_up_counter_lvc163_1_p3, n4_bit_up_counter_lvc163_2_p7, pull_resistor_14_node, FRAME_BUFFER_A0_17[11:8], n4_bit_up_counter_lvc163_3_p7
  Pull_Resistor #(.pull(1)) pull_resistor_15 ();  // open: node
  Pull_Resistor #(.pull(1)) pull_resistor_16 (.node(pull_resistor_16_node));
  Pull_Resistor #(.pull(1)) pull_resistor_17 (.node(pull_resistor_17_node));
  // _4_bit_Up_Counter__LVC163 4_bit_up_counter_lvc163_4: pin names not known; wires that end beside it: and_1_out, pull_resistor_16_node, n4_bit_up_counter_lvc163_1_p3, n4_bit_up_counter_lvc163_3_p7, pull_resistor_17_node, FRAME_BUFFER_A0_17[15:12], n4_bit_up_counter_lvc163_4_p7
  Pull_Resistor #(.pull(1)) pull_resistor_18 ();  // open: node
  Pull_Resistor #(.pull(1)) pull_resistor_19 (.node(pull_resistor_19_node));
  Pull_Resistor #(.pull(1)) pull_resistor_20 (.node(pull_resistor_20_node));
  // _4_bit_Up_Counter__LVC163 4_bit_up_counter_lvc163_5: pin names not known; wires that end beside it: and_1_out, pull_resistor_19_node, n4_bit_up_counter_lvc163_1_p3, n4_bit_up_counter_lvc163_4_p7, pull_resistor_20_node, {n4_bit_up_counter_lvc163_5_p6, FRAME_BUFFER_A0_17[17:16]}
  Pull_Resistor pull_resistor_21 ();  // open: node
  Pull_Resistor #(.pull(1)) pull_resistor_22 ();  // open: node
  Pull_Resistor #(.pull(1)) pull_resistor_23 (.node(pull_resistor_23_node));
  // _2_to_4_Decoder__LVC139 2_to_4_decoder_lvc139_1: pin names not known; wires that end beside it: n4_bit_up_counter_lvc163_5_p6, pull_resistor_23_node, {n2_to_4_decoder_lvc139_1_p3[3], FRAME_MEMORY_2_B, FRAME_MEMORY_1_B, FRAME_MEMORY_0_B}

  // Notes on the sheet:
  //   Source Address
endmodule

module Video_Frame_Buffer (
  input  [7:0] D_IN,
  input  MPU_ENABLE_B,
  input  VIDEO_BUFFER_ENABLE_B,
  input  [7:0] PALETTE_INDEX_IN,
  input  OEB,
  input  WEB,
  input  CEB_0,
  input  CEB_1,
  input  CEB_2,
  input  [17:0] Address_A0_17,
  output [7:0] D_OUT,
  output [7:0] PALETTE_OUT_D0_7,
  output [7:0] PIXEL_OUT_D0_7
);

  wire bidirectional_monsters_1_read, bidirectional_monsters_1_write;
  wire [7:0] n8_bit_bus_transceiver_lvc4245_1_p4;
  wire [15:0] ram_1_data;

  SRAM_Chipifier sram_chipifier_1 (.WEB(WEB), .OEB(OEB), .CEB(CEB_0));  // open: OE, E, WE
  SRAM_Chipifier sram_chipifier_2 (.WEB(WEB), .OEB(OEB), .CEB(CEB_1));  // open: OE, E, WE
  SRAM_Chipifier sram_chipifier_3 (.WEB(WEB), .OEB(OEB), .CEB(CEB_2));  // open: OE, E, WE
  RAM #(.dataWidth(16), .enables("line"), .trigger("high"), .addrWidth(18), .databus("bidir"), .\type ("nonvolatile")) ram_1 (
    .addr(Address_A0_17), .data(ram_1_data));  // open: we, oe, clk
  RAM #(.databus("bidir"), .enables("line"), .\type ("nonvolatile"), .trigger("high"), .dataWidth(16), .addrWidth(18)) ram_2 (
    .addr(Address_A0_17), .data(ram_1_data));  // open: we, oe, clk
  RAM #(.dataWidth(16), .enables("line"), .addrWidth(18), .databus("bidir"), .trigger("high"), .\type ("nonvolatile")) ram_3 (
    .addr(Address_A0_17), .data(ram_1_data));  // open: we, oe, clk
  // _8_bit_Line_Driver__LVC541 8_bit_line_driver_lvc541_1: pin names not known; wires that end beside it: MPU_ENABLE_B, WEB, PALETTE_INDEX_IN, ram_1_data[15:8]
  // Probe on ram_1_data
  // _8_bit_Bus_Transceiver__LVC4245 8_bit_bus_transceiver_lvc4245_1: pin names not known; wires that end beside it: MPU_ENABLE_B, ram_1_data[7:0], OEB, n8_bit_bus_transceiver_lvc4245_1_p4
  // _16_bit_Line_Driver__LVC16244 16_bit_line_driver_lvc16244_1: pin names not known; wires that end beside it: VIDEO_BUFFER_ENABLE_B, VIDEO_BUFFER_ENABLE_B, VIDEO_BUFFER_ENABLE_B, VIDEO_BUFFER_ENABLE_B, ram_1_data[11:8], ram_1_data[15:12], ram_1_data[3:0], ram_1_data[7:4], PALETTE_OUT_D0_7[3:0], PALETTE_OUT_D0_7[7:4], PIXEL_OUT_D0_7[3:0], PIXEL_OUT_D0_7[7:4]
  // Probe on n8_bit_bus_transceiver_lvc4245_1_p4
  // Probe on PALETTE_OUT_D0_7
  // Probe on PIXEL_OUT_D0_7
  assign n8_bit_bus_transceiver_lvc4245_1_p4 = bidirectional_monsters_1_read ? D_IN : 8'bz;  // Controlled_Buffer controlled_buffer_1
  assign D_OUT = bidirectional_monsters_1_write ? n8_bit_bus_transceiver_lvc4245_1_p4 : 8'bz;  // Controlled_Buffer controlled_buffer_2
  Bidirectional_Monsters bidirectional_monsters_1 (
    .WRITE(bidirectional_monsters_1_write), .READ(bidirectional_monsters_1_read), .RWB(OEB),
    .ENABLE_B(MPU_ENABLE_B));
endmodule
module Video_Palette (
  input  [7:0] D_IN,
  input  [17:0] Address_A0_17,
  input  MPU_VALID_B,
  input  OEB,
  input  WEB,
  input  PIXEL_VALID_B,
  input  [7:0] VIDEO_PALETTE_INDEX,
  input  [7:0] VIDEO_PIXEL_INDEX,
  input  RGB_OEB,
  input  RGB_LE,
  output [7:0] D_OUT,
  output [7:0] RED,
  output [7:0] GREEN,
  output [7:0] BLUE
);

  wire and_1_out, and_2_out, and_3_out, bidirectional_monsters_1_read, bidirectional_monsters_1_write,
       not_1_out, pull_resistor_1_node, pull_resistor_2_node, pull_resistor_8_node;
  wire [3:0] n2_to_4_decoder_lvc139_1_p5, n4_bit_multiplexer_lvc257_1_p5, n16_bit_line_driver_lvc16244_1_p9,
       n16_bit_line_driver_lvc16244_1_p10, n16_bit_line_driver_lvc16244_1_p11,
       n16_bit_line_driver_lvc16244_1_p12;
  wire [3:1] pull_resistor_5_node;
  wire [3:2] pull_resistor_3_node;
  wire [7:0] n8_bit_bus_transceiver_lvc4245_1_p4, ram_1_data, ram_2_data, ram_3_data;
  wire [7:7] n8_bit_line_driver_lvc541_1_p4;

  Pull_Resistor #(.pull(1)) pull_resistor_1 (.node(pull_resistor_1_node));
  Pull_Resistor #(.pull(1)) pull_resistor_2 (.node(pull_resistor_2_node));
  not not_1 (not_1_out, MPU_VALID_B);
  Pull_Resistor pull_resistor_3 (.node(pull_resistor_3_node[2]));
  Pull_Resistor pull_resistor_4 (.node(pull_resistor_3_node[3]));
  Pull_Resistor #(.pull(1)) pull_resistor_5 (.node(pull_resistor_5_node[1]));
  Pull_Resistor pull_resistor_6 (.node(pull_resistor_5_node[2]));
  Pull_Resistor pull_resistor_7 (.node(pull_resistor_5_node[3]));
  // _2_to_4_Decoder__LVC139 2_to_4_decoder_lvc139_1: pin names not known; wires that end beside it: MPU_VALID_B, pull_resistor_1_node, Address_A0_17[17:16], pull_resistor_2_node, n2_to_4_decoder_lvc139_1_p5
  // _16_bit_Line_Driver__LVC16244 16_bit_line_driver_lvc16244_1: pin names not known; wires that end beside it: MPU_VALID_B, MPU_VALID_B, MPU_VALID_B, MPU_VALID_B, Address_A0_17[15:12], Address_A0_17[11:8], Address_A0_17[7:4], Address_A0_17[3:0], n16_bit_line_driver_lvc16244_1_p9, n16_bit_line_driver_lvc16244_1_p10, n16_bit_line_driver_lvc16244_1_p11, n16_bit_line_driver_lvc16244_1_p12
  Pull_Resistor pull_resistor_8 (.node(pull_resistor_8_node));
  // _8_bit_Line_Driver__LVC541 8_bit_line_driver_lvc541_1: pin names not known; wires that end beside it: PIXEL_VALID_B, not_1_out, VIDEO_PALETTE_INDEX, {n8_bit_line_driver_lvc541_1_p4[7], n16_bit_line_driver_lvc16244_1_p9[2:0], n16_bit_line_driver_lvc16244_1_p10}
  // _8_bit_Line_Driver__LVC541 8_bit_line_driver_lvc541_2: pin names not known; wires that end beside it: PIXEL_VALID_B, not_1_out, VIDEO_PIXEL_INDEX, {n16_bit_line_driver_lvc16244_1_p11, n16_bit_line_driver_lvc16244_1_p12}
  // _4_bit_Multiplexer__LVC257 4_bit_multiplexer_lvc257_1: pin names not known; wires that end beside it: pull_resistor_8_node, MPU_VALID_B, {pull_resistor_3_node, WEB, OEB}, {pull_resistor_5_node, PIXEL_VALID_B}, n4_bit_multiplexer_lvc257_1_p5
  // Probe on {n16_bit_line_driver_lvc16244_1_p9[2:0], n16_bit_line_driver_lvc16244_1_p10, n16_bit_line_driver_lvc16244_1_p11, n16_bit_line_driver_lvc16244_1_p12}
  and and_1 (and_1_out, n2_to_4_decoder_lvc139_1_p5[0], not_1_out);
  and and_2 (and_2_out, n2_to_4_decoder_lvc139_1_p5[1], not_1_out);
  and and_3 (and_3_out, n2_to_4_decoder_lvc139_1_p5[2], not_1_out);
  RAM #(.databus("bidir"), .enables("line"), .trigger("high"), .addrWidth(15), .\type ("nonvolatile")) ram_1 (
    .addr({n16_bit_line_driver_lvc16244_1_p9[2:0], n16_bit_line_driver_lvc16244_1_p10, n16_bit_line_driver_lvc16244_1_p11, n16_bit_line_driver_lvc16244_1_p12}),
    .data(ram_1_data));  // open: we, oe, clk
  SRAM_Chipifier sram_chipifier_1 (
    .WEB(n4_bit_multiplexer_lvc257_1_p5[1]), .OEB(n4_bit_multiplexer_lvc257_1_p5[0]), .CEB(and_1_out));  // open: OE, E, WE
  RAM #(.databus("bidir"), .\type ("nonvolatile"), .addrWidth(15), .enables("line"), .trigger("high")) ram_2 (
    .addr({n16_bit_line_driver_lvc16244_1_p9[2:0], n16_bit_line_driver_lvc16244_1_p10, n16_bit_line_driver_lvc16244_1_p11, n16_bit_line_driver_lvc16244_1_p12}),
    .data(ram_2_data));  // open: we, oe, clk
  SRAM_Chipifier sram_chipifier_2 (
    .WEB(n4_bit_multiplexer_lvc257_1_p5[1]), .OEB(n4_bit_multiplexer_lvc257_1_p5[0]), .CEB(and_2_out));  // open: OE, E, WE
  RAM #(.databus("bidir"), .trigger("high"), .\type ("nonvolatile"), .enables("line"), .addrWidth(15)) ram_3 (
    .addr({n16_bit_line_driver_lvc16244_1_p9[2:0], n16_bit_line_driver_lvc16244_1_p10, n16_bit_line_driver_lvc16244_1_p11, n16_bit_line_driver_lvc16244_1_p12}),
    .data(ram_3_data));  // open: we, oe, clk
  SRAM_Chipifier sram_chipifier_3 (
    .WEB(n4_bit_multiplexer_lvc257_1_p5[1]), .OEB(n4_bit_multiplexer_lvc257_1_p5[0]), .CEB(and_3_out));  // open: OE, E, WE
  Pull_Resistor #(.pull(1)) pull_resistor_9 ();  // open: node
  // _8_bit_Bus_Transceiver__LVC4245 8_bit_bus_transceiver_lvc4245_1: pin names not known; wires that end beside it: n2_to_4_decoder_lvc139_1_p5[0], ram_1_data, OEB, n8_bit_bus_transceiver_lvc4245_1_p4
  // _8_bit_Bus_Transceiver__LVC4245 8_bit_bus_transceiver_lvc4245_2: pin names not known; wires that end beside it: n2_to_4_decoder_lvc139_1_p5[1], ram_2_data, OEB, n8_bit_bus_transceiver_lvc4245_1_p4
  // _8_bit_Bus_Transceiver__LVC4245 8_bit_bus_transceiver_lvc4245_3: pin names not known; wires that end beside it: n2_to_4_decoder_lvc139_1_p5[2], ram_3_data, OEB, n8_bit_bus_transceiver_lvc4245_1_p4
  // _8_bit_Bus_Transceiver__LVC4245 8_bit_bus_transceiver_lvc4245_4: pin names not known; wires that end beside it: n2_to_4_decoder_lvc139_1_p5[3], OEB, n8_bit_bus_transceiver_lvc4245_1_p4
  // Probe on n8_bit_bus_transceiver_lvc4245_1_p4
  // _16_bit_Latch__LVC16373 16_bit_latch_lvc16373_1: pin names not known; wires that end beside it: RGB_OEB, RGB_OEB, ram_1_data, RGB_LE, ram_2_data, RGB_LE, RED, GREEN
  // _8_bit_Latch__LVC573 8_bit_latch_lvc573_1: pin names not known; wires that end beside it: RGB_OEB, ram_3_data, RGB_LE, BLUE
  assign D_OUT = bidirectional_monsters_1_write ? n8_bit_bus_transceiver_lvc4245_1_p4 : 8'bz;  // Controlled_Buffer controlled_buffer_1
  assign n8_bit_bus_transceiver_lvc4245_1_p4 = bidirectional_monsters_1_read ? D_IN : 8'bz;  // Controlled_Buffer controlled_buffer_2
  Bidirectional_Monsters bidirectional_monsters_1 (
    .WRITE(bidirectional_monsters_1_write), .READ(bidirectional_monsters_1_read), .RWB(OEB),
    .ENABLE_B(MPU_VALID_B));
endmodule

module ADV7125 (
  input  [7:0] RED_D0_7,
  input  [7:0] GREEN_D0_7,
  input  [7:0] BLUE_D0_7,
  input  CLOCK,
  input  BLANK_B,
  input  SYNC_B,
  output IOR,
  output IOG,
  output IOB,
  output IOR_B,
  output IOG_B,
  output IOB_B
);

  wire comparator_1_gt, comparator_2_gt, comparator_3_gt, not_1_out;

  Comparator comparator_1 (.a(RED_D0_7), .b(8'h80), .gt(comparator_1_gt));  // open: eq, lt
  Comparator comparator_2 (.a(GREEN_D0_7), .b(8'h80), .gt(comparator_2_gt));  // open: eq, lt
  Comparator comparator_3 (.a(BLUE_D0_7), .b(8'h80), .gt(comparator_3_gt));  // open: eq, lt
  not not_1 (not_1_out, BLANK_B);
  and and_1 (IOR, comparator_1_gt, not_1_out);
  and and_2 (IOG, comparator_2_gt, not_1_out);
  and and_3 (IOB, comparator_3_gt, not_1_out);
  not not_2 (IOR_B, IOR);
  not not_3 (IOG_B, IOG);
  not not_4 (IOB_B, IOB);
endmodule

module Timing_Circuit (
  input  RESET,
  input  CLOCK_IN,
  output [7:0] SELECTOR_B,
  output RESET_0_B,
  output RESET_1_B,
  output SLOW_SELECTOR,
  output CLK,
  output CLK_B,
  output HCLK,
  output HCLK_B,
  output [3:0] MULTIPLEXER,
  output [3:0] COUNTER
);

  wire clock_1_out, clock_2_out, not_1_out, not_2_out, not_3_out, not_4_out, pull_resistor_1_node,
       pull_resistor_2_node, pull_resistor_3_node, pull_resistor_4_node, pull_resistor_5_node,
       pull_resistor_6_node, pull_resistor_8_node, pull_resistor_9_node, RSTB;
  wire [3:0] pull_resistor_7_node;
  wire [7:2] n8_bit_serial_in_shift_lvc595_1_p6;
  wire [7:4] n8_bit_latch_lvc574_1_p4, n8_bit_latch_lvc574_2_p4;

  not not_1 (not_1_out, RESET);
  Clock clock_1 (.out(clock_1_out));
  Clock clock_2 (.out(clock_2_out));
  // Digital_Oscilloscope #(.nState(32)) digital_oscilloscope_1: pin names not known; wires that end beside it: clock_2_out, SELECTOR_B[0], SELECTOR_B[1], SELECTOR_B[2], SELECTOR_B[3], SELECTOR_B[4], SELECTOR_B[5], SELECTOR_B[6], SELECTOR_B[7], RESET_0_B, RESET_1_B
  // EconoReset__DS1813 econoreset_ds1813_1: pin names not known; wires that end beside it: not_1_out, clock_1_out, RSTB
  Pull_Resistor pull_resistor_1 (.node(pull_resistor_1_node));
  D_Flip_Flop d_ff_1 (.clk(CLOCK_IN), .D(CLK_B), .Q(CLK), .Qn(CLK_B), .reset(not_2_out));  // open: preset
  not not_2 (not_2_out, RSTB);
  D_Flip_Flop d_ff_2 (.clk(CLK_B), .D(HCLK_B), .Q(HCLK), .Qn(HCLK_B), .reset(not_3_out));  // open: preset
  not not_3 (not_3_out, RSTB);
  // _8_bit_serial_in_shift__LVC595 8_bit_serial_in_shift_lvc595_1: pin names not known; wires that end beside it: pull_resistor_1_node, RSTB, RSTB, CLK, CLK, {n8_bit_serial_in_shift_lvc595_1_p6, RESET_1_B, RESET_0_B}
  Pull_Resistor #(.pull(1)) pull_resistor_2 (.node(pull_resistor_2_node));
  Pull_Resistor #(.pull(1)) pull_resistor_3 (.node(pull_resistor_3_node));
  Pull_Resistor #(.pull(1)) pull_resistor_4 (.node(pull_resistor_4_node));
  not not_4 (not_4_out, RESET_1_B);
  // _4_bit_Up_Counter__LVC163 4_bit_up_counter_lvc163_1: pin names not known; wires that end beside it: RESET_1_B, pull_resistor_2_node, pull_resistor_3_node, CLK, pull_resistor_4_node, RESET_1_B, COUNTER, SLOW_SELECTOR
  Pull_Resistor #(.pull(1)) pull_resistor_5 (.node(pull_resistor_5_node));
  Pull_Resistor #(.pull(1)) pull_resistor_6 (.node(pull_resistor_6_node));
  // _2_to_4_Decoder__LVC139 2_to_4_decoder_lvc139_1: pin names not known; wires that end beside it: pull_resistor_5_node, not_4_out, pull_resistor_6_node, COUNTER[1:0], MULTIPLEXER
  Pull_Resistor #(.pull(1)) pull_resistor_7 (.node(pull_resistor_7_node));
  Pull_Resistor pull_resistor_8 (.node(pull_resistor_8_node));
  Pull_Resistor pull_resistor_9 (.node(pull_resistor_9_node));
  // _8_bit_Latch__LVC574 8_bit_latch_lvc574_1: pin names not known; wires that end beside it: pull_resistor_8_node, {pull_resistor_7_node, MULTIPLEXER}, CLK_B, {n8_bit_latch_lvc574_1_p4, SELECTOR_B[6], SELECTOR_B[4], SELECTOR_B[2], SELECTOR_B[0]}
  // _8_bit_Latch__LVC574 8_bit_latch_lvc574_2: pin names not known; wires that end beside it: pull_resistor_9_node, {n8_bit_latch_lvc574_1_p4, SELECTOR_B[6], SELECTOR_B[4], SELECTOR_B[2], SELECTOR_B[0]}, CLK, {n8_bit_latch_lvc574_2_p4, SELECTOR_B[7], SELECTOR_B[5], SELECTOR_B[3], SELECTOR_B[1]}

  // Other names for the same wires on the sheet: RESET_0 = RESET_0_B; RESET_1 = RESET_1_B; CLOCK_B = CLK_B;
  //   HALF_CLOCK = HCLK; HALF_CLOCK_B = HCLK_B; SEL0 = SELECTOR_B[0]; SEL1 = SELECTOR_B[1]; SEL2 = SELECTOR_B[2];
  //   SEL3 = SELECTOR_B[3]; SEL4 = SELECTOR_B[4]; SEL5 = SELECTOR_B[5]; SEL6 = SELECTOR_B[6]; SEL7 = SELECTOR_B[7]

  // Notes on the sheet:
  //   Debug Outputs
endmodule

module Quick_Timing_Circuit (
  input  RESET,
  input  CLOCK_IN,
  output [7:0] SELECTOR_B,
  output RESET_0_B,
  output RESET_1_B,
  output SLOW_SELECTOR,
  output CLK,
  output CLK_B,
  output HCLK,
  output HCLK_B,
  output [3:0] MULTIPLEXER,
  output [3:0] COUNTER
);

  wire digital_oscilloscope_1_p2, not_1_out, not_3_out, not_4_out, pull_resistor_1_node,
       pull_resistor_2_node, pull_resistor_3_node, pull_resistor_4_node, pull_resistor_5_node,
       pull_resistor_6_node, pull_resistor_7_node, pull_resistor_9_node, RSTB;
  wire [3:0] pull_resistor_8_node;
  wire [7:0] n8_bit_serial_in_shift_lvc595_1_p6;
  wire [7:4] n8_bit_latch_lvc574_1_p4, n8_bit_latch_lvc574_2_p4;

  not not_1 (not_1_out, RESET);
  Clock clock_1 (.out(CLK));
  D_Flip_Flop d_ff_1 (.clk(CLK), .D(not_1_out), .Q(RSTB));  // open: Qn, preset, reset
  // Digital_Oscilloscope #(.nState(32)) digital_oscilloscope_1: pin names not known; wires that end beside it: CLOCK_IN, digital_oscilloscope_1_p2, SELECTOR_B[0], SELECTOR_B[1], SELECTOR_B[2], SELECTOR_B[3], SELECTOR_B[4], SELECTOR_B[5], SELECTOR_B[6], SELECTOR_B[7], RESET_0_B, RESET_1_B
  Clock clock_2 (.out(digital_oscilloscope_1_p2));
  Pull_Resistor pull_resistor_1 (.node(pull_resistor_1_node));
  not not_2 (CLK_B, CLK);
  D_Flip_Flop d_ff_2 (.clk(CLK), .D(HCLK_B), .Q(HCLK), .Qn(HCLK_B), .reset(not_3_out));  // open: preset
  not not_3 (not_3_out, RSTB);
  // _8_bit_serial_in_shift__LVC595 8_bit_serial_in_shift_lvc595_1: pin names not known; wires that end beside it: pull_resistor_1_node, RSTB, RSTB, CLK, CLK, {n8_bit_serial_in_shift_lvc595_1_p6[7:4], RESET_1_B, n8_bit_serial_in_shift_lvc595_1_p6[2], RESET_0_B, n8_bit_serial_in_shift_lvc595_1_p6[0]}
  Pull_Resistor #(.pull(1)) pull_resistor_2 (.node(pull_resistor_2_node));
  Pull_Resistor #(.pull(1)) pull_resistor_3 (.node(pull_resistor_3_node));
  Pull_Resistor #(.pull(1)) pull_resistor_4 (.node(pull_resistor_4_node));
  not not_4 (not_4_out, RESET_1_B);
  // _4_bit_Up_Counter__LVC163 4_bit_up_counter_lvc163_1: pin names not known; wires that end beside it: RESET_1_B, pull_resistor_2_node, pull_resistor_3_node, CLK, pull_resistor_4_node, RESET_1_B, COUNTER, SLOW_SELECTOR
  Pull_Resistor #(.pull(1)) pull_resistor_5 (.node(pull_resistor_5_node));
  Pull_Resistor #(.pull(1)) pull_resistor_6 (.node(pull_resistor_6_node));
  // _2_to_4_Decoder__LVC139 2_to_4_decoder_lvc139_1: pin names not known; wires that end beside it: pull_resistor_5_node, not_4_out, pull_resistor_6_node, COUNTER[1:0], MULTIPLEXER
  Pull_Resistor pull_resistor_7 (.node(pull_resistor_7_node));
  Pull_Resistor #(.pull(1)) pull_resistor_8 (.node(pull_resistor_8_node));
  Pull_Resistor pull_resistor_9 (.node(pull_resistor_9_node));
  // _8_bit_Latch__LVC574 8_bit_latch_lvc574_1: pin names not known; wires that end beside it: pull_resistor_7_node, {pull_resistor_8_node, MULTIPLEXER}, CLK_B, {n8_bit_latch_lvc574_1_p4, SELECTOR_B[6], SELECTOR_B[4], SELECTOR_B[2], SELECTOR_B[0]}
  // _8_bit_Latch__LVC574 8_bit_latch_lvc574_2: pin names not known; wires that end beside it: pull_resistor_9_node, {n8_bit_latch_lvc574_1_p4, SELECTOR_B[6], SELECTOR_B[4], SELECTOR_B[2], SELECTOR_B[0]}, CLK, {n8_bit_latch_lvc574_2_p4, SELECTOR_B[7], SELECTOR_B[5], SELECTOR_B[3], SELECTOR_B[1]}

  // Other names for the same wires on the sheet: RESET_0 = RESET_0_B; RESET_1 = RESET_1_B; CLOCK_B = CLK_B;
  //   HALF_CLOCK = HCLK; HALF_CLOCK_B = HCLK_B; SEL0 = SELECTOR_B[0]; SEL1 = SELECTOR_B[1]; SEL2 = SELECTOR_B[2];
  //   SEL3 = SELECTOR_B[3]; SEL4 = SELECTOR_B[4]; SEL5 = SELECTOR_B[5]; SEL6 = SELECTOR_B[6]; SEL7 = SELECTOR_B[7]

  // Notes on the sheet:
  //   Debug Outputs
endmodule

module Clock_Generator (
  input  [3:0] SELECT_HIGH_SPEED_S0_3,
  input  [3:0] SELECT_LOW_SPEED_S0_3,
  input  CLOCK_IN,
  input  RESET,
  output CLOCK_OUT
);

  wire d_ff_1_qn, d_ff_2_qn, not_1_out, not_2_out, not_3_out, pull_resistor_1_node, pull_resistor_2_node,
       pull_resistor_3_node, pull_resistor_4_node, pull_resistor_7_node;
  wire [3:0] n4_bit_multiplexer_lvc157_1_p5, n4_bit_multiplexer_lvc157_2_p5;
  wire [7:1] d_ff_1_q;
  wire [7:6] pull_resistor_5_node;
  wire [11:0] n12_bit_up_counter_hc4040_2_p3;
  wire [11:1] n12_bit_up_counter_hc4040_1_p3;

  Pull_Resistor pull_resistor_1 (.node(pull_resistor_1_node));
  Pull_Resistor pull_resistor_2 (.node(pull_resistor_2_node));
  Pull_Resistor #(.pull(1)) pull_resistor_3 (.node(pull_resistor_3_node));
  // _4_bit_Multiplexer__LVC157 4_bit_multiplexer_lvc157_1: pin names not known; wires that end beside it: pull_resistor_1_node, pull_resistor_3_node, 4'b0111, SELECT_HIGH_SPEED_S0_3, n4_bit_multiplexer_lvc157_1_p5
  // _4_bit_Multiplexer__LVC157 4_bit_multiplexer_lvc157_2: pin names not known; wires that end beside it: pull_resistor_2_node, pull_resistor_3_node, 4'b0111, SELECT_LOW_SPEED_S0_3, n4_bit_multiplexer_lvc157_2_p5
  not not_1 (not_1_out, RESET);
  D_Flip_Flop d_ff_1 (
    .clk(CLOCK_IN), .D(d_ff_1_qn), .Q(d_ff_1_q[1]), .Qn(d_ff_1_qn), .reset(not_2_out));  // open: preset
  not not_2 (not_2_out, RESET);
  D_Flip_Flop d_ff_2 (
    .clk(d_ff_1_qn), .D(d_ff_2_qn), .Q(d_ff_1_q[2]), .Qn(d_ff_2_qn), .reset(not_3_out));  // open: preset
  not not_3 (not_3_out, RESET);
  // _12_bit_Up_Counter__HC4040 12_bit_up_counter_hc4040_1: pin names not known; wires that end beside it: not_1_out, d_ff_2_qn, {n12_bit_up_counter_hc4040_1_p3[11:8], d_ff_1_q[6], n12_bit_up_counter_hc4040_1_p3[6:5], d_ff_1_q[5], n12_bit_up_counter_hc4040_1_p3[3], d_ff_1_q[4], n12_bit_up_counter_hc4040_1_p3[1], d_ff_1_q[3]}
  // _12_bit_Up_Counter__HC4040 12_bit_up_counter_hc4040_2: pin names not known; wires that end beside it: not_1_out, n12_bit_up_counter_hc4040_1_p3[11], n12_bit_up_counter_hc4040_2_p3
  Pull_Resistor pull_resistor_4 (.node(pull_resistor_4_node));
  Pull_Resistor pull_resistor_5 (.node(pull_resistor_5_node[6]));
  Pull_Resistor #(.pull(1)) pull_resistor_6 (.node(pull_resistor_5_node[7]));
  // _8_to_1_Multiplexer__B3251 8_to_1_multiplexer_b3251_1: pin names not known; wires that end beside it: pull_resistor_4_node, n4_bit_multiplexer_lvc157_2_p5[2:0], {pull_resistor_5_node, n12_bit_up_counter_hc4040_2_p3[11], n12_bit_up_counter_hc4040_2_p3[9], n12_bit_up_counter_hc4040_2_p3[7], n12_bit_up_counter_hc4040_2_p3[4], n12_bit_up_counter_hc4040_2_p3[1], n12_bit_up_counter_hc4040_1_p3[10]}, d_ff_1_q[7]
  Pull_Resistor pull_resistor_7 (.node(pull_resistor_7_node));
  // _8_to_1_Multiplexer__B3251 8_to_1_multiplexer_b3251_2: pin names not known; wires that end beside it: pull_resistor_7_node, n4_bit_multiplexer_lvc157_1_p5[2:0], {d_ff_1_q, CLOCK_IN}, CLOCK_OUT
endmodule

module User_Mode_Memory_Glue (
  input  [7:0] USER_BANK,
  input  [23:0] ADDRESS_IN_A0_23,
  input  INTERNAL_MEMORY_VALID,
  input  READ_ENABLE,
  input  READ_BANK_REMAP_B,
  input  WRITE_ENABLE,
  output [16:0] ADDRESS_OUT_A0_16,
  output OEB,
  output WEB,
  output CEB
);

  wire and_1_out, and_2_out, not_1_out, not_2_out, pull_resistor_1_node;

  Pull_Resistor #(.pull(1)) pull_resistor_1 (.node(pull_resistor_1_node));
  not not_1 (not_1_out, READ_BANK_REMAP_B);
  and and_1 (and_1_out, INTERNAL_MEMORY_VALID, READ_ENABLE);
  and and_2 (and_2_out, INTERNAL_MEMORY_VALID, WRITE_ENABLE);
  // _4_bit_Line_Driver__LVC125 4_bit_line_driver_lvc125_1: pin names not known; wires that end beside it: READ_BANK_REMAP_B, not_1_out, pull_resistor_1_node, pull_resistor_1_node, 1'b1, ADDRESS_IN_A0_23[16], ADDRESS_OUT_A0_16[16], ADDRESS_OUT_A0_16[16]
  // _16_bit_Line_Driver__LVC16244 16_bit_line_driver_lvc16244_1: pin names not known; wires that end beside it: READ_BANK_REMAP_B, READ_BANK_REMAP_B, READ_BANK_REMAP_B, READ_BANK_REMAP_B, USER_BANK[7:4], USER_BANK[3:0], ADDRESS_IN_A0_23[23:20], ADDRESS_IN_A0_23[19:16], ADDRESS_OUT_A0_16[15:12], ADDRESS_OUT_A0_16[11:8], ADDRESS_OUT_A0_16[7:4], ADDRESS_OUT_A0_16[3:0]
  // _16_bit_Line_Driver__LVC16244 16_bit_line_driver_lvc16244_2: pin names not known; wires that end beside it: not_1_out, not_1_out, not_1_out, not_1_out, ADDRESS_IN_A0_23[15:12], ADDRESS_IN_A0_23[11:8], ADDRESS_IN_A0_23[7:4], ADDRESS_IN_A0_23[3:0], ADDRESS_OUT_A0_16[15:12], ADDRESS_OUT_A0_16[11:8], ADDRESS_OUT_A0_16[7:4], ADDRESS_OUT_A0_16[3:0]
  not not_2 (not_2_out, READ_BANK_REMAP_B);
  nor nor_1 (OEB, and_1_out, not_2_out);
  nand nand_1 (WEB, READ_BANK_REMAP_B, and_2_out);
  Pull_Resistor pull_resistor_2 (.node(CEB));
endmodule

module Address_Decode (
  input  MPU_LOCK_IN,
  input  [23:0] ADDRESS_IN_A0_24,
  input  KERNAL_ROM_B,
  input  RWB,
  input  KERNAL_MODE,
  input  KERNAL_MODE_B,
  output INTERNAL_MEMORY_VALID,
  output SPECIAL_VALID_B,
  output DEVICE_VALID_B,
  output ROM_VALID,
  output MAIN_MEMORY_VALID_B,
  output [1:0] DEVICE_CHANNEL,
  output [5:0] DEVICE_IDENTIFIER,
  output [3:0] DEVICE_ADDRESS,
  output [15:0] SPECIAL_MEMORY_SELECTOR_B
);

  wire and_1_out, and_2_out, and_3_out, and_4_out, and_5_out, and_6_out, and_7_out, and_8_out, and_9_out,
       and_11_out, n8_bit_comparator_f521_1_p4, nand_1_out, nand_2_out, nand_3_out, nor_1_out, not_1_out,
       not_2_out, not_3_out, not_4_out, not_5_out, not_6_out, not_7_out, not_8_out, not_9_out, not_10_out,
       not_11_out, not_12_out, not_13_out, not_14_out, not_15_out, or_1_out, or_2_out, pull_resistor_1_node,
       pull_resistor_2_node;

  Pull_Resistor pull_resistor_1 (.node(pull_resistor_1_node));
  not not_1 (not_1_out, ADDRESS_IN_A0_24[16]);
  not not_2 (not_2_out, ADDRESS_IN_A0_24[17]);
  not not_3 (not_3_out, ADDRESS_IN_A0_24[18]);
  not not_4 (not_4_out, ADDRESS_IN_A0_24[19]);
  not not_5 (not_5_out, ADDRESS_IN_A0_24[20]);
  not not_6 (not_6_out, ADDRESS_IN_A0_24[21]);
  not not_7 (not_7_out, ADDRESS_IN_A0_24[22]);
  not not_8 (not_8_out, ADDRESS_IN_A0_24[23]);
  Pull_Resistor #(.pull(1)) pull_resistor_2 (.node(pull_resistor_2_node));
  not not_9 (not_9_out, KERNAL_ROM_B);
  not not_10 (not_10_out, ADDRESS_IN_A0_24[15]);
  // Probe on ADDRESS_IN_A0_24[7:0]
  // _8_bit_Comparator__F521 8_bit_comparator_f521_1: pin names not known; wires that end beside it: pull_resistor_1_node, ADDRESS_IN_A0_24[15:8], 8'h6f, n8_bit_comparator_f521_1_p4
  not not_11 (not_11_out, ADDRESS_IN_A0_24[3]);
  not not_12 (not_12_out, MPU_LOCK_IN);
  and and_1 (and_1_out, not_1_out, not_2_out, not_3_out, not_4_out);
  and and_2 (and_2_out, not_5_out, not_6_out, not_7_out, not_8_out);
  and and_3 (and_3_out, not_4_out, not_3_out, not_2_out, pull_resistor_2_node);
  and and_4 (and_4_out, ADDRESS_IN_A0_24[12], ADDRESS_IN_A0_24[13], ADDRESS_IN_A0_24[14], not_10_out);
  and and_5 (and_5_out, not_12_out, ADDRESS_IN_A0_24[15], not_9_out, RWB);
  or or_1 (or_1_out, MPU_LOCK_IN, KERNAL_MODE);
  and and_6 (and_6_out, not_12_out, KERNAL_MODE_B);
  not not_13 (not_13_out, and_2_out);
  not not_14 (not_14_out, and_1_out);
  and and_7 (and_7_out, and_2_out, and_1_out);
  and and_8 (and_8_out, and_3_out, and_2_out);
  nand nand_1 (nand_1_out, and_3_out, and_2_out);
  not not_15 (not_15_out, and_4_out);
  nand nand_2 (nand_2_out, not_12_out, and_4_out, and_1_out, and_2_out);
  or or_2 (or_2_out, not_13_out, not_14_out, n8_bit_comparator_f521_1_p4);
  and and_9 (and_9_out, and_1_out, and_2_out, KERNAL_MODE);
  and and_10 (ROM_VALID, and_7_out, or_1_out, and_5_out);
  and and_11 (and_11_out, not_15_out, n8_bit_comparator_f521_1_p4);
  or or_3 (DEVICE_VALID_B, and_6_out, nand_2_out);
  or or_4 (SPECIAL_VALID_B, and_6_out, or_2_out);
  nand nand_3 (nand_3_out, and_7_out, and_5_out);
  nor nor_1 (nor_1_out, nand_1_out, and_6_out);
  // Probe on ADDRESS_IN_A0_24[11:0]
  // _3_to_8_Decoder__LVC138 3_to_8_decoder_lvc138_1: pin names not known; wires that end beside it: n8_bit_comparator_f521_1_p4, not_11_out, ADDRESS_IN_A0_24[2:0], and_9_out, SPECIAL_MEMORY_SELECTOR_B[15:8]
  // _3_to_8_Decoder__LVC138 3_to_8_decoder_lvc138_2: pin names not known; wires that end beside it: n8_bit_comparator_f521_1_p4, ADDRESS_IN_A0_24[3], ADDRESS_IN_A0_24[2:0], and_9_out, SPECIAL_MEMORY_SELECTOR_B[7:0]
  and and_12 (INTERNAL_MEMORY_VALID, and_8_out, or_1_out, nand_3_out, and_11_out);
  or or_5 (MAIN_MEMORY_VALID_B, MPU_LOCK_IN, nor_1_out);
  LED led_1 (.in(INTERNAL_MEMORY_VALID));
  LED led_2 (.in(SPECIAL_VALID_B));
  LED led_3 (.in(DEVICE_VALID_B));
  LED led_4 (.in(ROM_VALID));
  LED led_5 (.in(MAIN_MEMORY_VALID_B));

  assign DEVICE_ADDRESS = ADDRESS_IN_A0_24[3:0];
  assign DEVICE_CHANNEL = ADDRESS_IN_A0_24[11:10];
  assign DEVICE_IDENTIFIER = ADDRESS_IN_A0_24[9:4];

  // Notes on the sheet:
  //   Bank Decode
  //   ROM Decode
  //   Device Decode (7000 to 7FFF)
  //   Address A12..15 == $F
  //   Special Memory Decode (6F00 to 6F0F)
  //   bits 0..3 all zero
  //   bits 4..7 all zero
  //   bits 1..3 all zero
  //   bank zero
  //   bank zero or one
  //   !(bank zero or one)
  //   !(bank zero && device address)
  //   !(kernal mode) || !(bank zero or one)
  //   CCLL LLLL AAAA
endmodule

module Interrupt_Vectoring (
  input  [7:0] ADDRESS_IN_A0_7,
  input  VPB,
  input  IRQ_0_B,
  input  IRQ_1_B,
  input  IRQ_2_B,
  input  IRQ_3_B,
  input  IRQ_4_B,
  input  IRQ_5_B,
  input  IRQ_6_B,
  input  IRQ_7_B,
  input  IRQ_8_B,
  input  NMI_0_B,
  input  NMI_1_B,
  input  NMI_2_B,
  input  NMI_3_B,
  output [7:0] ADDRESS_OUT_A0_7,
  output IRQ_B,
  output NMI_B
);

  wire nand_1_out, nand_2_out, not_1_out, not_2_out, not_3_out, not_4_out, not_5_out, not_6_out;
  wire [0:0] n8_bit_latch_lvc573_1_p4, n8_bit_latch_lvc573_2_p4, n8_bit_line_driver_lvc541_1_p4;
  wire [1:0] and_1_out;
  wire [3:0] n10_to_4_encoder_hc147_1_p2;

  not not_1 (not_1_out, VPB);
  nand nand_1 (nand_1_out, ADDRESS_IN_A0_7[1], ADDRESS_IN_A0_7[2], ADDRESS_IN_A0_7[3], not_1_out);
  not not_2 (not_2_out, ADDRESS_IN_A0_7[2]);
  nand nand_2 (nand_2_out, ADDRESS_IN_A0_7[1], not_2_out, ADDRESS_IN_A0_7[3], not_1_out);
  not not_3 (not_3_out, nand_1_out);
  and and_1 (and_1_out[0], NMI_0_B, NMI_2_B);
  and and_2 (and_1_out[1], NMI_0_B, NMI_1_B);
  and and_3 (NMI_B, NMI_0_B, NMI_1_B, NMI_2_B, NMI_3_B);
  not not_4 (not_4_out, nand_2_out);
  // Probe on and_1_out
  // _10_to_4_Encoder__HC147 10_to_4_encoder_hc147_1: pin names not known; wires that end beside it: {IRQ_8_B, IRQ_7_B, IRQ_6_B, IRQ_5_B, IRQ_4_B, IRQ_3_B, IRQ_2_B, IRQ_1_B, IRQ_0_B}, n10_to_4_encoder_hc147_1_p2
  not not_5 (not_5_out, NMI_B);
  and and_4 (IRQ_B, n10_to_4_encoder_hc147_1_p2[0], n10_to_4_encoder_hc147_1_p2[1], n10_to_4_encoder_hc147_1_p2[2], n10_to_4_encoder_hc147_1_p2[3]);
  // Probe on {3'b110, n10_to_4_encoder_hc147_1_p2, 1'b0}
  // Probe on {5'b11000, and_1_out, 1'b0}
  not not_6 (not_6_out, IRQ_B);
  // _8_bit_Line_Driver__LVC541 8_bit_line_driver_lvc541_1: pin names not known; wires that end beside it: not_3_out, not_4_out, ADDRESS_IN_A0_7, {ADDRESS_OUT_A0_7[7:1], n8_bit_line_driver_lvc541_1_p4[0]}
  // _8_bit_Latch__LVC573 8_bit_latch_lvc573_1: pin names not known; wires that end beside it: nand_1_out, {3'b110, n10_to_4_encoder_hc147_1_p2, 1'b0}, not_6_out, {ADDRESS_OUT_A0_7[7:1], n8_bit_latch_lvc573_1_p4[0]}
  // _8_bit_Latch__LVC573 8_bit_latch_lvc573_2: pin names not known; wires that end beside it: nand_2_out, {5'b11000, and_1_out, 1'b0}, not_5_out, {ADDRESS_OUT_A0_7[7:1], n8_bit_latch_lvc573_2_p4[0]}

  assign ADDRESS_OUT_A0_7[0] = ADDRESS_IN_A0_7[0];

  // Notes on the sheet:
  //   Address A1..3 == %111 && !VPB
  //   ((Address == $XXXE || $XXXF) && VP)
  //   Address A1..3 == %101 && !VPB
  //   ((Address == $XXXA || $XXXB) && VP)
  //   Low byte of address if no interrupt vectoring is taking place
  //   Low byte of IRQ vector with high nybble set to $D and bit 0 set to 0
  //   Low byte of NMI vector with high nybble set to $C and bit 0 set to 0
  //   ($C0, $C2, $C4, $C6)
  //   ($CC, $CE, $D0, $D2, $D4, $D6, $D8, $DA, $DC)
endmodule

module Interrupt_Detection (
  input  NATIVE_MODE,
  input  ADDRESS_IN_A0,
  input  PHI2_B,
  input  OPCODE_ADDRESS,
  input  [7:0] D,
  input  RESET_B,
  input  LATCH_D,
  output ENTER_INTERRUPT,
  output [7:0] OPCODE,
  output RETURN_FROM_INTERRUPT
);

  wire and_1_out, and_2_out, and_3_out, and_4_out, d_ff_1_q, d_ff_2_q, d_ff_2_qn,
       n8_bit_comparator_f521_1_p4, n8_bit_comparator_f521_2_p4, n8_bit_comparator_f521_3_p4, nand_1_out,
       nor_1_out, not_1_out, not_2_out, not_3_out, not_4_out, not_5_out, or_1_out, pull_resistor_2_node,
       pull_resistor_3_node, pull_resistor_4_node, pull_resistor_5_node, xor_1_out;
  wire [7:0] n8_bit_serial_in_shift_lvc595_1_p6;

  not not_1 (not_1_out, RESET_B);
  not not_2 (not_2_out, OPCODE_ADDRESS);
  not not_3 (not_3_out, RESET_B);
  Pull_Resistor pull_resistor_1 ();  // open: node
  and and_1 (and_1_out, OPCODE_ADDRESS, LATCH_D);
  xor xor_1 (xor_1_out, ADDRESS_IN_A0, d_ff_1_q);
  D_Flip_Flop d_ff_1 (.clk(PHI2_B), .D(ADDRESS_IN_A0), .Q(d_ff_1_q), .reset(not_1_out));  // open: Qn, preset
  D_Flip_Flop d_ff_2 (.clk(PHI2_B), .D(not_2_out), .Q(d_ff_2_q), .Qn(d_ff_2_qn), .reset(not_3_out));  // open: preset
  // _8_bit_Latch__LVC573 8_bit_latch_lvc573_1: pin names not known; wires that end beside it: D, and_1_out, OPCODE
  nor nor_1 (nor_1_out, xor_1_out, d_ff_2_q);
  Pull_Resistor pull_resistor_2 (.node(pull_resistor_2_node));
  Pull_Resistor pull_resistor_3 (.node(pull_resistor_3_node));
  Pull_Resistor pull_resistor_4 (.node(pull_resistor_4_node));
  // _8_bit_Comparator__F521 8_bit_comparator_f521_1: pin names not known; wires that end beside it: pull_resistor_2_node, OPCODE, {8{1'b0}}, n8_bit_comparator_f521_1_p4
  // _8_bit_Comparator__F521 8_bit_comparator_f521_2: pin names not known; wires that end beside it: pull_resistor_3_node, OPCODE, 8'h2, n8_bit_comparator_f521_2_p4
  // _8_bit_Comparator__F521 8_bit_comparator_f521_3: pin names not known; wires that end beside it: pull_resistor_4_node, OPCODE, 8'h40, n8_bit_comparator_f521_3_p4
  nand nand_1 (nand_1_out, n8_bit_comparator_f521_1_p4, n8_bit_comparator_f521_2_p4);
  not not_4 (not_4_out, n8_bit_comparator_f521_3_p4);
  and and_2 (and_2_out, xor_1_out, d_ff_2_qn, nand_1_out);
  and and_3 (and_3_out, xor_1_out, d_ff_2_qn, not_4_out);
  or or_1 (or_1_out, nor_1_out, and_2_out);
  Pull_Resistor pull_resistor_5 (.node(pull_resistor_5_node));
  not not_5 (not_5_out, RESET_B);
  // _8_bit_serial_in_shift__LVC595 8_bit_serial_in_shift_lvc595_1: pin names not known; wires that end beside it: pull_resistor_5_node, RESET_B, and_3_out, LATCH_D, LATCH_D, n8_bit_serial_in_shift_lvc595_1_p6
  and and_4 (and_4_out, NATIVE_MODE, LATCH_D, or_1_out);
  and and_5 (RETURN_FROM_INTERRUPT, NATIVE_MODE, LATCH_D, n8_bit_serial_in_shift_lvc595_1_p6[4]);
  or or_2 (ENTER_INTERRUPT, not_5_out, and_4_out);
  // Probe on OPCODE
  // Probe on n8_bit_serial_in_shift_lvc595_1_p6

  // Notes on the sheet:
  //   BRK
  //   COP
  //   RTI
endmodule

module Kernal_User_Mode (
  input  SA_USER_PROGRAM_ID_B,
  input  SA_INTERRUPTS_IN_DEPTH_B,
  input  READ_ENABLE_B,
  input  WRITE_ENABLE_B,
  input  RESET,
  input  [7:0] D_IN,
  input  ENTER_INTERRUPT,
  input  EXIT_INTERRUPT,
  input  READ_BANK_REMAP_B,
  input  [7:0] BA0_7,
  output [7:0] USER,
  output [7:0] D_OUT,
  output USER_MODE_ABILITY,
  output KERNAL_MODE,
  output KERNAL_MODE_B,
  output [7:0] INTERRUPT_DEPTH,
  output [7:0] MAIN_MEMORY_BA0_7
);

  wire n4_bit_up_down_counter_hct193_1_p4, n4_bit_up_down_counter_hct193_1_p5, nor_1_out, not_1_out,
       not_2_out, not_3_out, not_4_out, or_1_out, or_2_out, or_3_out, pull_resistor_1_node,
       pull_resistor_2_node;

  not not_1 (not_1_out, READ_BANK_REMAP_B);
  not not_2 (not_2_out, RESET);
  nor nor_1 (nor_1_out, WRITE_ENABLE_B, SA_USER_PROGRAM_ID_B);
  or or_1 (or_1_out, SA_USER_PROGRAM_ID_B, READ_ENABLE_B);
  or or_2 (or_2_out, READ_ENABLE_B, SA_INTERRUPTS_IN_DEPTH_B);
  or or_3 (or_3_out, SA_INTERRUPTS_IN_DEPTH_B, WRITE_ENABLE_B);
  not not_3 (not_3_out, ENTER_INTERRUPT);
  not not_4 (not_4_out, EXIT_INTERRUPT);
  Pull_Resistor pull_resistor_1 (.node(pull_resistor_1_node));
  // _8_bit_Latch__LVC573 8_bit_latch_lvc573_1: pin names not known; wires that end beside it: pull_resistor_1_node, D_IN, nor_1_out, USER
  // _4_bit_Up_Down_Counter__HCT193 4_bit_up_down_counter_hct193_1: pin names not known; wires that end beside it: or_3_out, not_2_out, D_IN[7:4], n4_bit_up_down_counter_hct193_1_p4, n4_bit_up_down_counter_hct193_1_p5, INTERRUPT_DEPTH[7:4]
  // _4_bit_Up_Down_Counter__HCT193 4_bit_up_down_counter_hct193_2: pin names not known; wires that end beside it: or_3_out, not_2_out, D_IN[3:0], not_3_out, not_4_out, INTERRUPT_DEPTH[3:0], n4_bit_up_down_counter_hct193_1_p4, n4_bit_up_down_counter_hct193_1_p5
  // Probe on USER
  Pull_Resistor pull_resistor_2 (.node(pull_resistor_2_node));
  // Probe on INTERRUPT_DEPTH
  // _16_bit_Line_Driver__LVC16244 16_bit_line_driver_lvc16244_1: pin names not known; wires that end beside it: or_1_out, or_1_out, or_2_out, or_2_out, USER[7:4], USER[3:0], INTERRUPT_DEPTH[7:4], INTERRUPT_DEPTH[3:0], D_OUT[7:4], D_OUT[3:0], D_OUT[7:4], D_OUT[3:0]
  // _8_bit_Comparator__F521 8_bit_comparator_f521_1: pin names not known; wires that end beside it: pull_resistor_2_node, {8{1'b0}}, INTERRUPT_DEPTH, KERNAL_MODE
  // Probe on KERNAL_MODE
  not not_5 (KERNAL_MODE_B, KERNAL_MODE);
  // _8_bit_Latch__LVC573 8_bit_latch_lvc573_2: pin names not known; wires that end beside it: KERNAL_MODE, D_IN, not_1_out, MAIN_MEMORY_BA0_7
  // _8_bit_Line_Driver__LVC541 8_bit_line_driver_lvc541_1: pin names not known; wires that end beside it: KERNAL_MODE_B, KERNAL_MODE_B, BA0_7, MAIN_MEMORY_BA0_7
  Pull_Resistor #(.pull(1)) pull_resistor_3 (.node(USER_MODE_ABILITY));

  // Notes on the sheet:
  //   User Program
  //   Interrupt Depth
endmodule

module Flags_Register (
  input  SA_FLAG_REGISTER_B,
  input  READ_ENABLE_B,
  input  RESET,
  input  [7:0] D_IN,
  input  WRITE_ENABLE_B,
  output [7:0] D_OUT,
  output [7:0] FLAG_REGISTER
);

  wire nor_1_out, or_1_out;

  nor nor_1 (nor_1_out, SA_FLAG_REGISTER_B, WRITE_ENABLE_B);
  or or_1 (or_1_out, SA_FLAG_REGISTER_B, READ_ENABLE_B);
  // _8_bit_Latch__LVC273 8_bit_latch_lvc273_1: pin names not known; wires that end beside it: RESET, D_IN, nor_1_out, FLAG_REGISTER
  // _8_bit_Line_Driver__LVC541 8_bit_line_driver_lvc541_1: pin names not known; wires that end beside it: or_1_out, or_1_out, FLAG_REGISTER, D_OUT
endmodule

module Clock_Control (
  input  RWB_B,
  input  ROM_ADDRESS_VALID,
  input  DEVICE_ADDRESS_VALID_B,
  input  UNSTOPPABLE_CLOCK,
  input  RESET,
  output CLOCK_ENABLE_B
);

  wire and_1_out, and_2_out, and_3_out, d_ff_2_q, d_ff_2_qn, d_ff_3_qn, nor_1_out, not_1_out, not_2_out,
       not_3_out, not_4_out, or_1_out, or_2_out;

  not not_1 (not_1_out, ROM_ADDRESS_VALID);
  and and_1 (and_1_out, not_1_out, DEVICE_ADDRESS_VALID_B);
  nor nor_1 (nor_1_out, RWB_B, and_1_out);
  and and_2 (and_2_out, RESET, or_1_out, or_2_out);
  or or_1 (or_1_out, not_1_out, d_ff_2_qn);
  D_Flip_Flop d_ff_1 (
    .clk(UNSTOPPABLE_CLOCK), .D(nor_1_out), .Q(CLOCK_ENABLE_B), .reset(not_2_out));  // open: Qn, preset
  not not_2 (not_2_out, and_2_out);
  or or_2 (or_2_out, DEVICE_ADDRESS_VALID_B, d_ff_3_qn);
  and and_3 (and_3_out, RESET, CLOCK_ENABLE_B);
  D_Flip_Flop d_ff_2 (
    .clk(UNSTOPPABLE_CLOCK), .D(CLOCK_ENABLE_B), .Q(d_ff_2_q), .Qn(d_ff_2_qn), .reset(not_3_out));  // open: preset
  not not_3 (not_3_out, and_3_out);
  D_Flip_Flop d_ff_3 (.clk(UNSTOPPABLE_CLOCK), .D(d_ff_2_q), .Qn(d_ff_3_qn), .reset(not_4_out));  // open: Q, preset
  not not_4 (not_4_out, and_3_out);
endmodule

module Selector_State (
  input  MPU_LOCK_IN,
  input  CLOCK_ENABLE_B,
  input  [7:0] SELECTOR,
  input  RESET,
  output BOARD_RESET,
  output SEL0,
  output SEL1,
  output SEL2,
  output SEL3,
  output BANK_LATCH,
  output DATA_TRANSMIT_B,
  output SEL4,
  output READ_BANK_REMAP_B,
  output SEL5,
  output STOP_SELECTOR_B,
  output DEVICE_STROBE_B,
  output SEL6,
  output WRITE_SELECTOR,
  output SEL7,
  output READ_SELECTOR,
  output PHI2
);

  wire pull_resistor_1_node, pull_resistor_3_node;
  wire [7:0] n8_bit_serial_in_shift_lvc595_1_p6, not_1_out;
  wire [7:1] not_2_out;

  Pull_Resistor pull_resistor_1 (.node(pull_resistor_1_node));
  or or_1 (SEL0, CLOCK_ENABLE_B, SELECTOR[0]);
  or or_2 (SEL1, CLOCK_ENABLE_B, SELECTOR[1]);
  or or_3 (SEL2, CLOCK_ENABLE_B, SELECTOR[2]);
  or or_4 (SEL3, CLOCK_ENABLE_B, SELECTOR[3]);
  or or_5 (SEL4, CLOCK_ENABLE_B, SELECTOR[4]);
  or or_6 (SEL5, CLOCK_ENABLE_B, SELECTOR[5]);
  or or_7 (SEL6, CLOCK_ENABLE_B, SELECTOR[6]);
  or or_8 (SEL7, CLOCK_ENABLE_B, SELECTOR[7]);
  // _8_bit_serial_in_shift__LVC595 8_bit_serial_in_shift_lvc595_1: pin names not known; wires that end beside it: pull_resistor_1_node, RESET, RESET, SELECTOR[3], SELECTOR[3], {n8_bit_serial_in_shift_lvc595_1_p6[7:4], BOARD_RESET, n8_bit_serial_in_shift_lvc595_1_p6[2:0]}
  and and_1 (not_1_out[7], SEL0, n8_bit_serial_in_shift_lvc595_1_p6[0]);
  not not_1 (not_1_out[0], SEL1);
  nand nand_1 (not_1_out[1], SEL1, SEL2);
  nand nand_2 (not_1_out[5], SEL5, SEL6);
  nand nand_3 (not_1_out[6], SEL5, SEL6, SEL7);
  and and_2 (not_2_out[7], SELECTOR[0], SELECTOR[4]);
  not not_2 (not_2_out[1], not_2_out[7]);
  Pull_Resistor #(.pull(1)) pull_resistor_2 (.node(not_2_out[2]));
  Pull_Resistor pull_resistor_3 (.node(pull_resistor_3_node));
  Selecting_8Bit_Data_Multiplexer selecting_8bit_data_multiplexer_1 (
    .OE(pull_resistor_3_node),
    .D_OUT({PHI2, READ_SELECTOR, WRITE_SELECTOR, DEVICE_STROBE_B, STOP_SELECTOR_B, READ_BANK_REMAP_B, DATA_TRANSMIT_B, BANK_LATCH}),
    .S(MPU_LOCK_IN), .DATA_0_D0_7({not_1_out[7:5], SEL4, SELECTOR[3], SEL2, not_1_out[1:0]}),
    .DATA_1_D0_8({{3{not_2_out[7]}}, SELECTOR[4:3], not_2_out[2:1], not_2_out[1]}));

  // Notes on the sheet:
  //   Bank Latch
  //   /Data Transmit
  //   /Read Bank Remap
  //   /Stop Selector
  //   /Device Strobe
  //   Write Selector
  //   Read Selector
  //   PHI2
  //   Bank Latch
  //   /Data Transmit
  //   /Read Bank Remap
  //   /Stop Selector
  //   /Device Strobe
  //   Write Selector
  //   Read Selector
  //   PHI2
endmodule

module Signals (
  input  [7:0] D,
  input  RWB,
  input  VDA,
  input  VPA,
  input  E,
  input  READ_SELECTOR,
  input  WRITE_SELECTOR,
  input  CLOCK_ENABLE_B,
  input  BANK_LATCH,
  output [7:0] BA0_7,
  output NATIVE_MODE,
  output RWB_B,
  output WRITE_ENABLE,
  output WRITE_ENABLE_B,
  output READ_ENABLE,
  output READ_ENABLE_B,
  output OPCODE_ADDRESS
);

  wire or_1_out, or_2_out, pull_resistor_1_node;

  // Probe on D
  not not_1 (RWB_B, RWB);
  Pull_Resistor pull_resistor_1 (.node(pull_resistor_1_node));
  and and_1 (OPCODE_ADDRESS, VDA, VPA);
  or or_1 (or_1_out, VDA, VPA);
  // _8_bit_Latch__LVC573 8_bit_latch_lvc573_1: pin names not known; wires that end beside it: pull_resistor_1_node, D, BANK_LATCH, BA0_7
  not not_2 (NATIVE_MODE, E);
  and and_2 (WRITE_ENABLE, WRITE_SELECTOR, RWB_B, or_1_out);
  and and_3 (READ_ENABLE, RWB, or_1_out, or_2_out);
  or or_2 (or_2_out, READ_SELECTOR, CLOCK_ENABLE_B);
  not not_3 (WRITE_ENABLE_B, WRITE_ENABLE);
  not not_4 (READ_ENABLE_B, READ_ENABLE);
endmodule

module Device_Strobe (
  input  SELECTOR_0_B,
  input  DEVICE_0_VALID_B,
  input  [1:0] CHANNEL_0_NUMBER,
  input  SELECTOR_1_B,
  input  DEVICE_1_VALID_B,
  input  [1:0] CHANNEL_1_NUMBER,
  input  RESET,
  output Channel_0_B,
  output Channel_1_B,
  output Channel_2_B,
  output Channel_3_B
);

  wire and_1_out, and_2_out, d_ff_1_q, d_ff_2_q, not_1_out, not_2_out, or_1_out, or_2_out;
  wire [3:0] n2_to_4_decoder_lvc139_1_p5, n2_to_4_decoder_lvc139_1_p6;

  D_Flip_Flop d_ff_1 (.clk(SELECTOR_0_B), .D(DEVICE_0_VALID_B), .Q(d_ff_1_q), .reset(not_1_out));  // open: Qn, preset
  not not_1 (not_1_out, RESET);
  D_Flip_Flop d_ff_2 (.clk(SELECTOR_1_B), .D(DEVICE_1_VALID_B), .Q(d_ff_2_q), .reset(not_2_out));  // open: Qn, preset
  not not_2 (not_2_out, RESET);
  and and_1 (and_1_out, DEVICE_0_VALID_B, d_ff_1_q);
  and and_2 (and_2_out, DEVICE_1_VALID_B, d_ff_2_q);
  or or_1 (or_1_out, SELECTOR_0_B, and_1_out);
  or or_2 (or_2_out, SELECTOR_1_B, and_2_out);
  // _2_to_4_Decoder__LVC139 2_to_4_decoder_lvc139_1: pin names not known; wires that end beside it: or_1_out, or_2_out, CHANNEL_0_NUMBER, CHANNEL_1_NUMBER, n2_to_4_decoder_lvc139_1_p5, n2_to_4_decoder_lvc139_1_p6
  // _4_bit_Line_Driver__LVC125 4_bit_line_driver_lvc125_1: pin names not known; wires that end beside it: SELECTOR_0_B, SELECTOR_0_B, SELECTOR_0_B, SELECTOR_0_B, n2_to_4_decoder_lvc139_1_p5[0], n2_to_4_decoder_lvc139_1_p5[1], n2_to_4_decoder_lvc139_1_p5[2], n2_to_4_decoder_lvc139_1_p5[3], Channel_0_B, Channel_1_B, Channel_2_B, Channel_3_B
  // _4_bit_Line_Driver__LVC125 4_bit_line_driver_lvc125_2: pin names not known; wires that end beside it: SELECTOR_1_B, SELECTOR_1_B, SELECTOR_1_B, SELECTOR_1_B, n2_to_4_decoder_lvc139_1_p6[0], n2_to_4_decoder_lvc139_1_p6[1], n2_to_4_decoder_lvc139_1_p6[2], n2_to_4_decoder_lvc139_1_p6[3], Channel_0_B, Channel_1_B, Channel_2_B, Channel_3_B
endmodule

module Device_Channel_Gateway (
  input  [7:0] CHANNEL_D_IN,
  input  [7:0] MPU_D_IN,
  input  FST,
  input  SELECTOR_B,
  input  MPU_RWB,
  input  MPU_DEVICE_VALID_B,
  input  [5:0] MPU_DEVICE_IDENTIFIER,
  input  [3:0] MPU_DEVICE_ADDRESS,
  output [7:0] MPU_D_OUT,
  output [7:0] CHANNEL_D_OUT,
  output [5:0] CHANNEL_DEVICE_IDENTIFIER,
  output [3:0] CHANNEL_DEVICE_ADDRESS,
  output CHANNEL_RWB_B,
  output CHANNEL_RWB
);

  wire bidirectional_monsters_1_read, bidirectional_monsters_1_write, bidirectional_monsters_2_read,
       bidirectional_monsters_2_write, nor_1_out, or_1_out, or_2_out, or_3_out, pull_resistor_2_node,
       pull_resistor_6_node, pull_resistor_8_node, pull_resistor_9_node;
  wire [1:0] n8_bit_bi_latch_lvc543_1_p8, pull_resistor_1_node;
  wire [3:0] n16_bit_latch_lvc16373_1_p7, n16_bit_latch_lvc16373_1_p7_2;
  wire [3:1] pull_resistor_3_node;
  wire [3:2] n4_bit_multiplexer_lvc157_1_p4;
  wire [7:0] controlled_buffer_2_out, n8_bit_bi_latch_lvc543_1_p5;

  assign MPU_D_OUT = bidirectional_monsters_1_read ? controlled_buffer_2_out : 8'bz;  // Controlled_Buffer controlled_buffer_1
  assign controlled_buffer_2_out = bidirectional_monsters_1_write ? MPU_D_IN : 8'bz;  // Controlled_Buffer controlled_buffer_2
  Bidirectional_Monsters bidirectional_monsters_1 (
    .WRITE(bidirectional_monsters_1_write), .READ(bidirectional_monsters_1_read), .RWB(MPU_RWB),
    .ENABLE_B(or_1_out));
  or or_1 (or_1_out, SELECTOR_B, MPU_DEVICE_VALID_B);
  not not_1 (pull_resistor_3_node[3], MPU_RWB);
  // Probe on controlled_buffer_2_out
  Pull_Resistor #(.pull(1)) pull_resistor_1 (.node(pull_resistor_1_node));
  Pull_Resistor pull_resistor_2 (.node(pull_resistor_2_node));
  Pull_Resistor #(.pull(1)) pull_resistor_3 (.node(pull_resistor_3_node[1]));
  or or_2 (or_2_out, SELECTOR_B, pull_resistor_3_node[3]);
  or or_3 (or_3_out, SELECTOR_B, MPU_RWB);
  nor nor_1 (nor_1_out, SELECTOR_B, FST);
  Pull_Resistor pull_resistor_4 ();  // open: node
  // _8_bit_Bi_latch__LVC543 8_bit_bi_latch_lvc543_1: pin names not known; wires that end beside it: FST, or_3_out, CHANNEL_RWB, controlled_buffer_2_out, n8_bit_bi_latch_lvc543_1_p5, CHANNEL_RWB_B, or_2_out, n8_bit_bi_latch_lvc543_1_p8[0]
  // _16_bit_Latch__LVC16373 16_bit_latch_lvc16373_1: pin names not known; wires that end beside it: pull_resistor_2_node, pull_resistor_2_node, {pull_resistor_1_node, MPU_DEVICE_IDENTIFIER}, nor_1_out, {MPU_DEVICE_ADDRESS, pull_resistor_3_node[3], MPU_RWB, pull_resistor_3_node[1], MPU_DEVICE_VALID_B}, nor_1_out, {n16_bit_latch_lvc16373_1_p7_2, n16_bit_latch_lvc16373_1_p7}, {CHANNEL_DEVICE_ADDRESS, CHANNEL_RWB_B, CHANNEL_RWB, n8_bit_bi_latch_lvc543_1_p8}
  // Probe on n8_bit_bi_latch_lvc543_1_p5
  Pull_Resistor pull_resistor_5 ();  // open: node
  Pull_Resistor #(.pull(1)) pull_resistor_6 (.node(pull_resistor_6_node));
  Pull_Resistor pull_resistor_7 ();  // open: node
  Pull_Resistor #(.pull(1)) pull_resistor_8 (.node(pull_resistor_8_node));
  // _4_bit_Multiplexer__LVC157 4_bit_multiplexer_lvc157_1: pin names not known; wires that end beside it: n8_bit_bi_latch_lvc543_1_p8[0], n16_bit_latch_lvc16373_1_p7_2, pull_resistor_6_node, {n4_bit_multiplexer_lvc157_1_p4, CHANNEL_DEVICE_IDENTIFIER[5:4]}
  // _4_bit_Multiplexer__LVC157 4_bit_multiplexer_lvc157_2: pin names not known; wires that end beside it: n8_bit_bi_latch_lvc543_1_p8[0], n16_bit_latch_lvc16373_1_p7, pull_resistor_8_node, CHANNEL_DEVICE_IDENTIFIER[3:0]
  assign n8_bit_bi_latch_lvc543_1_p5 = bidirectional_monsters_2_read ? CHANNEL_D_IN : 8'bz;  // Controlled_Buffer controlled_buffer_3
  Bidirectional_Monsters bidirectional_monsters_2 (
    .WRITE(bidirectional_monsters_2_write), .READ(bidirectional_monsters_2_read), .RWB(CHANNEL_RWB),
    .ENABLE_B(pull_resistor_9_node));
  assign CHANNEL_D_OUT = bidirectional_monsters_2_write ? n8_bit_bi_latch_lvc543_1_p5 : 8'bz;  // Controlled_Buffer controlled_buffer_4
  Pull_Resistor pull_resistor_9 (.node(pull_resistor_9_node));
endmodule

module Device_MPU_Gateway (
  input  [7:0] MPU_D_IN,
  input  [7:0] CHANNEL_D_IN,
  input  MPU_RWB,
  input  SELECTOR_B,
  input  MPU_DEVICE_VALID_B,
  input  [5:0] MPU_0_DEVICE_IDENTIFIER,
  input  [3:0] MPU_0_DEVICE_ADDRESS,
  output [7:0] CHANNEL_D_OUT,
  output [7:0] MPU_D_OUT,
  output CHANNEL_DEVICE_VALID_B,
  output CHANNEL_RWB,
  output [5:0] CHANNEL_DEVICE_IDENTIFIER,
  output [3:0] CHANNEL_DEVICE_ADDRESS
);

  wire bidirectional_monsters_1_read, bidirectional_monsters_1_write, bidirectional_monsters_2_read,
       bidirectional_monsters_2_write, not_1_out, or_1_out, pull_resistor_1_node, pull_resistor_2_node;
  wire [7:0] controlled_buffer_2_out, n8_bit_bi_latch_lvc543_1_p5;

  assign MPU_D_OUT = bidirectional_monsters_1_read ? controlled_buffer_2_out : 8'bz;  // Controlled_Buffer controlled_buffer_1
  assign controlled_buffer_2_out = bidirectional_monsters_1_write ? MPU_D_IN : 8'bz;  // Controlled_Buffer controlled_buffer_2
  Bidirectional_Monsters bidirectional_monsters_1 (
    .WRITE(bidirectional_monsters_1_write), .READ(bidirectional_monsters_1_read), .RWB(MPU_RWB),
    .ENABLE_B(MPU_DEVICE_VALID_B));
  or or_1 (or_1_out, SELECTOR_B, MPU_RWB);
  not not_1 (not_1_out, MPU_RWB);
  // Probe on controlled_buffer_2_out
  Pull_Resistor pull_resistor_1 (.node(pull_resistor_1_node));
  Pull_Resistor pull_resistor_2 (.node(pull_resistor_2_node));
  // _8_bit_Bi_latch__LVC543 8_bit_bi_latch_lvc543_1: pin names not known; wires that end beside it: MPU_RWB, or_1_out, pull_resistor_1_node, controlled_buffer_2_out, n8_bit_bi_latch_lvc543_1_p5, not_1_out, not_1_out, MPU_DEVICE_VALID_B
  // _16_bit_Line_Driver__LVC16244 16_bit_line_driver_lvc16244_1: pin names not known; wires that end beside it: SELECTOR_B, SELECTOR_B, SELECTOR_B, SELECTOR_B, {MPU_0_DEVICE_IDENTIFIER[5:4], MPU_RWB, MPU_DEVICE_VALID_B}, MPU_0_DEVICE_IDENTIFIER[3:0], MPU_0_DEVICE_ADDRESS, pull_resistor_2_node, {CHANNEL_DEVICE_IDENTIFIER[5:4], CHANNEL_RWB, CHANNEL_DEVICE_VALID_B}, CHANNEL_DEVICE_IDENTIFIER[3:0], CHANNEL_DEVICE_ADDRESS
  // Probe on n8_bit_bi_latch_lvc543_1_p5
  assign n8_bit_bi_latch_lvc543_1_p5 = bidirectional_monsters_2_read ? CHANNEL_D_IN : 8'bz;  // Controlled_Buffer controlled_buffer_3
  assign CHANNEL_D_OUT = bidirectional_monsters_2_write ? n8_bit_bi_latch_lvc543_1_p5 : 8'bz;  // Controlled_Buffer controlled_buffer_4
  Bidirectional_Monsters bidirectional_monsters_2 (
    .WRITE(bidirectional_monsters_2_write), .READ(bidirectional_monsters_2_read), .RWB(MPU_RWB),
    .ENABLE_B(SELECTOR_B));

  // Other names for the same wires on the sheet: ENABLE_LEFT_B = MPU_DEVICE_VALID_B; RWB = MPU_RWB;
  //   ENABLE_RIGHT_B = SELECTOR_B
endmodule

module Device_NULL_Gateway (
  input  [1:0] CHANNEL_IN,
  input  SELECTOR_B,
  output [7:0] CHANNEL_D_IN,
  output [1:0] CHANNEL_OUT,
  output CHANNEL_DEVICE_VALID_B,
  output CHANNEL_RWB,
  output [5:0] CHANNEL_DEVICE_IDENTIFIER,
  output [3:0] CHANNEL_DEVICE_ADDRESS
);

  wire pull_resistor_3_node;
  wire [1:0] pull_resistor_2_node;

  Pull_Resistor #(.pull(1)) pull_resistor_1 (.node(pull_resistor_2_node[1]));
  Pull_Resistor #(.pull(1)) pull_resistor_2 (.node(pull_resistor_2_node[0]));
  Pull_Resistor pull_resistor_3 (.node(pull_resistor_3_node));
  // _16_bit_Line_Driver__LVC16244 16_bit_line_driver_lvc16244_1: pin names not known; wires that end beside it: SELECTOR_B, SELECTOR_B, SELECTOR_B, SELECTOR_B, {2'b11, pull_resistor_2_node}, 4'b1111, 4'b1111, pull_resistor_3_node, {CHANNEL_DEVICE_IDENTIFIER[5:4], CHANNEL_RWB, CHANNEL_DEVICE_VALID_B}, CHANNEL_DEVICE_IDENTIFIER[3:0], CHANNEL_DEVICE_ADDRESS

  assign CHANNEL_OUT = CHANNEL_IN;

  // Other names for the same wires on the sheet: NC[7:0] = CHANNEL_D_IN
endmodule

module Microcontroller_Device (
  input  [5:0] CHANNEL_DEVICE_IDENTIFIER,
  input  [3:0] CHANNEL_DEVICE_ADDRESS,
  input  [7:0] D_IN,
  input  [7:0] MPU_ABILITY,
  input  CHANNEL_RWB,
  input  CHANNEL_RWB_B,
  input  RESET,
  input  SLOW_SELECTOR,
  input  [1:0] MPU_CHANNEL_IN,
  output RES_B,
  output IRQ_B,
  output [7:0] D_OUT,
  output NMI_B,
  output [1:0] MPU_CHANNEL_OUT
);

  wire and_1_out, and_2_out, d_ff_1_q, n8_bit_comparator_f521_1_p4, nor_1_out, not_1_out, not_2_out,
       not_3_out, or_1_out, or_2_out, or_3_out, or_4_out, PRESENCE_B, pull_resistor_2_node,
       pull_resistor_3_node, pull_resistor_5_node;
  wire [1:0] pull_resistor_1_node;
  wire [5:0] pull_resistor_4_node;
  wire [7:0] n8_bit_latch_lvc273_1_p4;
  wire [7:1] n3_to_8_decoder_lvc138_1_p5;

  Pull_Resistor pull_resistor_1 (.node(pull_resistor_1_node));
  Pull_Resistor #(.pull(1)) pull_resistor_2 (.node(pull_resistor_2_node));
  Pull_Resistor pull_resistor_3 (.node(pull_resistor_3_node));
  // _8_bit_Comparator__F521 8_bit_comparator_f521_1: pin names not known; wires that end beside it: pull_resistor_3_node, {pull_resistor_1_node, CHANNEL_DEVICE_IDENTIFIER}, 8'h2, n8_bit_comparator_f521_1_p4
  // _3_to_8_Decoder__LVC138 3_to_8_decoder_lvc138_1: pin names not known; wires that end beside it: CHANNEL_DEVICE_ADDRESS[3], CHANNEL_DEVICE_ADDRESS[3], CHANNEL_DEVICE_ADDRESS[2:0], pull_resistor_2_node, {n3_to_8_decoder_lvc138_1_p5, PRESENCE_B}
  Pull_Resistor pull_resistor_4 (.node(pull_resistor_4_node));
  or or_1 (or_1_out, n8_bit_comparator_f521_1_p4, CHANNEL_RWB);
  or or_2 (or_2_out, CHANNEL_RWB_B, n8_bit_comparator_f521_1_p4);
  not not_1 (not_1_out, n3_to_8_decoder_lvc138_1_p5[3]);
  nor nor_1 (nor_1_out, n3_to_8_decoder_lvc138_1_p5[2], or_1_out);
  or or_3 (or_3_out, or_2_out, n3_to_8_decoder_lvc138_1_p5[2]);
  or or_4 (or_4_out, or_2_out, n3_to_8_decoder_lvc138_1_p5[5]);
  and and_1 (and_1_out, not_1_out, or_2_out, D_IN[0]);
  // _8_bit_Line_Driver__LVC541 8_bit_line_driver_lvc541_1: pin names not known; wires that end beside it: or_2_out, n3_to_8_decoder_lvc138_1_p5[4], {pull_resistor_4_node, MPU_CHANNEL_IN}, D_OUT
  // _8_bit_Line_Driver__LVC541 8_bit_line_driver_lvc541_2: pin names not known; wires that end beside it: or_2_out, PRESENCE_B, 8'h8a, D_OUT
  Pull_Resistor #(.pull(1)) pull_resistor_5 (.node(pull_resistor_5_node));
  and and_2 (and_2_out, RESET, NMI_B);
  // _8_bit_Latch__LVC273 8_bit_latch_lvc273_1: pin names not known; wires that end beside it: RESET, D_IN, nor_1_out, n8_bit_latch_lvc273_1_p4
  // _16_bit_Line_Driver__LVC16244 16_bit_line_driver_lvc16244_1: pin names not known; wires that end beside it: or_3_out, or_3_out, or_4_out, or_4_out, n8_bit_latch_lvc273_1_p4[7:4], n8_bit_latch_lvc273_1_p4[3:0], MPU_ABILITY[7:4], MPU_ABILITY[3:0], D_OUT[7:4], D_OUT[3:0], D_OUT[7:4], D_OUT[3:0]
  D_Flip_Flop d_ff_1 (.clk(and_1_out), .D(pull_resistor_5_node), .Q(d_ff_1_q), .reset(not_2_out));  // open: Qn, preset
  not not_2 (not_2_out, and_2_out);
  D_Flip_Flop d_ff_2 (.clk(SLOW_SELECTOR), .D(d_ff_1_q), .Qn(NMI_B), .reset(not_3_out));  // open: Q, preset
  not not_3 (not_3_out, RESET);
  // Probe on n8_bit_latch_lvc273_1_p4
  not not_4 (RES_B, n8_bit_latch_lvc273_1_p4[0]);
  not not_5 (IRQ_B, n8_bit_latch_lvc273_1_p4[1]);

  assign MPU_CHANNEL_OUT = MPU_CHANNEL_IN;
endmodule

module Echo_Device (
  input  [5:0] CHANNEL_DEVICE_IDENTIFIER,
  input  [3:0] CHANNEL_DEVICE_ADDRESS,
  input  [7:0] D_IN,
  input  CHANNEL_RWB,
  output [7:0] D_OUT
);

  wire and_1_out, and_2_out, n8_bit_comparator_f521_1_p4, nand_1_out, not_1_out, not_2_out, not_3_out,
       or_2_out, or_3_out, or_4_out, or_5_out, PRESENCE_B, pull_resistor_2_node, pull_resistor_3_node;
  wire [1:0] pull_resistor_1_node;
  wire [7:0] n3_to_8_decoder_lvc138_1_p5, n8_bit_line_driver_lvc541_1_p4;

  Pull_Resistor pull_resistor_1 (.node(pull_resistor_1_node));
  Pull_Resistor #(.pull(1)) pull_resistor_2 (.node(pull_resistor_2_node));
  not not_1 (not_1_out, CHANNEL_RWB);
  Pull_Resistor pull_resistor_3 (.node(pull_resistor_3_node));
  // _8_bit_Comparator__F521 8_bit_comparator_f521_1: pin names not known; wires that end beside it: pull_resistor_3_node, {pull_resistor_1_node, CHANNEL_DEVICE_IDENTIFIER}, 8'h1, n8_bit_comparator_f521_1_p4
  // _3_to_8_Decoder__LVC138 3_to_8_decoder_lvc138_1: pin names not known; wires that end beside it: CHANNEL_DEVICE_ADDRESS[3], CHANNEL_DEVICE_ADDRESS[3], CHANNEL_DEVICE_ADDRESS[2:0], pull_resistor_2_node, n3_to_8_decoder_lvc138_1_p5
  // _8_bit_Line_Driver__LVC541 8_bit_line_driver_lvc541_1: pin names not known; wires that end beside it: not_1_out, PRESENCE_B, 8'h58, n8_bit_line_driver_lvc541_1_p4
  or or_1 (PRESENCE_B, n8_bit_comparator_f521_1_p4, n3_to_8_decoder_lvc138_1_p5[0]);
  or or_2 (or_2_out, n3_to_8_decoder_lvc138_1_p5[2], n8_bit_comparator_f521_1_p4);
  or or_3 (or_3_out, n3_to_8_decoder_lvc138_1_p5[3], n8_bit_comparator_f521_1_p4);
  not not_2 (not_2_out, or_2_out);
  not not_3 (not_3_out, or_3_out);
  or or_4 (or_4_out, or_2_out, not_1_out);
  and and_1 (and_1_out, not_2_out, not_1_out);
  or or_5 (or_5_out, or_3_out, not_1_out);
  and and_2 (and_2_out, not_3_out, not_1_out);
  // _16_bit_Latch__LVC16373 16_bit_latch_lvc16373_1: pin names not known; wires that end beside it: or_4_out, or_5_out, D_IN, and_1_out, D_IN, and_2_out, n8_bit_line_driver_lvc541_1_p4, n8_bit_line_driver_lvc541_1_p4
  nand nand_1 (nand_1_out, or_5_out, or_4_out);
  assign D_OUT = nand_1_out ? n8_bit_line_driver_lvc541_1_p4 : 8'bz;  // Controlled_Buffer controlled_buffer_1
endmodule

module Graphics_Device (
  input  [5:0] CHANNEL_DEVICE_IDENTIFIER,
  input  [3:0] CHANNEL_DEVICE_ADDRESS,
  input  [7:0] D_IN,
  input  CHANNEL_RWB,
  input  CHANNEL_RWB_B,
  input  [7:0] LINE_WIDTH_REMAINING_IN_W0_7,
  input  DONE_IRQB,
  output EIGHT_BIT,
  output TRANSPARENCY_B,
  output IRQ_ENABLE,
  output [3:0] PIXEL_HIGH_NYBBLE,
  output [11:0] LINE_WIDTH_W0_11,
  output [7:0] TRANSPARENCY_COLOUR,
  output [23:0] SOURCE_ADDRESS,
  output [23:0] DEST_ADDRESS,
  output START_RASTERISING,
  output [7:0] D_OUT,
  output REMAINING_WIDTH_LE,
  output REMAINING_WIDTH_HIGH_OEB,
  output REMAINING_WIDTH_LOW_OEB,
  output CLEAR_IRQ,
  output [3:0] DONE_IRQB_MPU_0_1_2_3
);

  wire n8_bit_comparator_f521_1_p4, nor_1_out, nor_2_out, nor_3_out, nor_4_out, nor_5_out, nor_6_out,
       nor_7_out, nor_8_out, nor_9_out, not_1_out, not_2_out, or_1_out, or_2_out, PRESENCE_B,
       pull_resistor_2_node, pull_resistor_3_node, pull_resistor_4_node, pull_resistor_5_node,
       pull_resistor_6_node, pull_resistor_7_node, pull_resistor_8_node, pull_resistor_9_node,
       pull_resistor_10_node, pull_resistor_11_node, pull_resistor_12_node, pull_resistor_13_node,
       pull_resistor_14_node;
  wire [1:0] pull_resistor_1_node;
  wire [7:0] n3_to_8_decoder_lvc138_2_p5;
  wire [7:1] n3_to_8_decoder_lvc138_1_p5;
  wire [7:2] n16_bit_latch_lvc16373_1_p7;

  Pull_Resistor pull_resistor_1 (.node(pull_resistor_1_node));
  Pull_Resistor #(.pull(1)) pull_resistor_2 (.node(pull_resistor_2_node));
  Pull_Resistor pull_resistor_3 (.node(pull_resistor_3_node));
  Pull_Resistor pull_resistor_4 (.node(pull_resistor_4_node));
  // _8_bit_Comparator__F521 8_bit_comparator_f521_1: pin names not known; wires that end beside it: pull_resistor_4_node, {pull_resistor_1_node, CHANNEL_DEVICE_IDENTIFIER}, 8'h4, n8_bit_comparator_f521_1_p4
  // _3_to_8_Decoder__LVC138 3_to_8_decoder_lvc138_1: pin names not known; wires that end beside it: CHANNEL_DEVICE_ADDRESS[3], CHANNEL_DEVICE_ADDRESS[3], CHANNEL_DEVICE_ADDRESS[2:0], pull_resistor_2_node, {n3_to_8_decoder_lvc138_1_p5, PRESENCE_B}
  // _3_to_8_Decoder__LVC138 3_to_8_decoder_lvc138_2: pin names not known; wires that end beside it: pull_resistor_3_node, pull_resistor_3_node, CHANNEL_DEVICE_ADDRESS[2:0], CHANNEL_DEVICE_ADDRESS[3], {n3_to_8_decoder_lvc138_2_p5[7:6], REMAINING_WIDTH_HIGH_OEB, REMAINING_WIDTH_LOW_OEB, n3_to_8_decoder_lvc138_2_p5[3:0]}
  or or_1 (or_1_out, n8_bit_comparator_f521_1_p4, CHANNEL_RWB);
  or or_2 (or_2_out, CHANNEL_RWB_B, n8_bit_comparator_f521_1_p4);
  Pull_Resistor pull_resistor_5 (.node(pull_resistor_5_node));
  nor nor_1 (nor_1_out, n3_to_8_decoder_lvc138_1_p5[2], or_1_out);
  Pull_Resistor pull_resistor_6 (.node(pull_resistor_6_node));
  nor nor_2 (nor_2_out, or_1_out, n3_to_8_decoder_lvc138_1_p5[3]);
  Pull_Resistor pull_resistor_7 (.node(pull_resistor_7_node));
  nor nor_3 (nor_3_out, n3_to_8_decoder_lvc138_1_p5[4], or_1_out);
  Pull_Resistor pull_resistor_8 (.node(pull_resistor_8_node));
  nor nor_4 (nor_4_out, n3_to_8_decoder_lvc138_1_p5[5], or_1_out);
  Pull_Resistor pull_resistor_9 (.node(pull_resistor_9_node));
  nor nor_5 (nor_5_out, n3_to_8_decoder_lvc138_1_p5[6], or_1_out);
  Pull_Resistor pull_resistor_10 (.node(pull_resistor_10_node));
  nor nor_6 (nor_6_out, n3_to_8_decoder_lvc138_1_p5[7], or_1_out);
  Pull_Resistor pull_resistor_11 (.node(pull_resistor_11_node));
  nor nor_7 (nor_7_out, n3_to_8_decoder_lvc138_2_p5[0], or_1_out);
  Pull_Resistor pull_resistor_12 (.node(pull_resistor_12_node));
  nor nor_8 (nor_8_out, n3_to_8_decoder_lvc138_2_p5[1], or_1_out);
  Pull_Resistor pull_resistor_13 (.node(pull_resistor_13_node));
  nor nor_9 (nor_9_out, n3_to_8_decoder_lvc138_2_p5[2], or_1_out);
  Pull_Resistor pull_resistor_14 (.node(pull_resistor_14_node));
  nor nor_10 (START_RASTERISING, n3_to_8_decoder_lvc138_2_p5[3], or_1_out);
  not not_1 (not_1_out, D_IN[0]);
  nor nor_11 (CLEAR_IRQ, not_1_out, or_1_out, n3_to_8_decoder_lvc138_2_p5[6]);
  // _16_bit_Latch__LVC16373 16_bit_latch_lvc16373_1: pin names not known; wires that end beside it: pull_resistor_5_node, pull_resistor_6_node, D_IN, nor_1_out, D_IN, nor_2_out, {n16_bit_latch_lvc16373_1_p7[7:4], IRQ_ENABLE, n16_bit_latch_lvc16373_1_p7[2], TRANSPARENCY_B, EIGHT_BIT}, {LINE_WIDTH_W0_11[11:8], PIXEL_HIGH_NYBBLE}
  // _16_bit_Latch__LVC16373 16_bit_latch_lvc16373_2: pin names not known; wires that end beside it: pull_resistor_7_node, pull_resistor_8_node, D_IN, nor_3_out, D_IN, nor_4_out, LINE_WIDTH_W0_11[7:0], TRANSPARENCY_COLOUR
  // _16_bit_Latch__LVC16373 16_bit_latch_lvc16373_3: pin names not known; wires that end beside it: pull_resistor_9_node, pull_resistor_10_node, D_IN, nor_5_out, D_IN, nor_6_out, SOURCE_ADDRESS[23:16], DEST_ADDRESS[23:16]
  // _16_bit_Latch__LVC16373 16_bit_latch_lvc16373_4: pin names not known; wires that end beside it: pull_resistor_11_node, pull_resistor_12_node, D_IN, nor_7_out, D_IN, nor_8_out, SOURCE_ADDRESS[7:0], SOURCE_ADDRESS[15:8]
  // _16_bit_Latch__LVC16373 16_bit_latch_lvc16373_5: pin names not known; wires that end beside it: pull_resistor_13_node, pull_resistor_14_node, D_IN, nor_9_out, D_IN, START_RASTERISING, DEST_ADDRESS[7:0], DEST_ADDRESS[15:8]
  // _8_bit_Line_Driver__LVC541 8_bit_line_driver_lvc541_1: pin names not known; wires that end beside it: or_2_out, PRESENCE_B, 8'h94, LINE_WIDTH_REMAINING_IN_W0_7
  not not_2 (not_2_out, DONE_IRQB);
  not not_3 (REMAINING_WIDTH_LE, REMAINING_WIDTH_LOW_OEB);
  nand nand_1 (DONE_IRQB_MPU_0_1_2_3[3], not_2_out, n16_bit_latch_lvc16373_1_p7[7]);
  nand nand_2 (DONE_IRQB_MPU_0_1_2_3[2], not_2_out, n16_bit_latch_lvc16373_1_p7[6]);
  nand nand_3 (DONE_IRQB_MPU_0_1_2_3[1], not_2_out, n16_bit_latch_lvc16373_1_p7[5]);
  nand nand_4 (DONE_IRQB_MPU_0_1_2_3[0], not_2_out, n16_bit_latch_lvc16373_1_p7[4]);

  assign D_OUT = LINE_WIDTH_REMAINING_IN_W0_7;

  // Notes on the sheet:
  //   Flags
  //   Pixel High Nybble (in low nybble) and Width (in high nybble)
  //   Width and Transparency
  //   Souce and Dest Banks
  //   Souce Address
  //   Dest Address
  //   IRQB_MPU_BIT_MASK
  //   If EIGHT_BIT is high then each pixel is 8 bits wide otherwise if EIGHT_BIT is low then each pixel is 4 bits wide.
  //   If IRQB_ENABLE is high then an IRQ is sent to each MPU in the IRQ_MPU_BIT_MASK.
  //   WIDTH_HIGH_NYBBLE and WIDTH_LOW_BYTE together form a 12 bit count of pixels being written to the destination.
  //   If EIGHT_BIT is low then PIXEL_HIGH_NYBBLE is prepended onto the 4 bit pixel value.
  //   If TRANSPARENCY_B is low and the 8 bit pixel value equals TRANSPARENCY_COLOUR then the pixel is not written to the destination.
endmodule

module Video_Device (
  input  [5:0] CHANNEL_DEVICE_IDENTIFIER,
  input  [3:0] CHANNEL_DEVICE_ADDRESS,
  input  [7:0] D_IN,
  input  CHANNEL_RWB,
  input  CHANNEL_RWB_B,
  input  RESET_B,
  input  [7:0] VERTICAL_RASTER_IN_D0_7,
  input  DONE_IRQB,
  output [1:0] PIXEL_DOUBLING_X,
  output FRAME_BUFFER,
  output IRQ_ENABLE,
  output [7:0] PALETTE_INDEX,
  output [7:0] HACTIVE_D4_11,
  output [7:0] H_FRONT_PORCH_D4_11,
  output [7:0] H_SYNC_D4_11,
  output [7:0] H_BACK_PORCH_D4_11,
  output [7:0] D_OUT,
  output [7:0] V_ACTIVE_D4_11,
  output [7:0] V_FRONT_PORCH_D0_7,
  output [7:0] V_SYNC_D0_7,
  output [7:0] V_BACK_PORCH_D0_7,
  output VERTICAL_RASTER_LE,
  output VERTICAL_RASTER_HIGH_OEB,
  output VERTICAL_RASTER_LOW_OEB,
  output CLOCK_OSCILLATOR_SEN,
  output CLOCK_OSCILLATOR_SCK,
  output CLOCK_OSCILLATOR_SDI,
  output CLEAR_IRQ,
  output [3:0] DONE_IRQB_MPU_0_1_2_3
);

  wire clock_1_out, n8_bit_comparator_f521_1_p4, nor_1_out, nor_2_out, nor_3_out, nor_4_out, nor_5_out,
       nor_6_out, nor_7_out, nor_8_out, nor_9_out, nor_10_out, nor_12_out, nor_13_out, not_1_out, not_2_out,
       or_1_out, or_2_out, or_3_out, PRESENCE_B, pull_resistor_2_node, pull_resistor_3_node,
       pull_resistor_4_node, pull_resistor_5_node, pull_resistor_6_node, pull_resistor_7_node,
       pull_resistor_8_node, pull_resistor_9_node, pull_resistor_10_node, pull_resistor_11_node,
       pull_resistor_12_node, pull_resistor_13_node, pull_resistor_14_node, pull_resistor_15_node;
  wire [1:0] pull_resistor_1_node;
  wire [3:0] n8_bit_line_driver_lvc541_1_p3;
  wire [7:0] n3_to_8_decoder_lvc138_2_p5;
  wire [7:1] n3_to_8_decoder_lvc138_1_p5;

  Pull_Resistor pull_resistor_1 (.node(pull_resistor_1_node));
  Clock clock_1 (.out(clock_1_out));
  Pull_Resistor pull_resistor_2 (.node(pull_resistor_2_node));
  Pull_Resistor #(.pull(1)) pull_resistor_3 (.node(pull_resistor_3_node));
  Pull_Resistor pull_resistor_4 (.node(pull_resistor_4_node));
  // _8_bit_Comparator__F521 8_bit_comparator_f521_1: pin names not known; wires that end beside it: pull_resistor_2_node, {pull_resistor_1_node, CHANNEL_DEVICE_IDENTIFIER}, 8'h5, n8_bit_comparator_f521_1_p4
  // _3_to_8_Decoder__LVC138 3_to_8_decoder_lvc138_1: pin names not known; wires that end beside it: CHANNEL_DEVICE_ADDRESS[3], CHANNEL_DEVICE_ADDRESS[3], CHANNEL_DEVICE_ADDRESS[2:0], pull_resistor_3_node, {n3_to_8_decoder_lvc138_1_p5, PRESENCE_B}, n3_to_8_decoder_lvc138_2_p5[7]
  // _3_to_8_Decoder__LVC138 3_to_8_decoder_lvc138_2: pin names not known; wires that end beside it: pull_resistor_4_node, pull_resistor_4_node, CHANNEL_DEVICE_ADDRESS[2:0], CHANNEL_DEVICE_ADDRESS[3], n3_to_8_decoder_lvc138_2_p5
  or or_1 (or_1_out, n8_bit_comparator_f521_1_p4, CHANNEL_RWB);
  or or_2 (or_2_out, CHANNEL_RWB_B, n8_bit_comparator_f521_1_p4);
  Pull_Resistor pull_resistor_5 (.node(pull_resistor_5_node));
  or or_3 (or_3_out, or_2_out, n3_to_8_decoder_lvc138_1_p5[2]);
  Pull_Resistor pull_resistor_6 (.node(pull_resistor_6_node));
  nor nor_1 (nor_1_out, n3_to_8_decoder_lvc138_1_p5[2], or_1_out);
  Pull_Resistor pull_resistor_7 (.node(pull_resistor_7_node));
  nor nor_2 (nor_2_out, or_1_out, n3_to_8_decoder_lvc138_1_p5[3]);
  Pull_Resistor pull_resistor_8 (.node(pull_resistor_8_node));
  nor nor_3 (nor_3_out, or_1_out, n3_to_8_decoder_lvc138_1_p5[4]);
  Pull_Resistor pull_resistor_9 (.node(pull_resistor_9_node));
  nor nor_4 (nor_4_out, or_1_out, n3_to_8_decoder_lvc138_1_p5[5]);
  Pull_Resistor pull_resistor_10 (.node(pull_resistor_10_node));
  nor nor_5 (nor_5_out, or_1_out, n3_to_8_decoder_lvc138_1_p5[7]);
  Pull_Resistor pull_resistor_11 (.node(pull_resistor_11_node));
  nor nor_6 (nor_6_out, or_1_out, n3_to_8_decoder_lvc138_1_p5[6]);
  Pull_Resistor pull_resistor_12 (.node(pull_resistor_12_node));
  nor nor_7 (nor_7_out, or_1_out, n3_to_8_decoder_lvc138_2_p5[3]);
  Pull_Resistor pull_resistor_13 (.node(pull_resistor_13_node));
  nor nor_8 (nor_8_out, or_1_out, n3_to_8_decoder_lvc138_2_p5[2]);
  Pull_Resistor pull_resistor_14 (.node(pull_resistor_14_node));
  nor nor_9 (nor_9_out, or_1_out, n3_to_8_decoder_lvc138_2_p5[1]);
  Pull_Resistor pull_resistor_15 (.node(pull_resistor_15_node));
  nor nor_10 (nor_10_out, or_1_out, n3_to_8_decoder_lvc138_2_p5[0]);
  nor nor_11 (VERTICAL_RASTER_LE, or_2_out, n3_to_8_decoder_lvc138_2_p5[0]);
  or or_4 (VERTICAL_RASTER_HIGH_OEB, or_2_out, n3_to_8_decoder_lvc138_2_p5[1]);
  or or_5 (VERTICAL_RASTER_LOW_OEB, or_2_out, n3_to_8_decoder_lvc138_2_p5[0]);
  nor nor_12 (nor_12_out, or_1_out, n3_to_8_decoder_lvc138_2_p5[5]);
  nor nor_13 (nor_13_out, or_1_out, n3_to_8_decoder_lvc138_2_p5[4]);
  not not_1 (not_1_out, D_IN[0]);
  // _8_bit_Line_Driver__LVC541 8_bit_line_driver_lvc541_1: pin names not known; wires that end beside it: pull_resistor_5_node, or_3_out, {n8_bit_line_driver_lvc541_1_p3, IRQ_ENABLE, FRAME_BUFFER, PIXEL_DOUBLING_X}, VERTICAL_RASTER_IN_D0_7
  // _16_bit_Latch__LVC16373 16_bit_latch_lvc16373_1: pin names not known; wires that end beside it: pull_resistor_6_node, pull_resistor_7_node, D_IN, nor_1_out, D_IN, nor_2_out, {n8_bit_line_driver_lvc541_1_p3, IRQ_ENABLE, FRAME_BUFFER, PIXEL_DOUBLING_X}, PALETTE_INDEX
  // _16_bit_Latch__LVC16373 16_bit_latch_lvc16373_2: pin names not known; wires that end beside it: pull_resistor_8_node, pull_resistor_9_node, D_IN, nor_3_out, D_IN, nor_4_out, HACTIVE_D4_11, H_FRONT_PORCH_D4_11
  // _16_bit_Latch__LVC16373 16_bit_latch_lvc16373_3: pin names not known; wires that end beside it: pull_resistor_10_node, pull_resistor_11_node, D_IN, nor_5_out, D_IN, nor_6_out, H_SYNC_D4_11, H_BACK_PORCH_D4_11
  // _16_bit_Latch__LVC16373 16_bit_latch_lvc16373_4: pin names not known; wires that end beside it: pull_resistor_12_node, pull_resistor_13_node, D_IN, nor_7_out, D_IN, nor_8_out, V_ACTIVE_D4_11, V_FRONT_PORCH_D0_7
  // _16_bit_Latch__LVC16373 16_bit_latch_lvc16373_5: pin names not known; wires that end beside it: pull_resistor_14_node, pull_resistor_15_node, D_IN, nor_9_out, D_IN, nor_10_out, V_SYNC_D0_7, V_BACK_PORCH_D0_7
  // _8_bit_Line_Driver__LVC541 8_bit_line_driver_lvc541_2: pin names not known; wires that end beside it: or_2_out, PRESENCE_B, 8'ha2, VERTICAL_RASTER_IN_D0_7
  nor nor_14 (CLEAR_IRQ, not_1_out, or_1_out, n3_to_8_decoder_lvc138_2_p5[6]);
  Parallel_To_SPI parallel_to_spi_1 (
    .CLOCK_IN(clock_1_out), .D(D_IN), .SCK(CLOCK_OSCILLATOR_SCK), .SEN(CLOCK_OSCILLATOR_SEN),
    .RESET_B(RESET_B), .LOAD_HIGH_B(nor_13_out), .LOAD_LOW_B(nor_12_out), .SDI(CLOCK_OSCILLATOR_SDI));  // open: BEGIN_SHIFT
  not not_2 (not_2_out, DONE_IRQB);
  nand nand_1 (DONE_IRQB_MPU_0_1_2_3[3], not_2_out, n8_bit_line_driver_lvc541_1_p3[3]);
  nand nand_2 (DONE_IRQB_MPU_0_1_2_3[2], not_2_out, n8_bit_line_driver_lvc541_1_p3[2]);
  nand nand_3 (DONE_IRQB_MPU_0_1_2_3[1], not_2_out, n8_bit_line_driver_lvc541_1_p3[1]);
  nand nand_4 (DONE_IRQB_MPU_0_1_2_3[0], not_2_out, n8_bit_line_driver_lvc541_1_p3[0]);

  assign D_OUT = VERTICAL_RASTER_IN_D0_7;

  // Notes on the sheet:
  //   10MHz Clock Oscillator
  //   Horizintal pixel count ÷ 16 (e.g. 640 ÷ 16 = 40)
endmodule

module SNES_Controller_Device (
  input  [5:0] CHANNEL_DEVICE_IDENTIFIER,
  input  [3:0] CHANNEL_DEVICE_ADDRESS,
  input  [7:0] SHIFT_REGISTER_IN,
  input  RESET_B,
  input  LATCH_RESET_B,
  input  [7:0] D_IN,
  input  CHANNEL_RWB,
  input  CHANNEL_RWB_B,
  output DEVICE_SELECTED,
  output [7:0] D_OUT,
  output COUNTER_RESET_B,
  output OE_CONTROLLER_0_LOW_B,
  output OE_CONTROLLER_0_HIGH_B,
  output OE_CONTROLLER_1_LOW_B,
  output OE_CONTROLLER_1_HIGH_B,
  output OE_CONTROLLER_2_LOW_B,
  output OE_CONTROLLER_2_HIGH_B,
  output OE_CONTROLLER_3_LOW_B,
  output OE_CONTROLLER_3_HIGH_B
);

  wire and_1_out, n8_bit_comparator_f521_1_p4, nor_1_out, or_1_out, or_2_out, pull_resistor_1_node,
       pull_resistor_3_node, pull_resistor_4_node;
  wire [1:0] pull_resistor_2_node;
  wire [7:0] n3_to_8_decoder_lvc138_1_p5, n3_to_8_decoder_lvc138_2_p5;
  wire [7:1] n8_bit_latch_lvc273_1_p4;

  Pull_Resistor pull_resistor_1 (.node(pull_resistor_1_node));
  Pull_Resistor pull_resistor_2 (.node(pull_resistor_2_node));
  Pull_Resistor #(.pull(1)) pull_resistor_3 (.node(pull_resistor_3_node));
  Pull_Resistor pull_resistor_4 (.node(pull_resistor_4_node));
  and and_1 (and_1_out, RESET_B, LATCH_RESET_B);
  // _8_bit_Comparator__F521 8_bit_comparator_f521_1: pin names not known; wires that end beside it: pull_resistor_1_node, {pull_resistor_2_node, CHANNEL_DEVICE_IDENTIFIER}, 8'h6, n8_bit_comparator_f521_1_p4
  // _3_to_8_Decoder__LVC138 3_to_8_decoder_lvc138_1: pin names not known; wires that end beside it: CHANNEL_DEVICE_ADDRESS[3], CHANNEL_DEVICE_ADDRESS[3], CHANNEL_DEVICE_ADDRESS[2:0], pull_resistor_3_node, n3_to_8_decoder_lvc138_1_p5
  // _3_to_8_Decoder__LVC138 3_to_8_decoder_lvc138_2: pin names not known; wires that end beside it: pull_resistor_4_node, pull_resistor_4_node, CHANNEL_DEVICE_ADDRESS[2:0], CHANNEL_DEVICE_ADDRESS[3], n3_to_8_decoder_lvc138_2_p5
  or or_1 (or_1_out, n8_bit_comparator_f521_1_p4, CHANNEL_RWB);
  or or_2 (or_2_out, CHANNEL_RWB_B, n8_bit_comparator_f521_1_p4);
  nor nor_1 (nor_1_out, or_1_out, n3_to_8_decoder_lvc138_1_p5[2]);
  or or_3 (OE_CONTROLLER_0_LOW_B, n3_to_8_decoder_lvc138_1_p5[4], or_2_out);
  or or_4 (OE_CONTROLLER_0_HIGH_B, n3_to_8_decoder_lvc138_1_p5[5], or_2_out);
  or or_5 (OE_CONTROLLER_1_LOW_B, n3_to_8_decoder_lvc138_1_p5[6], or_2_out);
  or or_6 (OE_CONTROLLER_1_HIGH_B, n3_to_8_decoder_lvc138_1_p5[7], or_2_out);
  or or_7 (OE_CONTROLLER_2_LOW_B, n3_to_8_decoder_lvc138_2_p5[1], or_2_out);
  or or_8 (OE_CONTROLLER_2_HIGH_B, n3_to_8_decoder_lvc138_2_p5[0], or_2_out);
  or or_9 (OE_CONTROLLER_3_LOW_B, n3_to_8_decoder_lvc138_2_p5[3], or_2_out);
  or or_10 (OE_CONTROLLER_3_HIGH_B, n3_to_8_decoder_lvc138_2_p5[2], or_2_out);
  // _8_bit_Line_Driver__LVC541 8_bit_line_driver_lvc541_1: pin names not known; wires that end beside it: or_2_out, n3_to_8_decoder_lvc138_1_p5[0], 8'hd0, SHIFT_REGISTER_IN
  // _8_bit_Latch__LVC273 8_bit_latch_lvc273_1: pin names not known; wires that end beside it: and_1_out, D_IN, nor_1_out, {n8_bit_latch_lvc273_1_p4, COUNTER_RESET_B}
  // _8_bit_Line_Driver__LVC541 8_bit_line_driver_lvc541_2: pin names not known; wires that end beside it: or_2_out, n3_to_8_decoder_lvc138_1_p5[2], {n8_bit_latch_lvc273_1_p4, COUNTER_RESET_B}, SHIFT_REGISTER_IN
  not not_1 (DEVICE_SELECTED, n8_bit_comparator_f521_1_p4);

  assign D_OUT = SHIFT_REGISTER_IN;
endmodule

module PS2_Input_Device (
  input  [5:0] CHANNEL_DEVICE_IDENTIFIER,
  input  [3:0] CHANNEL_DEVICE_ADDRESS,
  input  CHANNEL_RWB,
  input  CHANNEL_RWB_B,
  input  [7:0] FIFO_IN,
  input  [7:0] D_IN,
  input  RESET_B,
  output DEVICE_SELECTED,
  output OE_LOW_B,
  output OE_HIGH_B,
  output [7:0] D_OUT,
  output RESET_PS2_B
);

  wire d_type_flip_flop_lvc74_1_p9, n8_bit_comparator_f521_1_p4, nor_1_out, or_1_out, or_2_out,
       pull_resistor_1_node, pull_resistor_3_node, pull_resistor_4_node;
  wire [1:0] pull_resistor_2_node;
  wire [7:0] n3_to_8_decoder_lvc138_1_p5;

  Pull_Resistor pull_resistor_1 (.node(pull_resistor_1_node));
  Pull_Resistor pull_resistor_2 (.node(pull_resistor_2_node));
  Pull_Resistor #(.pull(1)) pull_resistor_3 (.node(pull_resistor_3_node));
  // _8_bit_Comparator__F521 8_bit_comparator_f521_1: pin names not known; wires that end beside it: pull_resistor_1_node, {pull_resistor_2_node, CHANNEL_DEVICE_IDENTIFIER}, 8'h7, n8_bit_comparator_f521_1_p4
  // _3_to_8_Decoder__LVC138 3_to_8_decoder_lvc138_1: pin names not known; wires that end beside it: CHANNEL_DEVICE_ADDRESS[3], CHANNEL_DEVICE_ADDRESS[3], CHANNEL_DEVICE_ADDRESS[2:0], pull_resistor_3_node, n3_to_8_decoder_lvc138_1_p5
  or or_1 (or_1_out, n8_bit_comparator_f521_1_p4, CHANNEL_RWB);
  or or_2 (or_2_out, CHANNEL_RWB_B, n8_bit_comparator_f521_1_p4);
  nor nor_1 (nor_1_out, or_1_out, n3_to_8_decoder_lvc138_1_p5[4]);
  or or_3 (OE_LOW_B, n3_to_8_decoder_lvc138_1_p5[2], or_2_out);
  or or_4 (OE_HIGH_B, n3_to_8_decoder_lvc138_1_p5[3], or_2_out);
  Pull_Resistor #(.pull(1)) pull_resistor_4 (.node(pull_resistor_4_node));
  // _8_bit_Line_Driver__LVC541 8_bit_line_driver_lvc541_1: pin names not known; wires that end beside it: or_2_out, n3_to_8_decoder_lvc138_1_p5[0], 8'h62, FIFO_IN
  // D_type_Flip_Flop__LVC74 d_type_flip_flop_lvc74_1: pin names not known; wires that end beside it: RESET_B, pull_resistor_4_node, RESET_B, pull_resistor_4_node, nor_1_out, D_IN[0], nor_1_out, D_IN[1], d_type_flip_flop_lvc74_1_p9
  not not_1 (DEVICE_SELECTED, n8_bit_comparator_f521_1_p4);
  and and_1 (RESET_PS2_B, RESET_B, d_type_flip_flop_lvc74_1_p9);

  assign D_OUT = FIFO_IN;
endmodule

module Main_Memory_Gateway (
  input  [7:0] D_IN_LEFT,
  input  [7:0] D_IN_RIGHT,
  input  GATEWAY_ENABLE_B,
  input  MEMORY_OEB_IN,
  input  MEMORY_WEB_IN,
  input  [23:0] ADDRESS_IN_A0_23,
  output [7:0] D_OUT_LEFT,
  output [7:0] D_OUT_RIGHT,
  output MEMORY_OEB_OUT,
  output MEMORY_WEB_OUT,
  output [23:0] MADDRESS_OUT_A0_23
);

  wire and_1_out, and_2_out, bidirectional_monsters_1_read, bidirectional_monsters_1_write,
       bidirectional_monsters_2_read, bidirectional_monsters_2_write, n8_bit_bi_latch_lvc543_1_p8, or_1_out,
       pull_resistor_3_node, pull_resistor_4_node;
  wire [1:0] n16_bit_line_driver_lvc16244_1_p10, pull_resistor_2_node;
  wire [7:0] controlled_buffer_1_out, n8_bit_bi_latch_lvc543_1_p5;

  assign controlled_buffer_1_out = bidirectional_monsters_1_write ? D_IN_LEFT : 8'bz;  // Controlled_Buffer controlled_buffer_1
  assign D_OUT_LEFT = bidirectional_monsters_1_read ? controlled_buffer_1_out : 8'bz;  // Controlled_Buffer controlled_buffer_2
  Bidirectional_Monsters bidirectional_monsters_1 (
    .WRITE(bidirectional_monsters_1_write), .READ(bidirectional_monsters_1_read), .RWB(MEMORY_WEB_IN),
    .ENABLE_B(and_1_out));
  and and_1 (and_1_out, or_1_out, MEMORY_OEB_IN);
  or or_1 (or_1_out, MEMORY_WEB_IN, GATEWAY_ENABLE_B);
  // Probe on controlled_buffer_1_out
  Pull_Resistor #(.pull(1)) pull_resistor_1 (.node(pull_resistor_2_node[1]));
  Pull_Resistor #(.pull(1)) pull_resistor_2 (.node(pull_resistor_2_node[0]));
  Pull_Resistor pull_resistor_3 (.node(pull_resistor_3_node));
  Pull_Resistor #(.pull(1)) pull_resistor_4 (.node(pull_resistor_4_node));
  // _8_bit_Bi_latch__LVC543 8_bit_bi_latch_lvc543_1: pin names not known; wires that end beside it: MEMORY_WEB_IN, or_1_out, pull_resistor_3_node, controlled_buffer_1_out, n8_bit_bi_latch_lvc543_1_p5, GATEWAY_ENABLE_B, MEMORY_OEB_IN, n8_bit_bi_latch_lvc543_1_p8
  // _16_bit_Line_Driver__LVC16244 16_bit_line_driver_lvc16244_1: pin names not known; wires that end beside it: pull_resistor_2_node[1], GATEWAY_ENABLE_B, GATEWAY_ENABLE_B, GATEWAY_ENABLE_B, GATEWAY_ENABLE_B, pull_resistor_4_node, {MEMORY_OEB_IN, MEMORY_WEB_IN, pull_resistor_2_node}, ADDRESS_IN_A0_23[23:20], ADDRESS_IN_A0_23[19:16], {MEMORY_OEB_OUT, MEMORY_WEB_OUT, n16_bit_line_driver_lvc16244_1_p10}, MADDRESS_OUT_A0_23[23:20], MADDRESS_OUT_A0_23[19:16]
  // _16_bit_Line_Driver__LVC16244 16_bit_line_driver_lvc16244_2: pin names not known; wires that end beside it: GATEWAY_ENABLE_B, GATEWAY_ENABLE_B, GATEWAY_ENABLE_B, GATEWAY_ENABLE_B, ADDRESS_IN_A0_23[15:12], ADDRESS_IN_A0_23[11:8], ADDRESS_IN_A0_23[7:4], ADDRESS_IN_A0_23[3:0], MADDRESS_OUT_A0_23[15:12], MADDRESS_OUT_A0_23[11:8], MADDRESS_OUT_A0_23[7:4], MADDRESS_OUT_A0_23[3:0]
  Pull_Resistor pull_resistor_5 (.node(n8_bit_bi_latch_lvc543_1_p8));
  assign n8_bit_bi_latch_lvc543_1_p5 = bidirectional_monsters_2_read ? D_IN_RIGHT : 8'bz;  // Controlled_Buffer controlled_buffer_3
  // Probe on n8_bit_bi_latch_lvc543_1_p5
  assign D_OUT_RIGHT = bidirectional_monsters_2_write ? n8_bit_bi_latch_lvc543_1_p5 : 8'bz;  // Controlled_Buffer controlled_buffer_4
  Bidirectional_Monsters bidirectional_monsters_2 (
    .WRITE(bidirectional_monsters_2_write), .READ(bidirectional_monsters_2_read), .RWB(MEMORY_WEB_IN),
    .ENABLE_B(and_2_out));
  and and_2 (and_2_out, or_1_out, GATEWAY_ENABLE_B);
endmodule

module Memory_Transceiver (
  input  [7:0] MPU_D_IN,
  input  [7:0] MAIN_MEMORY_D_IN,
  input  MAIN_MEMORY_VALID_B,
  input  MEMORY_LOCKOUT,
  input  RWB,
  input  RWB_B,
  input  [23:0] ADDRESS_IN_A0_23,
  output [7:0] MPU_D_OUT,
  output [7:0] MAIN_MEMORY_D_OUT,
  output WE_B,
  output OE_B,
  output [23:0] ADDRESS_OUT_A0_23
);

  wire bidirectional_monsters_1_read, bidirectional_monsters_1_write, bidirectional_monsters_2_read,
       bidirectional_monsters_2_write, or_1_out, pull_resistor_3_node;
  wire [1:0] n16_bit_line_driver_lvc16244_1_p9, pull_resistor_2_node;
  wire [7:0] controlled_buffer_1_out, n8_bit_bus_transceiver_lvc4245_1_p4;

  or or_1 (or_1_out, MAIN_MEMORY_VALID_B, MEMORY_LOCKOUT);
  assign controlled_buffer_1_out = bidirectional_monsters_1_write ? MPU_D_IN : 8'bz;  // Controlled_Buffer controlled_buffer_1
  assign MPU_D_OUT = bidirectional_monsters_1_read ? controlled_buffer_1_out : 8'bz;  // Controlled_Buffer controlled_buffer_2
  Bidirectional_Monsters bidirectional_monsters_1 (
    .WRITE(bidirectional_monsters_1_write), .READ(bidirectional_monsters_1_read), .RWB(RWB),
    .ENABLE_B(or_1_out));
  Pull_Resistor #(.pull(1)) pull_resistor_1 (.node(pull_resistor_2_node[1]));
  Pull_Resistor #(.pull(1)) pull_resistor_2 (.node(pull_resistor_2_node[0]));
  Pull_Resistor #(.pull(1)) pull_resistor_3 (.node(pull_resistor_3_node));
  // _8_bit_Bus_Transceiver__LVC4245 8_bit_bus_transceiver_lvc4245_1: pin names not known; wires that end beside it: or_1_out, controlled_buffer_1_out, RWB, n8_bit_bus_transceiver_lvc4245_1_p4
  // _16_bit_Line_Driver__LVC16244 16_bit_line_driver_lvc16244_1: pin names not known; wires that end beside it: or_1_out, or_1_out, or_1_out, or_1_out, pull_resistor_3_node, {RWB, RWB_B, pull_resistor_2_node}, ADDRESS_IN_A0_23[19:16], ADDRESS_IN_A0_23[23:20], {WE_B, OE_B, n16_bit_line_driver_lvc16244_1_p9}, ADDRESS_OUT_A0_23[19:16], ADDRESS_OUT_A0_23[23:20]
  // _16_bit_Line_Driver__LVC16244 16_bit_line_driver_lvc16244_2: pin names not known; wires that end beside it: or_1_out, or_1_out, or_1_out, or_1_out, ADDRESS_IN_A0_23[15:12], ADDRESS_IN_A0_23[11:8], ADDRESS_IN_A0_23[7:4], ADDRESS_IN_A0_23[3:0], ADDRESS_OUT_A0_23[15:12], ADDRESS_OUT_A0_23[11:8], ADDRESS_OUT_A0_23[7:4], ADDRESS_OUT_A0_23[3:0]
  assign n8_bit_bus_transceiver_lvc4245_1_p4 = bidirectional_monsters_2_read ? MAIN_MEMORY_D_IN : 8'bz;  // Controlled_Buffer controlled_buffer_3
  assign MAIN_MEMORY_D_OUT = bidirectional_monsters_2_write ? n8_bit_bus_transceiver_lvc4245_1_p4 : 8'bz;  // Controlled_Buffer controlled_buffer_4
  Bidirectional_Monsters bidirectional_monsters_2 (
    .WRITE(bidirectional_monsters_2_write), .READ(bidirectional_monsters_2_read), .RWB(RWB),
    .ENABLE_B(or_1_out));
endmodule

module Memory_Lockout_And_Generator (
  input  MAIN_MEMORY_VALID_1_B,
  input  MAIN_MEMORY_VALID_2_B,
  input  MAIN_MEMORY_VALID_3_B,
  input  GATEWAY_ENABLE_B,
  input  RESET,
  input  SLOW_SELECTOR,
  input  [23:0] ADDRESS_IN_A0_23,
  output LOCKOUT,
  output NMI_B,
  output WE_B,
  output OE_B,
  output [23:0] ADDRESS_OUT_A0_23
);

  wire and_1_out, and_2_out, and_3_out, d_ff_1_q, nand_1_out, not_2_out, not_3_out, or_1_out, or_2_out,
       or_3_out, or_4_out, pull_resistor_5_node, pull_resistor_6_node;
  wire [1:0] n16_bit_line_driver_lvc16244_1_p9;
  wire [3:0] pull_resistor_4_node;

  or or_1 (or_1_out, MAIN_MEMORY_VALID_2_B, MAIN_MEMORY_VALID_1_B);
  or or_2 (or_2_out, MAIN_MEMORY_VALID_1_B, MAIN_MEMORY_VALID_3_B);
  or or_3 (or_3_out, MAIN_MEMORY_VALID_3_B, MAIN_MEMORY_VALID_2_B);
  nand nand_1 (nand_1_out, MAIN_MEMORY_VALID_1_B, MAIN_MEMORY_VALID_2_B, MAIN_MEMORY_VALID_3_B);
  Pull_Resistor #(.pull(1)) pull_resistor_1 (.node(pull_resistor_4_node[3]));
  Pull_Resistor pull_resistor_2 (.node(pull_resistor_4_node[2]));
  Pull_Resistor #(.pull(1)) pull_resistor_3 (.node(pull_resistor_4_node[1]));
  Pull_Resistor #(.pull(1)) pull_resistor_4 (.node(pull_resistor_4_node[0]));
  and and_1 (and_1_out, or_1_out, or_2_out, or_3_out);
  and and_2 (and_2_out, and_1_out, nand_1_out);
  or or_4 (or_4_out, and_2_out, GATEWAY_ENABLE_B);
  Pull_Resistor #(.pull(1)) pull_resistor_5 (.node(pull_resistor_5_node));
  Pull_Resistor #(.pull(1)) pull_resistor_6 (.node(pull_resistor_6_node));
  and and_3 (and_3_out, RESET, NMI_B);
  // _16_bit_Line_Driver__LVC16244 16_bit_line_driver_lvc16244_1: pin names not known; wires that end beside it: or_4_out, or_4_out, or_4_out, or_4_out, pull_resistor_5_node, pull_resistor_4_node, ADDRESS_IN_A0_23[19:16], ADDRESS_IN_A0_23[23:20], {WE_B, OE_B, n16_bit_line_driver_lvc16244_1_p9}, ADDRESS_OUT_A0_23[19:16], ADDRESS_OUT_A0_23[23:20]
  // _16_bit_Line_Driver__LVC16244 16_bit_line_driver_lvc16244_2: pin names not known; wires that end beside it: or_4_out, or_4_out, or_4_out, or_4_out, ADDRESS_IN_A0_23[15:12], ADDRESS_IN_A0_23[11:8], ADDRESS_IN_A0_23[7:4], ADDRESS_IN_A0_23[3:0], ADDRESS_OUT_A0_23[15:12], ADDRESS_OUT_A0_23[11:8], ADDRESS_OUT_A0_23[7:4], ADDRESS_OUT_A0_23[3:0]
  not not_1 (LOCKOUT, and_1_out);
  D_Flip_Flop d_ff_1 (.clk(and_1_out), .D(pull_resistor_6_node), .Q(d_ff_1_q), .reset(not_2_out));  // open: Qn, preset
  not not_2 (not_2_out, and_3_out);
  D_Flip_Flop d_ff_2 (.clk(SLOW_SELECTOR), .D(d_ff_1_q), .Qn(NMI_B), .reset(not_3_out));  // open: Q, preset
  not not_3 (not_3_out, RESET);
endmodule

module SNES_Input_Board (
  input  CONTROLLER_DATA_0,
  input  CONTROLLER_DATA_1,
  input  CONTROLLER_DATA_2,
  input  CONTROLLER_DATA_3,
  input  RESET_B,
  input  COUNTER_RESET_B,
  input  OE_CONTROLLER_0_LOW_B,
  input  OE_CONTROLLER_0_HIGH_B,
  input  OE_CONTROLLER_1_LOW_B,
  input  OE_CONTROLLER_1_HIGH_B,
  input  OE_CONTROLLER_2_LOW_B,
  input  OE_CONTROLLER_2_HIGH_B,
  input  OE_CONTROLLER_3_LOW_B,
  input  OE_CONTROLLER_3_HIGH_B,
  output DONE_SHIFTING_B,
  output CONTROLLER_CLOCK,
  output CONTROLLER_LATCH,
  output SHIFT_IN_CLOCK,
  output [7:0] SHIFT_REGISTER_OUT
);

  wire and_1_out, and_2_out, clock_1_out, d_ff_1_qn, not_1_out, not_2_out, not_3_out,
       snes_input_timing_1_pre_clock;
  wire [11:0] n12_bit_up_counter_hc4040_1_p3;

  Clock clock_1 (.out(clock_1_out));
  not not_1 (not_1_out, COUNTER_RESET_B);
  and and_1 (and_1_out, RESET_B, not_1_out);
  // _12_bit_Up_Counter__HC4040 12_bit_up_counter_hc4040_1: pin names not known; wires that end beside it: and_1_out, clock_1_out, n12_bit_up_counter_hc4040_1_p3
  SNES_Input_Timing snes_input_timing_1 (
    .CONTROLLER_LE(CONTROLLER_LATCH), .PRE_CLOCK(snes_input_timing_1_pre_clock),
    .COUNTER(n12_bit_up_counter_hc4040_1_p3[9:0]), .CONTROLLER_CLOCK(CONTROLLER_CLOCK),
    .DONE_SHIFTING_B(DONE_SHIFTING_B));
  D_Flip_Flop d_ff_1 (
    .clk(snes_input_timing_1_pre_clock), .D(CONTROLLER_CLOCK), .Qn(d_ff_1_qn), .reset(not_2_out));  // open: Q, preset
  not not_2 (not_2_out, RESET_B);
  not not_3 (not_3_out, RESET_B);
  D_Flip_Flop d_ff_2 (
    .clk(snes_input_timing_1_pre_clock), .D(d_ff_1_qn), .Qn(SHIFT_IN_CLOCK), .reset(not_3_out));  // open: Q, preset
  and and_2 (and_2_out, RESET_B, CONTROLLER_LATCH);
  SNES_Shift_Register snes_shift_register_1 (
    .CONTROLLER_DATA_3(CONTROLLER_DATA_3), .MRB(and_2_out), .OE_CONTROLLER_0_LOW_B(OE_CONTROLLER_0_LOW_B),
    .SHIFT_REGISTER_OUT(SHIFT_REGISTER_OUT), .CONTROLLER_DATA_2(CONTROLLER_DATA_2),
    .OE_CONTROLLER_0_HIGH_B(OE_CONTROLLER_0_HIGH_B), .CONTROLLER_DATA_1(CONTROLLER_DATA_1),
    .CONTROLLER_DATA_0(CONTROLLER_DATA_0), .OE_CONTROLLER_1_LOW_B(OE_CONTROLLER_1_LOW_B),
    .OE_CONTROLLER_2_HIGH_B(OE_CONTROLLER_2_HIGH_B), .OE_CONTROLLER_1_HIGH_B(OE_CONTROLLER_1_HIGH_B),
    .SHIFT_IN_CLOCK(SHIFT_IN_CLOCK), .OE_CONTROLLER_3_LOW_B(OE_CONTROLLER_3_LOW_B),
    .OE_CONTROLLER_3_HIGH_B(OE_CONTROLLER_3_HIGH_B), .OE_CONTROLLER_2_LOW_B(OE_CONTROLLER_2_LOW_B));

  // Notes on the sheet:
  //   10MHz Clock Oscillator
endmodule

module SNES_Input_Timing (
  input  [9:0] COUNTER,
  output DONE_SHIFTING_B,
  output CONTROLLER_CLOCK,
  output CONTROLLER_LE,
  output PRE_CLOCK
);

  wire and_1_out, nor_1_out, not_1_out, not_2_out, not_3_out, not_4_out, or_1_out, pull_resistor_2_node;
  wire [1:0] nand_1_out;
  wire [5:0] pull_resistor_1_node;
  wire [7:1] n8_bit_latch_lvc373_1_p4;

  and and_1 (and_1_out, COUNTER[0], COUNTER[1], COUNTER[2]);
  not not_1 (not_1_out, COUNTER[5]);
  not not_2 (not_2_out, COUNTER[6]);
  or or_1 (or_1_out, not_1_out, not_2_out, COUNTER[7]);
  not not_3 (not_3_out, COUNTER[9]);
  nor nor_1 (nor_1_out, COUNTER[6], COUNTER[7], COUNTER[8], COUNTER[9]);
  not not_4 (not_4_out, nor_1_out);
  or or_2 (DONE_SHIFTING_B, or_1_out, COUNTER[8], not_3_out);
  Pull_Resistor #(.pull(1)) pull_resistor_1 (.node(pull_resistor_1_node));
  nand nand_1 (nand_1_out[0], COUNTER[4], not_4_out);
  and and_2 (nand_1_out[1], COUNTER[5], nor_1_out);
  Pull_Resistor pull_resistor_2 (.node(pull_resistor_2_node));
  // _8_bit_Latch__LVC373 8_bit_latch_lvc373_1: pin names not known; wires that end beside it: pull_resistor_2_node, {pull_resistor_1_node, nand_1_out}, and_1_out, {n8_bit_latch_lvc373_1_p4, CONTROLLER_CLOCK}
  not not_5 (CONTROLLER_LE, n8_bit_latch_lvc373_1_p4[1]);

  assign PRE_CLOCK = COUNTER[3];
endmodule

module SNES_Shift_Register (
  input  CONTROLLER_DATA_0,
  input  CONTROLLER_DATA_1,
  input  CONTROLLER_DATA_2,
  input  CONTROLLER_DATA_3,
  input  OE_CONTROLLER_0_LOW_B,
  input  OE_CONTROLLER_0_HIGH_B,
  input  OE_CONTROLLER_1_LOW_B,
  input  OE_CONTROLLER_1_HIGH_B,
  input  OE_CONTROLLER_2_LOW_B,
  input  OE_CONTROLLER_2_HIGH_B,
  input  OE_CONTROLLER_3_LOW_B,
  input  OE_CONTROLLER_3_HIGH_B,
  input  MRB,
  input  SHIFT_IN_CLOCK,
  output [7:0] SHIFT_REGISTER_OUT
);

  wire n8_bit_serial_in_shift_lvc595_1_p7, n8_bit_serial_in_shift_lvc595_2_p7,
       n8_bit_serial_in_shift_lvc595_3_p7, n8_bit_serial_in_shift_lvc595_4_p7, not_1_out, not_2_out,
       not_3_out, not_4_out, not_5_out, not_6_out, not_7_out, not_8_out;

  not not_1 (not_1_out, OE_CONTROLLER_0_LOW_B);
  not not_2 (not_2_out, OE_CONTROLLER_1_LOW_B);
  not not_3 (not_3_out, OE_CONTROLLER_2_LOW_B);
  not not_4 (not_4_out, OE_CONTROLLER_3_LOW_B);
  // _8_bit_serial_in_shift__LVC595 8_bit_serial_in_shift_lvc595_1: pin names not known; wires that end beside it: OE_CONTROLLER_0_LOW_B, MRB, CONTROLLER_DATA_0, SHIFT_IN_CLOCK, not_1_out, SHIFT_REGISTER_OUT, n8_bit_serial_in_shift_lvc595_1_p7
  // _8_bit_serial_in_shift__LVC595 8_bit_serial_in_shift_lvc595_2: pin names not known; wires that end beside it: OE_CONTROLLER_1_LOW_B, MRB, CONTROLLER_DATA_1, SHIFT_IN_CLOCK, not_2_out, SHIFT_REGISTER_OUT, n8_bit_serial_in_shift_lvc595_2_p7
  // _8_bit_serial_in_shift__LVC595 8_bit_serial_in_shift_lvc595_3: pin names not known; wires that end beside it: OE_CONTROLLER_2_LOW_B, MRB, CONTROLLER_DATA_2, SHIFT_IN_CLOCK, not_3_out, SHIFT_REGISTER_OUT, n8_bit_serial_in_shift_lvc595_3_p7
  // _8_bit_serial_in_shift__LVC595 8_bit_serial_in_shift_lvc595_4: pin names not known; wires that end beside it: OE_CONTROLLER_3_LOW_B, MRB, CONTROLLER_DATA_3, SHIFT_IN_CLOCK, not_4_out, SHIFT_REGISTER_OUT, n8_bit_serial_in_shift_lvc595_4_p7
  not not_5 (not_5_out, OE_CONTROLLER_0_HIGH_B);
  not not_6 (not_6_out, OE_CONTROLLER_1_HIGH_B);
  not not_7 (not_7_out, OE_CONTROLLER_2_HIGH_B);
  not not_8 (not_8_out, OE_CONTROLLER_3_HIGH_B);
  // _8_bit_serial_in_shift__LVC595 8_bit_serial_in_shift_lvc595_5: pin names not known; wires that end beside it: OE_CONTROLLER_0_HIGH_B, MRB, n8_bit_serial_in_shift_lvc595_1_p7, SHIFT_IN_CLOCK, not_5_out, SHIFT_REGISTER_OUT
  // _8_bit_serial_in_shift__LVC595 8_bit_serial_in_shift_lvc595_6: pin names not known; wires that end beside it: OE_CONTROLLER_1_HIGH_B, MRB, n8_bit_serial_in_shift_lvc595_2_p7, SHIFT_IN_CLOCK, not_6_out, SHIFT_REGISTER_OUT
  // _8_bit_serial_in_shift__LVC595 8_bit_serial_in_shift_lvc595_7: pin names not known; wires that end beside it: OE_CONTROLLER_2_HIGH_B, MRB, n8_bit_serial_in_shift_lvc595_3_p7, SHIFT_IN_CLOCK, not_7_out, SHIFT_REGISTER_OUT
  // _8_bit_serial_in_shift__LVC595 8_bit_serial_in_shift_lvc595_8: pin names not known; wires that end beside it: OE_CONTROLLER_3_HIGH_B, MRB, n8_bit_serial_in_shift_lvc595_4_p7, SHIFT_IN_CLOCK, not_8_out, SHIFT_REGISTER_OUT
endmodule

module Address_Counter (
  input  RESET_B,
  input  CLOCK,
  input  LOAD_B,
  input  [23:0] START_ADDRESS_A0_23,
  output [23:0] ADDRESS_OUT_A0_23
);

  wire n4_bit_up_counter_lvc161_1_p8, n4_bit_up_counter_vhc161_1_p8, n4_bit_up_counter_vhc161_2_p8,
       n4_bit_up_counter_vhc161_3_p8, n4_bit_up_counter_vhc161_4_p8, pull_resistor_1_node,
       pull_resistor_2_node;

  Pull_Resistor #(.pull(1)) pull_resistor_1 (.node(pull_resistor_1_node));
  Pull_Resistor #(.pull(1)) pull_resistor_2 (.node(pull_resistor_2_node));
  // _4_bit_Up_Counter__LVC161 4_bit_up_counter_lvc161_1: pin names not known; wires that end beside it: RESET_B, LOAD_B, START_ADDRESS_A0_23[3:0], CLOCK, pull_resistor_1_node, pull_resistor_2_node, ADDRESS_OUT_A0_23[3:0], n4_bit_up_counter_lvc161_1_p8
  // _4_bit_Up_Counter__VHC161 4_bit_up_counter_vhc161_1: pin names not known; wires that end beside it: RESET_B, LOAD_B, START_ADDRESS_A0_23[7:4], CLOCK, n4_bit_up_counter_lvc161_1_p8, pull_resistor_2_node, ADDRESS_OUT_A0_23[7:4], n4_bit_up_counter_vhc161_1_p8
  // _4_bit_Up_Counter__VHC161 4_bit_up_counter_vhc161_2: pin names not known; wires that end beside it: RESET_B, LOAD_B, START_ADDRESS_A0_23[11:8], CLOCK, n4_bit_up_counter_vhc161_1_p8, pull_resistor_2_node, ADDRESS_OUT_A0_23[11:8], n4_bit_up_counter_vhc161_2_p8
  // _4_bit_Up_Counter__VHC161 4_bit_up_counter_vhc161_3: pin names not known; wires that end beside it: RESET_B, LOAD_B, START_ADDRESS_A0_23[15:12], CLOCK, n4_bit_up_counter_vhc161_2_p8, pull_resistor_2_node, ADDRESS_OUT_A0_23[15:12], n4_bit_up_counter_vhc161_3_p8
  // _4_bit_Up_Counter__VHC161 4_bit_up_counter_vhc161_4: pin names not known; wires that end beside it: RESET_B, LOAD_B, START_ADDRESS_A0_23[19:16], CLOCK, n4_bit_up_counter_vhc161_3_p8, pull_resistor_2_node, ADDRESS_OUT_A0_23[19:16], n4_bit_up_counter_vhc161_4_p8
  // _4_bit_Up_Counter__VHC161 4_bit_up_counter_vhc161_5: pin names not known; wires that end beside it: RESET_B, LOAD_B, START_ADDRESS_A0_23[23:20], CLOCK, n4_bit_up_counter_vhc161_4_p8, pull_resistor_2_node, ADDRESS_OUT_A0_23[23:20]

  // Notes on the sheet:
  //   Source Address
endmodule

module PS2_Input_Board (
  input  PS2_DATA_0,
  input  PS2_CLOCK_0,
  input  PS2_DATA_1,
  input  PS2_CLOCK_1,
  input  RESET_B,
  input  OE_LOW_BYTE_B,
  input  OE_HIGH_BYTE_B,
  output PS2_ACTIVE_0,
  output PS2_ACTIVE_1,
  output [7:0] FIFO_OUT
);

  wire clock_1_out, ps2_shift_register_1_ps2_active_0_b, ps2_shift_register_2_ps2_active_0_b,
       ps2_write_state_1_oe_ps2_data_0_b, ps2_write_state_1_oe_ps2_data_1_b, ps2_write_state_1_ps2_number,
       ps2_write_state_1_reset_active_0_b, ps2_write_state_1_reset_active_1_b,
       ps2_write_state_1_write_ps2_data_0_b, ps2_write_state_1_write_ps2_data_1_b;
  wire [7:0] ps2_shift_register_1_shift_register_out_d0_7;

  Clock clock_1 (.out(clock_1_out));
  PS2_Shift_Register ps2_shift_register_1 (
    .CLOCK_OSCILLATOR(clock_1_out), .OE_B(ps2_write_state_1_oe_ps2_data_0_b), .RESET_B(RESET_B),
    .RESET_ACTIVE_B(ps2_write_state_1_reset_active_0_b),
    .SHIFT_REGISTER_OUT_D0_7(ps2_shift_register_1_shift_register_out_d0_7), .PS2_CLOCK(PS2_CLOCK_0),
    .PS2_DATA(PS2_DATA_0), .PS2_ACTIVE_0_B(ps2_shift_register_1_ps2_active_0_b));
  PS2_Shift_Register ps2_shift_register_2 (
    .CLOCK_OSCILLATOR(clock_1_out), .OE_B(ps2_write_state_1_oe_ps2_data_1_b), .RESET_B(RESET_B),
    .RESET_ACTIVE_B(ps2_write_state_1_reset_active_1_b),
    .SHIFT_REGISTER_OUT_D0_7(ps2_shift_register_1_shift_register_out_d0_7), .PS2_CLOCK(PS2_CLOCK_1),
    .PS2_DATA(PS2_DATA_1), .PS2_ACTIVE_0_B(ps2_shift_register_2_ps2_active_0_b));
  PS2_Write_State ps2_write_state_1 (
    .PS2_ACTIVE_0_B(ps2_shift_register_1_ps2_active_0_b), .RESET_B(RESET_B),
    .WRITE_PS2_DATA_0_B(ps2_write_state_1_write_ps2_data_0_b),
    .OE_PS2_DATA_0_B(ps2_write_state_1_oe_ps2_data_0_b),
    .PS2_ACTIVE_1_B(ps2_shift_register_2_ps2_active_0_b), .PS2_NUMBER(ps2_write_state_1_ps2_number),
    .RESET_ACTIVE_0_B(ps2_write_state_1_reset_active_0_b), .CLOCK_OSCILLATOR(clock_1_out),
    .OE_PS2_DATA_1_B(ps2_write_state_1_oe_ps2_data_1_b),
    .RESET_ACTIVE_1_B(ps2_write_state_1_reset_active_1_b),
    .WRITE_PS2_DATA_1_B(ps2_write_state_1_write_ps2_data_1_b));
  PS2_FIFO ps2_fifo_1 (
    .OE_HIGH_B(OE_HIGH_BYTE_B), .READ_FIFO_B(OE_LOW_BYTE_B), .D_OUT_D0_7(FIFO_OUT),
    .D0_7(ps2_shift_register_1_shift_register_out_d0_7), .OE_LOW_B(OE_LOW_BYTE_B),
    .WRITE_PS2_DATA_0_B(ps2_write_state_1_write_ps2_data_0_b),
    .WRITE_PS2_DATA_1_B(ps2_write_state_1_write_ps2_data_1_b), .D8(ps2_write_state_1_ps2_number),
    .RESET_B(RESET_B));
  not not_1 (PS2_ACTIVE_0, ps2_shift_register_1_ps2_active_0_b);
  not not_2 (PS2_ACTIVE_1, ps2_shift_register_2_ps2_active_0_b);

  // Notes on the sheet:
  //   10MHz Clock Oscillator
endmodule

module PS2_FIFO (
  input  WRITE_PS2_DATA_0_B,
  input  WRITE_PS2_DATA_1_B,
  input  RESET_B,
  input  READ_FIFO_B,
  input  D8,
  input  [7:0] D0_7,
  input  OE_HIGH_B,
  input  OE_LOW_B,
  output [7:0] D_OUT_D0_7
);

  wire and_1_out, not_1_out, not_2_out, or_1_out, or_2_out, pull_resistor_1_node;
  wire [3:0] pull_resistor_2_node;
  wire [3:1] n512_byte_fifo_idt7201_1_p8;
  wire [8:0] n512_byte_fifo_idt7201_1_p6;

  and and_1 (and_1_out, WRITE_PS2_DATA_0_B, WRITE_PS2_DATA_1_B);
  or or_1 (or_1_out, and_1_out, not_1_out);
  not not_1 (not_1_out, RESET_B);
  or or_2 (or_2_out, not_1_out, READ_FIFO_B);
  Pull_Resistor pull_resistor_1 (.node(pull_resistor_1_node));
  // _512_Byte_FIFO__IDT7201 512_byte_fifo_idt7201_1: pin names not known; wires that end beside it: or_1_out, or_2_out, RESET_B, pull_resistor_1_node, {D8, D0_7}, n512_byte_fifo_idt7201_1_p6, n512_byte_fifo_idt7201_1_p8[3], n512_byte_fifo_idt7201_1_p8[1], n512_byte_fifo_idt7201_1_p8[2]
  // Probe on n512_byte_fifo_idt7201_1_p6
  not not_2 (not_2_out, READ_FIFO_B);
  Pull_Resistor #(.pull(1)) pull_resistor_2 (.node(pull_resistor_2_node));
  // _16_bit_Latch__LVC16373 16_bit_latch_lvc16373_1: pin names not known; wires that end beside it: OE_HIGH_B, OE_LOW_B, {pull_resistor_2_node, n512_byte_fifo_idt7201_1_p8, n512_byte_fifo_idt7201_1_p6[8]}, not_2_out, n512_byte_fifo_idt7201_1_p6[7:0], not_2_out, D_OUT_D0_7, D_OUT_D0_7
endmodule

module PS2_Write_State (
  input  PS2_ACTIVE_0_B,
  input  PS2_ACTIVE_1_B,
  input  RESET_B,
  input  CLOCK_OSCILLATOR,
  output PS2_NUMBER,
  output OE_PS2_DATA_0_B,
  output WRITE_PS2_DATA_0_B,
  output RESET_ACTIVE_0_B,
  output OE_PS2_DATA_1_B,
  output WRITE_PS2_DATA_1_B,
  output RESET_ACTIVE_1_B
);

  wire d_ff_1_q, d_ff_2_q, not_1_out, not_2_out, not_3_out, not_4_out, not_5_out, not_6_out,
       pull_resistor_2_node, pull_resistor_3_node, pull_resistor_4_node, pull_resistor_5_node,
       pull_resistor_6_node;
  wire [3:0] n4_bit_up_counter_lvc163_1_p6;
  wire [7:0] n3_to_8_decoder_lvc138_1_p5;

  Pull_Resistor #(.pull(1)) pull_resistor_1 ();  // open: node
  Pull_Resistor #(.pull(1)) pull_resistor_2 (.node(pull_resistor_2_node));
  Pull_Resistor #(.pull(1)) pull_resistor_3 (.node(pull_resistor_3_node));
  Pull_Resistor #(.pull(1)) pull_resistor_4 (.node(pull_resistor_4_node));
  // _4_bit_Up_Counter__LVC163 4_bit_up_counter_lvc163_1: pin names not known; wires that end beside it: RESET_B, pull_resistor_2_node, CLOCK_OSCILLATOR, pull_resistor_3_node, pull_resistor_4_node, n4_bit_up_counter_lvc163_1_p6
  Pull_Resistor pull_resistor_5 (.node(pull_resistor_5_node));
  Pull_Resistor #(.pull(1)) pull_resistor_6 (.node(pull_resistor_6_node));
  // _3_to_8_Decoder__LVC138 3_to_8_decoder_lvc138_1: pin names not known; wires that end beside it: pull_resistor_5_node, pull_resistor_5_node, n4_bit_up_counter_lvc163_1_p6[2:0], pull_resistor_6_node, n3_to_8_decoder_lvc138_1_p5
  not not_1 (not_1_out, n3_to_8_decoder_lvc138_1_p5[0]);
  not not_2 (not_2_out, n3_to_8_decoder_lvc138_1_p5[5]);
  D_Flip_Flop d_ff_1 (
    .clk(not_1_out), .D(PS2_ACTIVE_0_B), .Q(d_ff_1_q), .preset(not_4_out), .reset(not_3_out));  // open: Qn
  not not_3 (not_3_out, RESET_ACTIVE_0_B);
  not not_4 (not_4_out, RESET_B);
  D_Flip_Flop d_ff_2 (
    .clk(not_2_out), .D(PS2_ACTIVE_1_B), .Q(d_ff_2_q), .preset(not_6_out), .reset(not_5_out));  // open: Qn
  not not_5 (not_5_out, RESET_ACTIVE_1_B);
  not not_6 (not_6_out, RESET_B);
  and and_1 (OE_PS2_DATA_0_B, n3_to_8_decoder_lvc138_1_p5[0], n3_to_8_decoder_lvc138_1_p5[1]);
  or or_1 (WRITE_PS2_DATA_0_B, n3_to_8_decoder_lvc138_1_p5[1], d_ff_1_q);
  or or_2 (RESET_ACTIVE_0_B, n3_to_8_decoder_lvc138_1_p5[2], d_ff_1_q);
  and and_2 (OE_PS2_DATA_1_B, n3_to_8_decoder_lvc138_1_p5[5], n3_to_8_decoder_lvc138_1_p5[6]);
  or or_3 (WRITE_PS2_DATA_1_B, n3_to_8_decoder_lvc138_1_p5[6], d_ff_2_q);
  or or_4 (RESET_ACTIVE_1_B, n3_to_8_decoder_lvc138_1_p5[7], d_ff_2_q);

  assign PS2_NUMBER = OE_PS2_DATA_0_B;
endmodule

module PS2_Shift_Register (
  input  OE_B,
  input  PS2_DATA,
  input  PS2_CLOCK,
  input  RESET_B,
  input  CLOCK_OSCILLATOR,
  input  RESET_ACTIVE_B,
  output [7:0] SHIFT_REGISTER_OUT_D0_7,
  output PS2_ACTIVE_0_B
);

  wire and_1_out, and_2_out, clock_detector_1_clock_detect_b, d_ff_1_q, d_ff_1_qn,
       n8_bit_serial_in_shift_lvc595_1_p7, not_1_out, pull_resistor_1_node;
  wire [1:0] n8_bit_serial_in_shift_lvc595_1_p6;
  wire [7:2] n8_bit_serial_in_shift_lvc595_2_p6;

  Clock_Detector clock_detector_1 (
    .TICKY_CLOCK(CLOCK_OSCILLATOR), .CLOCK_DETECT_B(clock_detector_1_clock_detect_b), .CLOCK(PS2_CLOCK));
  LED led_1 (.in(clock_detector_1_clock_detect_b));
  and and_1 (and_1_out, RESET_B, d_ff_1_qn);
  and and_2 (and_2_out, PS2_CLOCK, clock_detector_1_clock_detect_b);
  // _8_bit_serial_in_shift__LVC595 8_bit_serial_in_shift_lvc595_1: pin names not known; wires that end beside it: OE_B, and_1_out, PS2_DATA, PS2_CLOCK, and_2_out, {SHIFT_REGISTER_OUT_D0_7[2], SHIFT_REGISTER_OUT_D0_7[3], SHIFT_REGISTER_OUT_D0_7[4], SHIFT_REGISTER_OUT_D0_7[5], SHIFT_REGISTER_OUT_D0_7[6], SHIFT_REGISTER_OUT_D0_7[7], n8_bit_serial_in_shift_lvc595_1_p6}, n8_bit_serial_in_shift_lvc595_1_p7
  // _8_bit_serial_in_shift__LVC595 8_bit_serial_in_shift_lvc595_2: pin names not known; wires that end beside it: OE_B, and_1_out, n8_bit_serial_in_shift_lvc595_1_p7, PS2_CLOCK, and_2_out, {n8_bit_serial_in_shift_lvc595_2_p6, SHIFT_REGISTER_OUT_D0_7[0], SHIFT_REGISTER_OUT_D0_7[1]}
  D_Flip_Flop d_ff_1 (.clk(CLOCK_OSCILLATOR), .D(and_2_out), .Q(d_ff_1_q), .Qn(d_ff_1_qn));  // open: preset, reset
  Pull_Resistor #(.pull(1)) pull_resistor_1 (.node(pull_resistor_1_node));
  D_Flip_Flop d_ff_2 (
    .clk(d_ff_1_q), .D(pull_resistor_1_node), .Qn(PS2_ACTIVE_0_B), .reset(not_1_out));  // open: Q, preset
  not not_1 (not_1_out, RESET_ACTIVE_B);
  // Probe on SHIFT_REGISTER_OUT_D0_7
endmodule

module Selecting_24Bit_Address_Multiplexer (
  input  OE,
  input  S,
  input  [23:0] ADDRESS_0_A0_23,
  input  [23:0] ADDRESS_1_A0_23,
  output [23:0] ADDRESS_A0_23
);

  wire not_1_out, or_1_out, or_2_out;

  not not_1 (not_1_out, S);
  // Probe on ADDRESS_0_A0_23
  // Probe on ADDRESS_1_A0_23
  or or_1 (or_1_out, OE, S);
  or or_2 (or_2_out, not_1_out, OE);
  // _16_bit_Line_Driver__LVC16244 16_bit_line_driver_lvc16244_1: pin names not known; wires that end beside it: or_1_out, or_1_out, or_2_out, or_2_out, ADDRESS_0_A0_23[23:20], ADDRESS_0_A0_23[19:16], ADDRESS_1_A0_23[23:20], ADDRESS_1_A0_23[19:16], ADDRESS_A0_23[23:20], ADDRESS_A0_23[19:16], ADDRESS_A0_23[23:20], ADDRESS_A0_23[19:16]
  // _16_bit_Line_Driver__LVC16244 16_bit_line_driver_lvc16244_2: pin names not known; wires that end beside it: or_1_out, or_1_out, or_1_out, or_1_out, ADDRESS_0_A0_23[15:12], ADDRESS_0_A0_23[11:8], ADDRESS_0_A0_23[7:4], ADDRESS_0_A0_23[3:0], ADDRESS_A0_23[15:12], ADDRESS_A0_23[11:8], ADDRESS_A0_23[7:4], ADDRESS_A0_23[3:0]
  // _16_bit_Line_Driver__LVC16244 16_bit_line_driver_lvc16244_3: pin names not known; wires that end beside it: or_2_out, or_2_out, or_2_out, or_2_out, ADDRESS_1_A0_23[15:12], ADDRESS_1_A0_23[11:8], ADDRESS_1_A0_23[7:4], ADDRESS_1_A0_23[3:0], ADDRESS_A0_23[15:12], ADDRESS_A0_23[11:8], ADDRESS_A0_23[7:4], ADDRESS_A0_23[3:0]
endmodule
module Enabling_24Bit_Address_Multiplexer (
  input  OEB_0,
  input  OEB_1,
  input  [23:0] ADDRESS_0_A0_23,
  input  [23:0] ADDRESS_1_A0_23,
  output [23:0] ADDRESS_A0_23
);

  // Probe on ADDRESS_0_A0_23
  // Probe on ADDRESS_1_A0_23
  // _16_bit_Line_Driver__LVC16244 16_bit_line_driver_lvc16244_1: pin names not known; wires that end beside it: OEB_0, OEB_0, OEB_1, OEB_1, ADDRESS_0_A0_23[23:20], ADDRESS_0_A0_23[19:16], ADDRESS_1_A0_23[23:20], ADDRESS_1_A0_23[19:16], ADDRESS_A0_23[23:20], ADDRESS_A0_23[19:16], ADDRESS_A0_23[23:20], ADDRESS_A0_23[19:16]
  // _16_bit_Line_Driver__LVC16244 16_bit_line_driver_lvc16244_2: pin names not known; wires that end beside it: OEB_0, OEB_0, OEB_0, OEB_0, ADDRESS_0_A0_23[15:12], ADDRESS_0_A0_23[11:8], ADDRESS_0_A0_23[7:4], ADDRESS_0_A0_23[3:0], ADDRESS_A0_23[15:12], ADDRESS_A0_23[11:8], ADDRESS_A0_23[7:4], ADDRESS_A0_23[3:0]
  // _16_bit_Line_Driver__LVC16244 16_bit_line_driver_lvc16244_3: pin names not known; wires that end beside it: OEB_1, OEB_1, OEB_1, OEB_1, ADDRESS_1_A0_23[15:12], ADDRESS_1_A0_23[11:8], ADDRESS_1_A0_23[7:4], ADDRESS_1_A0_23[3:0], ADDRESS_A0_23[15:12], ADDRESS_A0_23[11:8], ADDRESS_A0_23[7:4], ADDRESS_A0_23[3:0]
endmodule

module Selecting_8Bit_Data_Multiplexer (
  input  [7:0] DATA_0_D0_7,
  input  [7:0] DATA_1_D0_8,
  input  OE,
  input  S,
  output [7:0] D_OUT
);

  // _4_bit_Multiplexer__LVC257 4_bit_multiplexer_lvc257_1: pin names not known; wires that end beside it: OE, S, DATA_0_D0_7[7:4], DATA_1_D0_8[7:4], D_OUT[7:4]
  // _4_bit_Multiplexer__LVC257 4_bit_multiplexer_lvc257_2: pin names not known; wires that end beside it: OE, S, DATA_0_D0_7[3:0], DATA_1_D0_8[3:0], D_OUT[3:0]
endmodule

module Parallel_To_SPI (
  input  CLOCK_IN,
  input  RESET_B,
  input  BEGIN_SHIFT,
  input  LOAD_LOW_B,
  input  LOAD_HIGH_B,
  input  [7:0] D,
  output SEN,
  output SDI,
  output SCK
);

  wire and_1_out, d_ff_1_q, d_ff_1_qn, d_ff_2_q, d_ff_3_q, d_ff_3_qn, n8_bit_down_counter_hct40103_1_p5,
       n8_bit_line_driver_lvc541_1_p4, n8_bit_parallel_in_shift_lv165_1_p6,
       n8_bit_parallel_in_shift_lv165_2_p6, not_1_out, not_2_out, not_3_out, pull_resistor_1_node,
       pull_resistor_4_node;

  D_Flip_Flop d_ff_1 (.clk(CLOCK_IN), .D(d_ff_1_qn), .Q(d_ff_1_q), .Qn(d_ff_1_qn));  // open: preset, reset
  D_Flip_Flop d_ff_2 (
    .clk(BEGIN_SHIFT), .D(pull_resistor_1_node), .Q(d_ff_2_q), .reset(not_1_out));  // open: Qn, preset
  Pull_Resistor #(.pull(1)) pull_resistor_1 (.node(pull_resistor_1_node));
  not not_1 (not_1_out, and_1_out);
  and and_1 (and_1_out, RESET_B, n8_bit_down_counter_hct40103_1_p5);
  not not_2 (not_2_out, RESET_B);
  D_Flip_Flop d_ff_3 (.clk(d_ff_1_q), .D(d_ff_2_q), .Q(d_ff_3_q), .Qn(d_ff_3_qn), .reset(not_2_out));  // open: preset
  D_Flip_Flop d_ff_4 (.clk(d_ff_1_q), .D(d_ff_3_q), .Qn(SEN), .reset(not_3_out));  // open: Q, preset
  not not_3 (not_3_out, RESET_B);
  Pull_Resistor #(.pull(1)) pull_resistor_2 ();  // open: node
  Pull_Resistor #(.pull(1)) pull_resistor_3 ();  // open: node
  Pull_Resistor pull_resistor_4 (.node(pull_resistor_4_node));
  // _8_bit_Line_Driver__LVC541 8_bit_line_driver_lvc541_1: pin names not known; wires that end beside it: BEGIN_SHIFT, BEGIN_SHIFT, 8'h1f, n8_bit_line_driver_lvc541_1_p4
  // _8_bit_Down_Counter__HCT40103 8_bit_down_counter_hct40103_1: pin names not known; wires that end beside it: BEGIN_SHIFT, d_ff_3_qn, CLOCK_IN, n8_bit_line_driver_lvc541_1_p4, n8_bit_down_counter_hct40103_1_p5
  // _8_bit_parallel_in_shift__LV165 8_bit_parallel_in_shift_lv165_1: pin names not known; wires that end beside it: SEN, LOAD_LOW_B, SCK, D, pull_resistor_4_node, n8_bit_parallel_in_shift_lv165_1_p6
  // _8_bit_parallel_in_shift__LV165 8_bit_parallel_in_shift_lv165_2: pin names not known; wires that end beside it: SEN, LOAD_HIGH_B, SCK, D, n8_bit_parallel_in_shift_lv165_1_p6, n8_bit_parallel_in_shift_lv165_2_p6
  // Probe on n8_bit_parallel_in_shift_lv165_2_p6
  or or_1 (SCK, SEN, d_ff_1_qn);
  or or_2 (SDI, SEN, n8_bit_parallel_in_shift_lv165_2_p6);
  // Digital_Oscilloscope #(.nState(24)) digital_oscilloscope_1: pin names not known; wires that end beside it: d_ff_1_q, SEN, SDI, SCK

  // Notes on the sheet:
  //   Enable
  //   Data
  //   Clock
endmodule

module Signal_Dragger_2Bit (
  input  CLK,
  input  INPUT1,
  input  RESET_B,
  input  INPUT2,
  output OUTPUT1,
  output OUTPUT2
);

  wire d_ff_1_q, d_ff_2_q, not_1_out, not_2_out, not_3_out, not_4_out;

  D_Flip_Flop d_ff_1 (.clk(CLK), .D(INPUT1), .Q(d_ff_1_q), .reset(not_1_out));  // open: Qn, preset
  not not_1 (not_1_out, RESET_B);
  D_Flip_Flop d_ff_2 (.clk(CLK), .D(INPUT2), .Q(d_ff_2_q), .reset(not_2_out));  // open: Qn, preset
  not not_2 (not_2_out, RESET_B);
  not not_3 (not_3_out, RESET_B);
  not not_4 (not_4_out, RESET_B);
  D_Flip_Flop d_ff_3 (.clk(CLK), .D(d_ff_1_q), .Q(OUTPUT1), .reset(not_3_out));  // open: Qn, preset
  D_Flip_Flop d_ff_4 (.clk(CLK), .D(d_ff_2_q), .Q(OUTPUT2), .reset(not_4_out));  // open: Qn, preset
endmodule

module Graphics_Board (
  input  EIGHT_BIT,
  input  TRANSPARENCY_B,
  input  [3:0] HIGH_NYBBLE,
  input  [7:0] TRANSPARENCY_COLOUR_INDEX,
  input  [7:0] D_IN,
  input  START_RASTERISING,
  input  [11:0] LINE_WIDTH_0_11,
  input  [23:0] SOURCE_ADDRESS,
  input  [23:0] DESTINATION_ADDRESS,
  input  [7:0] SELECTOR,
  input  RESET_B,
  input  REMAINING_WIDTH_LE,
  input  REMAINING_WIDTH_LOW_OEB,
  input  REMAINING_WIDTH_HIGH_OEB,
  input  IRQ_ENABLE,
  input  IRQ_CLEAR,
  input  MEMORY_LOCKOUT,
  output [23:0] ADDRESS_A0_23,
  output OEB,
  output WEB,
  output [7:0] D_OUT,
  output MAIN_MEMORY_VALID_B,
  output DONE_IRQB,
  output [7:0] LINE_WIDTH_REMAINING_W0_7
);

  wire graphics_line_state_1_clock_dest, graphics_line_state_1_clock_source, graphics_line_state_1_load,
       graphics_pixel_data_1_pixel_0_transparent_b, graphics_pixel_data_1_pixel_1_transparent_b,
       graphics_pixel_state_1_read_tick, graphics_pixel_state_1_read_tick_b,
       graphics_pixel_state_1_write_tick_0_b, graphics_pixel_state_1_write_tick_1_b, not_1_out, or_1_out,
       or_2_out, or_3_out, RWB, RWB_B;
  wire [7:0] D, graphics_pixel_data_1_pixel_0_d0_7, graphics_pixel_data_1_pixel_1_d0_7;
  wire [11:0] graphics_line_state_1_debug_remaining_d0_11;
  wire [23:0] ADDRESS, address_counter_1_address_out_a0_23, address_counter_2_address_out_a0_23;

  not not_1 (not_1_out, graphics_pixel_state_1_read_tick_b);
  Graphics_Line_State graphics_line_state_1 (
    .TICK_SOURCE(not_1_out), .DEBUG_REMAINING_D0_11(graphics_line_state_1_debug_remaining_d0_11),
    .WIDTH_LOW_OEB(REMAINING_WIDTH_LOW_OEB), .LOAD(graphics_line_state_1_load), .CLK(SELECTOR[0]),
    .WIDTH_HIGH_OEB(REMAINING_WIDTH_HIGH_OEB), .WIDTH_PULSE_LE(REMAINING_WIDTH_LE), .CLEAR_IRQ(IRQ_CLEAR),
    .CLOCK_DEST(graphics_line_state_1_clock_dest), .LINE_WIDTH_L0_11(LINE_WIDTH_0_11),
    .CLOCK_SOURCE(graphics_line_state_1_clock_source), .START_RASTERISING(START_RASTERISING),
    .RESET_B(RESET_B), .IRQ_B(DONE_IRQB), .WIDTH_REMAINING_D0_7(LINE_WIDTH_REMAINING_W0_7),
    .TICK_DEST(graphics_pixel_state_1_read_tick_b), .IRQ_ENABLE(IRQ_ENABLE), .VALID_B(MAIN_MEMORY_VALID_B));
  // Probe on graphics_line_state_1_debug_remaining_d0_11
  Graphics_Pixel_Data graphics_pixel_data_1 (
    .PIXEL_0_D0_7(graphics_pixel_data_1_pixel_0_d0_7), .LE(graphics_pixel_state_1_read_tick),
    .PIXEL_1_TRANSPARENT_B(graphics_pixel_data_1_pixel_1_transparent_b), .D_IN(D),
    .PIXEL_0_TRANSPARENT_B(graphics_pixel_data_1_pixel_0_transparent_b),
    .PIXEL_1_D0_7(graphics_pixel_data_1_pixel_1_d0_7), .HIGH_NYBBLE_D0_3(HIGH_NYBBLE), .EIGHT_BIT(EIGHT_BIT),
    .TRANSPARENCY_COLOUR_INDEX(TRANSPARENCY_COLOUR_INDEX), .TRANSPARENCY_B(TRANSPARENCY_B));
  Graphics_Pixel_State graphics_pixel_state_1 (
    .WRITE_TICK_0_B(graphics_pixel_state_1_write_tick_0_b), .CLOCK(SELECTOR[0]),
    .ENABLE_B(MAIN_MEMORY_VALID_B), .WRITE_TICK_1_B(graphics_pixel_state_1_write_tick_1_b),
    .RESET_B(RESET_B), .READ_TICK_B(graphics_pixel_state_1_read_tick_b), .EIGHT_BIT(EIGHT_BIT),
    .READ_TICK(graphics_pixel_state_1_read_tick));
  // Probe on graphics_pixel_data_1_pixel_0_d0_7
  // Probe on graphics_pixel_data_1_pixel_1_d0_7
  Address_Counter address_counter_1 (
    .ADDRESS_OUT_A0_23(address_counter_1_address_out_a0_23), .LOAD_B(graphics_line_state_1_load),
    .START_ADDRESS_A0_23(SOURCE_ADDRESS), .CLOCK(graphics_line_state_1_clock_source), .RESET_B(RESET_B));
  Address_Counter address_counter_2 (
    .ADDRESS_OUT_A0_23(address_counter_2_address_out_a0_23), .LOAD_B(graphics_line_state_1_load),
    .START_ADDRESS_A0_23(DESTINATION_ADDRESS), .CLOCK(graphics_line_state_1_clock_dest), .RESET_B(RESET_B));
  or or_1 (or_1_out, graphics_pixel_data_1_pixel_0_transparent_b, graphics_pixel_state_1_write_tick_0_b);
  or or_2 (or_2_out, graphics_pixel_state_1_write_tick_1_b, graphics_pixel_data_1_pixel_1_transparent_b);
  // Probe on address_counter_1_address_out_a0_23
  // Probe on address_counter_2_address_out_a0_23
  or or_3 (or_3_out, RWB, MAIN_MEMORY_VALID_B);
  not not_2 (RWB, RWB_B);
  and and_1 (RWB_B, or_1_out, or_2_out, graphics_pixel_state_1_read_tick_b);
  Selecting_8Bit_Data_Multiplexer selecting_8bit_data_multiplexer_1 (
    .OE(or_3_out), .D_OUT(D), .S(graphics_pixel_state_1_write_tick_0_b),
    .DATA_0_D0_7(graphics_pixel_data_1_pixel_0_d0_7), .DATA_1_D0_8(graphics_pixel_data_1_pixel_1_d0_7));
  Selecting_24Bit_Address_Multiplexer selecting_24bit_address_multiplexer_1 (
    .ADDRESS_0_A0_23(address_counter_1_address_out_a0_23), .S(RWB_B),
    .ADDRESS_1_A0_23(address_counter_2_address_out_a0_23), .ADDRESS_A0_23(ADDRESS), .OE(MAIN_MEMORY_VALID_B));
  Memory_Transceiver memory_transceiver_1 (
    .WE_B(WEB), .MAIN_MEMORY_VALID_B(MAIN_MEMORY_VALID_B), .ADDRESS_IN_A0_23(ADDRESS),
    .MAIN_MEMORY_D_OUT(D_OUT), .RWB(RWB), .MAIN_MEMORY_D_IN(D_IN), .MEMORY_LOCKOUT(MEMORY_LOCKOUT),
    .OE_B(OEB), .MPU_D_IN(D), .MPU_D_OUT(D), .RWB_B(RWB_B), .ADDRESS_OUT_A0_23(ADDRESS_A0_23));
endmodule

module Graphics_Line_State (
  input  [11:0] LINE_WIDTH_L0_11,
  input  START_RASTERISING,
  input  RESET_B,
  input  CLK,
  input  TICK_DEST,
  input  TICK_SOURCE,
  input  WIDTH_PULSE_LE,
  input  WIDTH_LOW_OEB,
  input  WIDTH_HIGH_OEB,
  input  CLEAR_IRQ,
  input  IRQ_ENABLE,
  output [11:0] DEBUG_REMAINING_D0_11,
  output LOAD,
  output CLOCK_DEST,
  output VALID_B,
  output CLOCK_SOURCE,
  output IRQ_B,
  output [7:0] WIDTH_REMAINING_D0_7
);

  wire and_1_out, and_2_out, d_type_flip_flop_lvc74_1_p5, d_type_flip_flop_lvc74_1_p7,
       d_type_flip_flop_lvc74_1_p8, d_type_flip_flop_lvc74_3_p8, d_type_flip_flop_lvc74_3_p10,
       n4_bit_up_down_counter_hct193_1_p6, n4_bit_up_down_counter_hct193_2_p7,
       n4_bit_up_down_counter_hct193_3_p7, not_1_out, not_2_out, not_3_out, not_4_out, or_1_out, or_2_out,
       pull_resistor_1_node, pull_resistor_2_node, pull_resistor_4_node, pull_resistor_5_node,
       pull_resistor_6_node;
  wire [3:0] pull_resistor_7_node;

  not not_1 (not_1_out, START_RASTERISING);
  and and_1 (and_1_out, or_2_out, RESET_B);
  and and_2 (and_2_out, RESET_B, not_2_out);
  not not_2 (not_2_out, CLEAR_IRQ);
  // D_type_Flip_Flop__LVC74 d_type_flip_flop_lvc74_1: pin names not known; wires that end beside it: and_1_out, not_1_out, RESET_B, not_1_out, d_type_flip_flop_lvc74_1_p5, START_RASTERISING, d_type_flip_flop_lvc74_1_p7, d_type_flip_flop_lvc74_1_p8, LOAD
  Pull_Resistor #(.pull(1)) pull_resistor_1 (.node(pull_resistor_1_node));
  Pull_Resistor #(.pull(1)) pull_resistor_2 (.node(pull_resistor_2_node));
  not not_3 (not_3_out, RESET_B);
  and and_3 (d_type_flip_flop_lvc74_1_p5, d_type_flip_flop_lvc74_1_p7, CLK);
  // D_type_Flip_Flop__LVC74 d_type_flip_flop_lvc74_2: pin names not known; wires that end beside it: and_2_out, pull_resistor_1_node, pull_resistor_2_node, pull_resistor_2_node, d_type_flip_flop_lvc74_1_p8, IRQ_ENABLE, pull_resistor_2_node, pull_resistor_2_node, IRQ_B
  not not_4 (not_4_out, LOAD);
  and and_4 (CLOCK_DEST, LOAD, d_type_flip_flop_lvc74_1_p5, TICK_DEST);
  and and_5 (CLOCK_SOURCE, LOAD, d_type_flip_flop_lvc74_1_p5, TICK_SOURCE);
  or or_1 (or_1_out, not_4_out, CLOCK_DEST);
  Pull_Resistor #(.pull(1)) pull_resistor_3 ();  // open: node
  // _4_bit_Up_Down_Counter__HCT193 4_bit_up_down_counter_hct193_1: pin names not known; wires that end beside it: LOAD, not_3_out, LINE_WIDTH_L0_11[3:0], or_1_out, DEBUG_REMAINING_D0_11[3:0], n4_bit_up_down_counter_hct193_1_p6
  Pull_Resistor #(.pull(1)) pull_resistor_4 (.node(pull_resistor_4_node));
  // _4_bit_Up_Down_Counter__HCT193 4_bit_up_down_counter_hct193_2: pin names not known; wires that end beside it: LOAD, not_3_out, LINE_WIDTH_L0_11[7:4], pull_resistor_4_node, n4_bit_up_down_counter_hct193_1_p6, DEBUG_REMAINING_D0_11[7:4], n4_bit_up_down_counter_hct193_2_p7
  Pull_Resistor #(.pull(1)) pull_resistor_5 (.node(pull_resistor_5_node));
  // _4_bit_Up_Down_Counter__HCT193 4_bit_up_down_counter_hct193_3: pin names not known; wires that end beside it: LOAD, not_3_out, LINE_WIDTH_L0_11[11:8], pull_resistor_5_node, n4_bit_up_down_counter_hct193_2_p7, DEBUG_REMAINING_D0_11[11:8], n4_bit_up_down_counter_hct193_3_p7
  or or_2 (or_2_out, d_type_flip_flop_lvc74_3_p10, n4_bit_up_down_counter_hct193_3_p7);
  Pull_Resistor #(.pull(1)) pull_resistor_6 (.node(pull_resistor_6_node));
  Pull_Resistor pull_resistor_7 (.node(pull_resistor_7_node));
  // D_type_Flip_Flop__LVC74 d_type_flip_flop_lvc74_3: pin names not known; wires that end beside it: RESET_B, pull_resistor_6_node, RESET_B, pull_resistor_6_node, d_type_flip_flop_lvc74_1_p5, n4_bit_up_down_counter_hct193_3_p7, d_type_flip_flop_lvc74_1_p5, d_type_flip_flop_lvc74_3_p8, d_type_flip_flop_lvc74_3_p8, d_type_flip_flop_lvc74_3_p10
  // _8_bit_Latch__LVC574 8_bit_latch_lvc574_1: pin names not known; wires that end beside it: WIDTH_HIGH_OEB, {pull_resistor_7_node, DEBUG_REMAINING_D0_11[11:8]}, WIDTH_PULSE_LE, WIDTH_REMAINING_D0_7
  // _8_bit_Latch__LVC574 8_bit_latch_lvc574_2: pin names not known; wires that end beside it: WIDTH_LOW_OEB, DEBUG_REMAINING_D0_11[7:0], WIDTH_PULSE_LE, WIDTH_REMAINING_D0_7
  nand nand_1 (VALID_B, LOAD, d_type_flip_flop_lvc74_1_p7);
endmodule

module Graphics_Pixel_State (
  input  ENABLE_B,
  input  RESET_B,
  input  CLOCK,
  input  EIGHT_BIT,
  output READ_TICK,
  output READ_TICK_B,
  output WRITE_TICK_0_B,
  output WRITE_TICK_1_B
);

  wire and_1_out, and_2_out, not_1_out, not_2_out, not_3_out, or_1_out, or_2_out, pull_resistor_1_node,
       pull_resistor_2_node, pull_resistor_3_node, pull_resistor_4_node, pull_resistor_5_node;
  wire [3:0] n4_bit_up_counter_lvc163_1_p7;
  wire [7:3] n3_to_8_decoder_lvc138_1_p5;

  not not_1 (not_1_out, ENABLE_B);
  not not_2 (not_2_out, CLOCK);
  and and_1 (and_1_out, not_1_out, RESET_B, and_2_out);
  Pull_Resistor #(.pull(1)) pull_resistor_1 (.node(pull_resistor_1_node));
  Pull_Resistor #(.pull(1)) pull_resistor_2 (.node(pull_resistor_2_node));
  Pull_Resistor #(.pull(1)) pull_resistor_3 (.node(pull_resistor_3_node));
  // _4_bit_Up_Counter__LVC163 4_bit_up_counter_lvc163_1: pin names not known; wires that end beside it: and_1_out, pull_resistor_1_node, pull_resistor_2_node, not_2_out, pull_resistor_3_node, pull_resistor_3_node, n4_bit_up_counter_lvc163_1_p7
  Pull_Resistor pull_resistor_4 (.node(pull_resistor_4_node));
  Pull_Resistor #(.pull(1)) pull_resistor_5 (.node(pull_resistor_5_node));
  // _3_to_8_Decoder__LVC138 3_to_8_decoder_lvc138_1: pin names not known; wires that end beside it: pull_resistor_4_node, n4_bit_up_counter_lvc163_1_p7[3], n4_bit_up_counter_lvc163_1_p7[2:0], pull_resistor_5_node, {n3_to_8_decoder_lvc138_1_p5, WRITE_TICK_1_B, WRITE_TICK_0_B, READ_TICK_B}
  not not_3 (not_3_out, EIGHT_BIT);
  or or_1 (or_1_out, not_3_out, WRITE_TICK_0_B);
  or or_2 (or_2_out, EIGHT_BIT, WRITE_TICK_1_B);
  not not_4 (READ_TICK, READ_TICK_B);
  and and_2 (and_2_out, or_1_out, or_2_out);

  // Notes on the sheet:
  //   Reset Counter
endmodule

module Graphics_Pixel_Data (
  input  [7:0] D_IN,
  input  EIGHT_BIT,
  input  [3:0] HIGH_NYBBLE_D0_3,
  input  LE,
  input  TRANSPARENCY_B,
  input  [7:0] TRANSPARENCY_COLOUR_INDEX,
  output [7:0] PIXEL_0_D0_7,
  output [7:0] PIXEL_1_D0_7,
  output PIXEL_0_TRANSPARENT_B,
  output PIXEL_1_TRANSPARENT_B
);

  wire pull_resistor_1_node, pull_resistor_2_node;
  wire [3:0] n4_bit_multiplexer_lvc157_1_p5;

  Pull_Resistor pull_resistor_1 (.node(pull_resistor_1_node));
  // _4_bit_Multiplexer__LVC157 4_bit_multiplexer_lvc157_1: pin names not known; wires that end beside it: pull_resistor_1_node, EIGHT_BIT, HIGH_NYBBLE_D0_3, D_IN[7:4], n4_bit_multiplexer_lvc157_1_p5
  Pull_Resistor pull_resistor_2 (.node(pull_resistor_2_node));
  // _16_bit_Latch__LVC16373 16_bit_latch_lvc16373_1: pin names not known; wires that end beside it: pull_resistor_2_node, pull_resistor_2_node, {n4_bit_multiplexer_lvc157_1_p5, D_IN[3:0]}, LE, {HIGH_NYBBLE_D0_3, D_IN[7:4]}, LE, PIXEL_0_D0_7, PIXEL_1_D0_7
  // _8_bit_Comparator__F521 8_bit_comparator_f521_1: pin names not known; wires that end beside it: TRANSPARENCY_B, PIXEL_0_D0_7, TRANSPARENCY_COLOUR_INDEX, PIXEL_0_TRANSPARENT_B
  // _8_bit_Comparator__F521 8_bit_comparator_f521_2: pin names not known; wires that end beside it: TRANSPARENCY_B, PIXEL_1_D0_7, TRANSPARENCY_COLOUR_INDEX, PIXEL_1_TRANSPARENT_B

  // Notes on the sheet:
  //   Pixel Data
endmodule

module Instruction_Counter (
  input  RESET,
  input  A0,
  input  PHI2_B,
  input  OPCODE_ADDRESS,
  input  OEB_C0_7,
  input  OEB_C8_15,
  input  OEB_C16_23,
  input  OEB_C24_31,
  input  READ_ENABLE_B,
  output [7:0] D_OUT,
  output [31:0] COUNT
);

  wire d_type_flip_flop_lvc74_1_p7, d_type_flip_flop_lvc74_1_p8, n8_bit_up_counter_hc590_1_p5,
       n8_bit_up_counter_hc590_2_p6, n8_bit_up_counter_hc590_3_p6, nor_1_out, not_1_out, not_2_out, or_1_out,
       or_2_out, or_3_out, or_4_out, or_5_out, xor_1_out;

  not not_1 (not_1_out, OPCODE_ADDRESS);
  not not_2 (not_2_out, OEB_C0_7);
  Pull_Resistor #(.pull(1)) pull_resistor_1 ();  // open: node
  Pull_Resistor #(.pull(1)) pull_resistor_2 ();  // open: node
  or or_1 (or_1_out, OEB_C0_7, READ_ENABLE_B);
  or or_2 (or_2_out, OEB_C8_15, READ_ENABLE_B);
  or or_3 (or_3_out, OEB_C16_23, READ_ENABLE_B);
  or or_4 (or_4_out, OEB_C24_31, READ_ENABLE_B);
  // D_type_Flip_Flop__LVC74 d_type_flip_flop_lvc74_1: pin names not known; wires that end beside it: RESET, RESET, PHI2_B, A0, PHI2_B, not_1_out, d_type_flip_flop_lvc74_1_p7, d_type_flip_flop_lvc74_1_p8
  xor xor_1 (xor_1_out, A0, d_type_flip_flop_lvc74_1_p7);
  nor nor_1 (nor_1_out, xor_1_out, d_type_flip_flop_lvc74_1_p8);
  or or_5 (or_5_out, nor_1_out, xor_1_out);
  Pull_Resistor pull_resistor_3 ();  // open: node
  Pull_Resistor pull_resistor_4 ();  // open: node
  // _8_bit_Up_Counter__HC590 8_bit_up_counter_hc590_1: pin names not known; wires that end beside it: RESET, or_5_out, not_2_out, COUNT[7:0], n8_bit_up_counter_hc590_1_p5
  Pull_Resistor pull_resistor_5 ();  // open: node
  // _8_bit_Up_Counter__HC590 8_bit_up_counter_hc590_2: pin names not known; wires that end beside it: RESET, n8_bit_up_counter_hc590_1_p5, or_5_out, not_2_out, COUNT[15:8], n8_bit_up_counter_hc590_2_p6
  Pull_Resistor pull_resistor_6 ();  // open: node
  // _8_bit_Up_Counter__HC590 8_bit_up_counter_hc590_3: pin names not known; wires that end beside it: RESET, n8_bit_up_counter_hc590_2_p6, or_5_out, not_2_out, COUNT[23:16], n8_bit_up_counter_hc590_3_p6
  Pull_Resistor pull_resistor_7 ();  // open: node
  // _8_bit_Up_Counter__HC590 8_bit_up_counter_hc590_4: pin names not known; wires that end beside it: RESET, n8_bit_up_counter_hc590_3_p6, or_5_out, not_2_out, COUNT[31:24]
  // _16_bit_Line_Driver__LVC16244 16_bit_line_driver_lvc16244_1: pin names not known; wires that end beside it: or_1_out, or_1_out, or_2_out, or_2_out
  // _16_bit_Line_Driver__LVC16244 16_bit_line_driver_lvc16244_2: pin names not known; wires that end beside it: or_3_out, or_3_out, or_4_out, or_4_out
endmodule

module Microcontroller_Testing (
  input  RESET
);

  wire BANK_LATCH, CLOCK_ENABLE_B, DATA_TRANSMIT_B, DEVICE_STROBE_B, DEVICE_VALID_B, ENTER_INTERRUPT,
       EXIT_INTERRUPT, FST, INTERNAL_MEMORY_VALID, IRQ_B, KERNAL_MODE, KERNAL_MODE_B, KERNAL_ROM_B,
       main_memory_gateway_1_memory_oeb_out, main_memory_gateway_1_memory_web_out, MAIN_MEMORY_VALID_B,
       MEMORY_LOCKOUT_CHANNEL_0, memory_transceiver_1_oe_b, memory_transceiver_1_we_b,
       microprocessor_w65c816_1_p6, microprocessor_w65c816_1_p13, microprocessor_w65c816_1_p14,
       microprocessor_w65c816_1_p15, MPU_LOCK_IN, n8_bit_bi_latch_lvc543_1_p5, n8_bit_bi_latch_lvc543_2_p5,
       n8_bit_comparator_f521_1_p4, n16_bit_latch_lvc16373_1_p7, n16_bit_latch_lvc16373_1_p8, NATIVE_MODE,
       NMI_B, NMIB_LOCKOUT_CHANNEL_0, nor_1_out, not_1_out, not_2_out, not_3_out, not_4_out, not_5_out,
       not_6_out, not_7_out, not_8_out, OPCODE_ADDRESS, or_1_out, or_2_out, or_3_out, or_4_out, or_5_out,
       or_6_out, PHI2, pull_resistor_5_node, pull_resistor_6_node, pull_resistor_10_node,
       pull_resistor_13_node, pull_resistor_14_node, pull_resistor_16_node, pull_resistor_17_node,
       pull_resistor_20_node, pull_resistor_21_node, pull_resistor_24_node, pull_resistor_25_node,
       pull_resistor_27_node, pull_resistor_28_node, quick_timing_circuit_1_clk,
       quick_timing_circuit_1_reset_1_b, RDY, READ_BANK_REMAP_B, READ_ENABLE, READ_ENABLE_B, READ_SELECTOR,
       RESET_t, ROM_ADDRESS_VALID, RWB, RWB_B, SA_FLAG_REGISTER_B, SA_INSTRUCTION_COUNTER_0,
       SA_INSTRUCTION_COUNTER_1, SA_INSTRUCTION_COUNTER_2, SA_INSTRUCTION_COUNTER_3,
       SA_INTERRUPTS_IN_DEPTH_B, SA_USER_PROGRAM_ID_B, SEL0, SEL2, SEL4, SEL6, selector_state_1_sel0,
       selector_state_1_sel1, selector_state_1_sel2, selector_state_1_sel3, selector_state_1_sel4,
       selector_state_1_sel5, selector_state_1_sel6, selector_state_1_sel7, SLW, SPECIAL_ADDRESS_VALID_B,
       STOP_SELECTOR, user_mode_memory_glue_1_ceb, user_mode_memory_glue_1_oeb, user_mode_memory_glue_1_web,
       VPB, WRITE_ENABLE, WRITE_ENABLE_B, WRITE_SELECTOR;
  wire [1:0] DEVICE_CHANNEL, n16_bit_line_driver_lvc16244_1_p8, pull_resistor_7_node;
  wire [3:0] DEVICE_ADDRESS, n2_to_4_decoder_lvc139_1_p4, n16_bit_line_driver_lvc16244_1_p10,
       pull_resistor_2_node, pull_resistor_8_node;
  wire [5:0] DEVICE_IDENTIFIER, n16_bit_line_driver_lvc16244_1_p9;
  wire [7:0] A0_7, A8_15, BA0_7, D, interrupt_detection_1_opcode, IRAM_A0_7, KERNAL_ROM_data,
       kernal_user_mode_1_interrupt_depth, main_memory_gateway_1_d_out_right,
       memory_transceiver_1_main_memory_d_out, microprocessor_w65c816_1_p10, MRAM_A16_23,
       n3_to_8_decoder_lvc138_1_p5, n8_bit_bus_transceiver_lvc4245_2_p4, pull_resistor_18_node,
       pull_resistor_22_node, pull_resistor_26_node, USER_PROGRAM_ID;
  wire [7:1] quick_timing_circuit_1_selector_b;
  wire [7:2] flags_register_1_flag_register;
  wire [8:0] pull_resistor_1_node;
  wire [11:3] address_decode_1_special_memory_selector_b;
  wire [16:0] user_mode_memory_glue_1_address_out_a0_16;
  wire [23:0] main_memory_gateway_1_maddress_out_a0_23, memory_transceiver_1_address_out_a0_23,
       pull_resistor_15_node, pull_resistor_19_node, pull_resistor_23_node;
  wire [31:0] instruction_counter_1_count;
  wire [39:0] T1, T2;

  Quick_Timing_Circuit quick_timing_circuit_1 (
    .RESET_1_B(quick_timing_circuit_1_reset_1_b), .RESET(RESET),
    .SELECTOR_B({quick_timing_circuit_1_selector_b[7], SEL6, quick_timing_circuit_1_selector_b[5], SEL4, quick_timing_circuit_1_selector_b[3], SEL2, quick_timing_circuit_1_selector_b[1], SEL0}),
    .CLK(quick_timing_circuit_1_clk), .SLOW_SELECTOR(SLW));  // open: HCLK_B, MULTIPLEXER, COUNTER, RESET_0_B, HCLK, CLK_B, CLOCK_IN
  // Probe on {BA0_7, A8_15, A0_7}
  not not_1 (not_1_out, PHI2);
  Pull_Resistor #(.pull(1)) pull_resistor_1 (.node(pull_resistor_1_node));
  Pull_Resistor #(.pull(1)) pull_resistor_2 (.node(pull_resistor_2_node));
  LED led_1 (.in(selector_state_1_sel0));
  // Probe on D
  LED led_2 (.in(selector_state_1_sel4));
  LED led_3 (.in(selector_state_1_sel2));
  LED led_4 (.in(selector_state_1_sel1));
  LED led_5 (.in(selector_state_1_sel3));
  Selector_State selector_state_1 (
    .SEL0(selector_state_1_sel0), .SEL5(selector_state_1_sel5), .DEVICE_STROBE_B(DEVICE_STROBE_B),
    .SEL2(selector_state_1_sel2), .READ_SELECTOR(READ_SELECTOR), .READ_BANK_REMAP_B(READ_BANK_REMAP_B),
    .WRITE_SELECTOR(WRITE_SELECTOR), .RESET(quick_timing_circuit_1_reset_1_b), .BOARD_RESET(RESET_t),
    .SEL6(selector_state_1_sel6),
    .SELECTOR({quick_timing_circuit_1_selector_b[7], SEL6, quick_timing_circuit_1_selector_b[5], SEL4, quick_timing_circuit_1_selector_b[3], SEL2, quick_timing_circuit_1_selector_b[1], SEL0}),
    .PHI2(PHI2), .STOP_SELECTOR_B(STOP_SELECTOR), .DATA_TRANSMIT_B(DATA_TRANSMIT_B),
    .SEL1(selector_state_1_sel1), .MPU_LOCK_IN(MPU_LOCK_IN), .SEL7(selector_state_1_sel7),
    .SEL3(selector_state_1_sel3), .CLOCK_ENABLE_B(CLOCK_ENABLE_B), .BANK_LATCH(BANK_LATCH),
    .SEL4(selector_state_1_sel4));
  Address_Decode address_decode_1 (
    .DEVICE_CHANNEL(DEVICE_CHANNEL), .ADDRESS_IN_A0_24({BA0_7, A8_15, A0_7}), .MPU_LOCK_IN(MPU_LOCK_IN),
    .INTERNAL_MEMORY_VALID(INTERNAL_MEMORY_VALID), .RWB(RWB), .DEVICE_ADDRESS(DEVICE_ADDRESS),
    .DEVICE_VALID_B(DEVICE_VALID_B), .KERNAL_MODE_B(KERNAL_MODE_B), .DEVICE_IDENTIFIER(DEVICE_IDENTIFIER),
    .ROM_VALID(ROM_ADDRESS_VALID), .KERNAL_MODE(KERNAL_MODE), .KERNAL_ROM_B(KERNAL_ROM_B),
    .MAIN_MEMORY_VALID_B(MAIN_MEMORY_VALID_B),
    .SPECIAL_MEMORY_SELECTOR_B({SA_INSTRUCTION_COUNTER_3, SA_INSTRUCTION_COUNTER_2, SA_INSTRUCTION_COUNTER_1, SA_INSTRUCTION_COUNTER_0, address_decode_1_special_memory_selector_b, SA_FLAG_REGISTER_B, SA_INTERRUPTS_IN_DEPTH_B, SA_USER_PROGRAM_ID_B}),
    .SPECIAL_VALID_B(SPECIAL_ADDRESS_VALID_B));
  Interrupt_Detection interrupt_detection_1 (
    .LATCH_D(WRITE_SELECTOR), .OPCODE_ADDRESS(OPCODE_ADDRESS), .OPCODE(interrupt_detection_1_opcode),
    .RESET_B(RESET_t), .ADDRESS_IN_A0(A0_7[0]), .NATIVE_MODE(NATIVE_MODE),
    .RETURN_FROM_INTERRUPT(EXIT_INTERRUPT), .ENTER_INTERRUPT(ENTER_INTERRUPT), .D(D), .PHI2_B(not_1_out));
  Interrupt_Vectoring interrupt_vectoring_1 (
    .IRQ_6_B(pull_resistor_1_node[6]), .IRQ_8_B(pull_resistor_1_node[8]), .IRQ_5_B(pull_resistor_1_node[5]),
    .IRQ_B(IRQ_B), .NMI_3_B(pull_resistor_2_node[3]), .IRQ_7_B(pull_resistor_1_node[7]),
    .IRQ_0_B(pull_resistor_1_node[0]), .NMI_0_B(pull_resistor_2_node[0]), .ADDRESS_IN_A0_7(A0_7),
    .NMI_B(NMI_B), .IRQ_1_B(pull_resistor_1_node[1]), .IRQ_4_B(pull_resistor_1_node[4]),
    .NMI_1_B(pull_resistor_2_node[1]), .NMI_2_B(pull_resistor_2_node[2]), .IRQ_3_B(pull_resistor_1_node[3]),
    .IRQ_2_B(pull_resistor_1_node[2]), .ADDRESS_OUT_A0_7(IRAM_A0_7), .VPB(VPB));
  LED led_6 (.in(selector_state_1_sel6));
  LED led_7 (.in(selector_state_1_sel7));
  LED led_8 (.in(selector_state_1_sel5));
  not not_2 (not_2_out, CLOCK_ENABLE_B);
  and and_1 (FST, not_2_out, quick_timing_circuit_1_clk);
  Counter #(.width(32), .max('hffffffff)) counter_1 (.clk(FST));  // open: load, D, count, Q, carry, up, clr
  // Probe on interrupt_detection_1_opcode
  or or_1 (or_1_out, RWB_B, SEL4);
  // Probe on D
  Pull_Resistor #(.pull(1)) pull_resistor_3 ();  // open: node
  or or_2 (or_2_out, DEVICE_VALID_B, SEL4);
  Pull_Resistor #(.pull(1)) pull_resistor_4 ();  // open: node
  Pull_Resistor #(.pull(1)) pull_resistor_5 (.node(pull_resistor_5_node));
  // _8_bit_Bi_latch__LVC543 8_bit_bi_latch_lvc543_1: pin names not known; wires that end beside it: RWB, RWB, SEL4, D, n8_bit_bi_latch_lvc543_1_p5, or_1_out, RWB_B, DEVICE_VALID_B
  // _16_bit_Line_Driver__LVC16244 16_bit_line_driver_lvc16244_1: pin names not known; wires that end beside it: SEL4, SEL4, SEL4, SEL4, {DEVICE_IDENTIFIER[5:4], WRITE_ENABLE_B, READ_ENABLE_B}, DEVICE_IDENTIFIER[3:0], DEVICE_ADDRESS, {n16_bit_line_driver_lvc16244_1_p9[5:4], n16_bit_line_driver_lvc16244_1_p8}, n16_bit_line_driver_lvc16244_1_p9[3:0], n16_bit_line_driver_lvc16244_1_p10
  // _2_to_4_Decoder__LVC139 2_to_4_decoder_lvc139_1: pin names not known; wires that end beside it: or_2_out, DEVICE_CHANNEL, pull_resistor_5_node, n2_to_4_decoder_lvc139_1_p4
  LED led_9 (.in(INTERNAL_MEMORY_VALID));
  LED led_10 (.in(SPECIAL_ADDRESS_VALID_B));
  LED led_11 (.in(DEVICE_VALID_B));
  LED led_12 (.in(ROM_ADDRESS_VALID));
  LED led_13 (.in(MAIN_MEMORY_VALID_B));
  Pull_Resistor #(.pull(1)) pull_resistor_6 (.node(pull_resistor_6_node));
  // Probe on n8_bit_bi_latch_lvc543_1_p5
  // Microprocessor__W65C816 microprocessor_w65c816_1: pin names not known; wires that end beside it: pull_resistor_6_node, IRQ_B, NMI_B, RESET_t, PHI2, microprocessor_w65c816_1_p6, T1, T2, {A8_15, A0_7}, microprocessor_w65c816_1_p10, RWB, RDY, microprocessor_w65c816_1_p13, microprocessor_w65c816_1_p14, microprocessor_w65c816_1_p15, FST, VPB
  Clock_Control clock_control_1 (
    .DEVICE_ADDRESS_VALID_B(DEVICE_VALID_B), .RESET(RESET_t), .RWB_B(RWB_B),
    .UNSTOPPABLE_CLOCK(STOP_SELECTOR), .ROM_ADDRESS_VALID(ROM_ADDRESS_VALID), .CLOCK_ENABLE_B(CLOCK_ENABLE_B));
  Flags_Register flags_register_1 (
    .FLAG_REGISTER({flags_register_1_flag_register, KERNAL_ROM_B, MPU_LOCK_IN}),
    .WRITE_ENABLE_B(WRITE_ENABLE_B), .D_IN(D), .D_OUT(D), .READ_ENABLE_B(READ_ENABLE_B), .RESET(RESET_t),
    .SA_FLAG_REGISTER_B(SA_FLAG_REGISTER_B));
  Pull_Resistor pull_resistor_7 (.node(pull_resistor_7_node));
  Pull_Resistor pull_resistor_8 (.node(pull_resistor_8_node));
  // Probe on {A8_15, A0_7}
  Pull_Resistor #(.pull(1)) pull_resistor_9 (.node(microprocessor_w65c816_1_p15));
  Pull_Resistor pull_resistor_10 (.node(pull_resistor_10_node));
  not not_3 (not_3_out, n2_to_4_decoder_lvc139_1_p4[0]);
  // Probe on microprocessor_w65c816_1_p10
  // Probe on {BA0_7, A8_15, IRAM_A0_7}
  // _8_bit_Bi_latch__LVC543 8_bit_bi_latch_lvc543_2: pin names not known; wires that end beside it: n16_bit_line_driver_lvc16244_1_p8[1], n16_bit_line_driver_lvc16244_1_p8[1], n2_to_4_decoder_lvc139_1_p4[0], n8_bit_bi_latch_lvc543_1_p5, n8_bit_bi_latch_lvc543_2_p5, n16_bit_line_driver_lvc16244_1_p8[0], n16_bit_line_driver_lvc16244_1_p8[0], n2_to_4_decoder_lvc139_1_p4[0]
  // _16_bit_Latch__LVC16373 16_bit_latch_lvc16373_1: pin names not known; wires that end beside it: pull_resistor_10_node, pull_resistor_10_node, {pull_resistor_7_node, n16_bit_line_driver_lvc16244_1_p9}, not_3_out, {pull_resistor_8_node, n16_bit_line_driver_lvc16244_1_p10}, not_3_out, n16_bit_latch_lvc16373_1_p7, n16_bit_latch_lvc16373_1_p8
  Signals signals_1 (
    .VPA(microprocessor_w65c816_1_p14), .D(microprocessor_w65c816_1_p10), .READ_ENABLE(READ_ENABLE),
    .OPCODE_ADDRESS(OPCODE_ADDRESS), .CLOCK_ENABLE_B(CLOCK_ENABLE_B), .WRITE_ENABLE_B(WRITE_ENABLE_B),
    .BA0_7(BA0_7), .RWB_B(RWB_B), .RWB(RWB), .BANK_LATCH(BANK_LATCH), .E(microprocessor_w65c816_1_p6),
    .WRITE_ENABLE(WRITE_ENABLE), .WRITE_SELECTOR(WRITE_SELECTOR), .READ_SELECTOR(READ_SELECTOR),
    .VDA(microprocessor_w65c816_1_p13), .READ_ENABLE_B(READ_ENABLE_B), .NATIVE_MODE(NATIVE_MODE));
  User_Mode_Memory_Glue user_mode_memory_glue_1 (
    .ADDRESS_IN_A0_23({BA0_7, A8_15, IRAM_A0_7}), .READ_ENABLE(READ_ENABLE), .WRITE_ENABLE(WRITE_ENABLE),
    .INTERNAL_MEMORY_VALID(INTERNAL_MEMORY_VALID), .USER_BANK(USER_PROGRAM_ID),
    .ADDRESS_OUT_A0_16(user_mode_memory_glue_1_address_out_a0_16), .OEB(user_mode_memory_glue_1_oeb),
    .READ_BANK_REMAP_B(READ_BANK_REMAP_B), .CEB(user_mode_memory_glue_1_ceb),
    .WEB(user_mode_memory_glue_1_web));
  // _8_bit_Bus_Transceiver__LVC4245 8_bit_bus_transceiver_lvc4245_1: pin names not known; wires that end beside it: DATA_TRANSMIT_B, microprocessor_w65c816_1_p10, RWB, D
  Pull_Resistor pull_resistor_11 (.node({A8_15, A0_7}));
  not not_4 (not_4_out, ROM_ADDRESS_VALID);
  or or_3 (or_3_out, not_4_out, READ_ENABLE_B);
  Pull_Resistor pull_resistor_12 (.node(D));
  // Probe on user_mode_memory_glue_1_address_out_a0_16
  RAM #(.databus("bidir"), .enables("line"), .trigger("high"), .addrWidth(17), .\type ("nonvolatile")) INTERNAL_MEMORY (
    .addr(user_mode_memory_glue_1_address_out_a0_16), .data(D));  // open: we, oe, clk
  LED led_14 (.in(user_mode_memory_glue_1_oeb));
  SRAM_Chipifier sram_chipifier_1 (
    .WEB(user_mode_memory_glue_1_web), .OEB(user_mode_memory_glue_1_oeb), .CEB(user_mode_memory_glue_1_ceb));  // open: OE, E, WE
  LED led_15 (.in(user_mode_memory_glue_1_web));
  LED led_16 (.in(user_mode_memory_glue_1_ceb));
  // Probe on {A8_15[6:0], IRAM_A0_7}
  ROM #(.addrWidth(16)) KERNAL_ROM (.addr({1'b1, A8_15[6:0], IRAM_A0_7}), .data(KERNAL_ROM_data));
  not not_5 (not_5_out, or_3_out);
  LED led_17 (.in(or_3_out));
  // Probe on n8_bit_bi_latch_lvc543_2_p5
  // Probe on {BA0_7, A8_15, A0_7}
  // Probe on D
  Kernal_User_Mode kernal_user_mode_1 (
    .INTERRUPT_DEPTH(kernal_user_mode_1_interrupt_depth), .D_OUT(D), .USER(USER_PROGRAM_ID), .BA0_7(BA0_7),
    .EXIT_INTERRUPT(EXIT_INTERRUPT), .READ_ENABLE_B(READ_ENABLE_B), .MAIN_MEMORY_BA0_7(MRAM_A16_23),
    .KERNAL_MODE(KERNAL_MODE), .SA_INTERRUPTS_IN_DEPTH_B(SA_INTERRUPTS_IN_DEPTH_B),
    .SA_USER_PROGRAM_ID_B(SA_USER_PROGRAM_ID_B), .WRITE_ENABLE_B(WRITE_ENABLE_B), .RESET(RESET_t),
    .KERNAL_MODE_B(KERNAL_MODE_B), .ENTER_INTERRUPT(ENTER_INTERRUPT), .READ_BANK_REMAP_B(READ_BANK_REMAP_B),
    .D_IN(D));  // open: USER_MODE_ABILITY
  // Probe on n16_bit_latch_lvc16373_1_p7
  // Probe on n16_bit_latch_lvc16373_1_p8
  not not_6 (not_6_out, READ_BANK_REMAP_B);
  // Probe on D
  // Probe on D
  assign D = not_5_out ? KERNAL_ROM_data : 8'bz;  // Controlled_Buffer controlled_buffer_1
  // Probe on USER_PROGRAM_ID
  // Probe on MRAM_A16_23
  // Probe on kernal_user_mode_1_interrupt_depth
  or or_4 (or_4_out, READ_ENABLE_B, n8_bit_comparator_f521_1_p4);
  nor nor_1 (nor_1_out, WRITE_ENABLE_B, n8_bit_comparator_f521_1_p4);
  or or_5 (or_5_out, MAIN_MEMORY_VALID_B, not_6_out, DATA_TRANSMIT_B);
  // _8_bit_Comparator__F521 8_bit_comparator_f521_1: pin names not known; wires that end beside it: DEVICE_VALID_B, n16_bit_latch_lvc16373_1_p7, 8'h1, n8_bit_comparator_f521_1_p4
  // _8_bit_Bus_Transceiver__LVC4245 8_bit_bus_transceiver_lvc4245_2: pin names not known; wires that end beside it: or_5_out, D, RWB, n8_bit_bus_transceiver_lvc4245_2_p4
  // _8_bit_Latch__LVC573 8_bit_latch_lvc573_1: pin names not known; wires that end beside it: or_4_out, n8_bit_bi_latch_lvc543_2_p5, nor_1_out, n8_bit_bi_latch_lvc543_2_p5
  // Probe on n8_bit_bus_transceiver_lvc4245_2_p4
  Pull_Resistor #(.pull(1)) pull_resistor_13 (.node(pull_resistor_13_node));
  Pull_Resistor #(.pull(1)) pull_resistor_14 (.node(pull_resistor_14_node));
  // Probe on {MRAM_A16_23, A8_15, A0_7}
  not not_7 (not_7_out, PHI2);
  Memory_Transceiver memory_transceiver_1 (
    .WE_B(memory_transceiver_1_we_b), .MAIN_MEMORY_VALID_B(MAIN_MEMORY_VALID_B),
    .ADDRESS_IN_A0_23({MRAM_A16_23, A8_15, A0_7}),
    .MAIN_MEMORY_D_OUT(memory_transceiver_1_main_memory_d_out), .RWB(RWB),
    .MAIN_MEMORY_D_IN(memory_transceiver_1_main_memory_d_out), .MEMORY_LOCKOUT(MEMORY_LOCKOUT_CHANNEL_0),
    .OE_B(memory_transceiver_1_oe_b), .MPU_D_IN(n8_bit_bus_transceiver_lvc4245_2_p4),
    .MPU_D_OUT(n8_bit_bus_transceiver_lvc4245_2_p4), .RWB_B(RWB_B),
    .ADDRESS_OUT_A0_23(memory_transceiver_1_address_out_a0_23));
  Memory_Lockout_And_Generator memory_lockout_and_generator_1 (
    .NMI_B(NMIB_LOCKOUT_CHANNEL_0), .MAIN_MEMORY_VALID_3_B(pull_resistor_14_node),
    .LOCKOUT(MEMORY_LOCKOUT_CHANNEL_0), .RESET(RESET_t), .ADDRESS_IN_A0_23(24'h4aaaaa),
    .WE_B(memory_transceiver_1_oe_b), .MAIN_MEMORY_VALID_1_B(MAIN_MEMORY_VALID_B),
    .MAIN_MEMORY_VALID_2_B(pull_resistor_13_node), .SLOW_SELECTOR(SLW), .GATEWAY_ENABLE_B(SEL0),
    .OE_B(memory_transceiver_1_we_b), .ADDRESS_OUT_A0_23(memory_transceiver_1_address_out_a0_23));
  Instruction_Counter instruction_counter_1 (
    .COUNT(instruction_counter_1_count), .READ_ENABLE_B(READ_ENABLE_B), .OEB_C8_15(SA_INSTRUCTION_COUNTER_1),
    .D_OUT(D), .A0(A0_7[0]), .OEB_C0_7(SA_INSTRUCTION_COUNTER_0), .RESET(RESET_t),
    .OPCODE_ADDRESS(OPCODE_ADDRESS), .OEB_C24_31(SA_INSTRUCTION_COUNTER_3),
    .OEB_C16_23(SA_INSTRUCTION_COUNTER_2), .PHI2_B(not_7_out));
  // Probe on instruction_counter_1_count
  // Probe on memory_transceiver_1_address_out_a0_23
  // Probe on memory_transceiver_1_main_memory_d_out
  Pull_Resistor pull_resistor_15 (.node(pull_resistor_15_node));
  Pull_Resistor pull_resistor_16 (.node(pull_resistor_16_node));
  Pull_Resistor #(.pull(1)) pull_resistor_17 (.node(pull_resistor_17_node));
  Pull_Resistor pull_resistor_18 (.node(pull_resistor_18_node));
  Pull_Resistor pull_resistor_19 (.node(pull_resistor_19_node));
  Pull_Resistor pull_resistor_20 (.node(pull_resistor_20_node));
  Pull_Resistor #(.pull(1)) pull_resistor_21 (.node(pull_resistor_21_node));
  Pull_Resistor pull_resistor_22 (.node(pull_resistor_22_node));
  Pull_Resistor pull_resistor_23 (.node(pull_resistor_23_node));
  Pull_Resistor pull_resistor_24 (.node(pull_resistor_24_node));
  Pull_Resistor #(.pull(1)) pull_resistor_25 (.node(pull_resistor_25_node));
  Pull_Resistor pull_resistor_26 (.node(pull_resistor_26_node));
  Main_Memory_Gateway main_memory_gateway_1 (
    .MEMORY_WEB_IN(memory_transceiver_1_we_b), .MADDRESS_OUT_A0_23(main_memory_gateway_1_maddress_out_a0_23),
    .ADDRESS_IN_A0_23(memory_transceiver_1_address_out_a0_23), .GATEWAY_ENABLE_B(SEL6),
    .D_OUT_RIGHT(main_memory_gateway_1_d_out_right), .D_OUT_LEFT(memory_transceiver_1_main_memory_d_out),
    .D_IN_LEFT(memory_transceiver_1_main_memory_d_out), .MEMORY_OEB_IN(memory_transceiver_1_oe_b),
    .D_IN_RIGHT(main_memory_gateway_1_d_out_right), .MEMORY_OEB_OUT(main_memory_gateway_1_memory_oeb_out),
    .MEMORY_WEB_OUT(main_memory_gateway_1_memory_web_out));
  Main_Memory_Gateway main_memory_gateway_2 (
    .MEMORY_WEB_IN(pull_resistor_17_node), .MADDRESS_OUT_A0_23(main_memory_gateway_1_maddress_out_a0_23),
    .ADDRESS_IN_A0_23(pull_resistor_15_node), .GATEWAY_ENABLE_B(SEL0),
    .D_OUT_RIGHT(main_memory_gateway_1_d_out_right), .D_OUT_LEFT(pull_resistor_18_node),
    .D_IN_LEFT(pull_resistor_18_node), .MEMORY_OEB_IN(pull_resistor_16_node),
    .D_IN_RIGHT(main_memory_gateway_1_d_out_right), .MEMORY_OEB_OUT(main_memory_gateway_1_memory_oeb_out),
    .MEMORY_WEB_OUT(main_memory_gateway_1_memory_web_out));
  Main_Memory_Gateway main_memory_gateway_3 (
    .MEMORY_WEB_IN(pull_resistor_21_node), .MADDRESS_OUT_A0_23(main_memory_gateway_1_maddress_out_a0_23),
    .ADDRESS_IN_A0_23(pull_resistor_19_node), .GATEWAY_ENABLE_B(SEL2),
    .D_OUT_RIGHT(main_memory_gateway_1_d_out_right), .D_OUT_LEFT(pull_resistor_22_node),
    .D_IN_LEFT(pull_resistor_22_node), .MEMORY_OEB_IN(pull_resistor_20_node),
    .D_IN_RIGHT(main_memory_gateway_1_d_out_right), .MEMORY_OEB_OUT(main_memory_gateway_1_memory_oeb_out),
    .MEMORY_WEB_OUT(main_memory_gateway_1_memory_web_out));
  Main_Memory_Gateway main_memory_gateway_4 (
    .MEMORY_WEB_IN(pull_resistor_25_node), .MADDRESS_OUT_A0_23(main_memory_gateway_1_maddress_out_a0_23),
    .ADDRESS_IN_A0_23(pull_resistor_23_node), .GATEWAY_ENABLE_B(SEL4),
    .D_OUT_RIGHT(main_memory_gateway_1_d_out_right), .D_OUT_LEFT(pull_resistor_26_node),
    .D_IN_LEFT(pull_resistor_26_node), .MEMORY_OEB_IN(pull_resistor_24_node),
    .D_IN_RIGHT(main_memory_gateway_1_d_out_right), .MEMORY_OEB_OUT(main_memory_gateway_1_memory_oeb_out),
    .MEMORY_WEB_OUT(main_memory_gateway_1_memory_web_out));
  // Probe on main_memory_gateway_1_maddress_out_a0_23
  // Probe on main_memory_gateway_1_d_out_right
  Pull_Resistor pull_resistor_27 (.node(pull_resistor_27_node));
  Pull_Resistor #(.pull(1)) pull_resistor_28 (.node(pull_resistor_28_node));
  // _3_to_8_Decoder__LVC138 3_to_8_decoder_lvc138_1: pin names not known; wires that end beside it: pull_resistor_27_node, pull_resistor_27_node, main_memory_gateway_1_maddress_out_a0_23[23:21], pull_resistor_28_node, n3_to_8_decoder_lvc138_1_p5
  not not_8 (not_8_out, FST);
  or or_6 (or_6_out, main_memory_gateway_1_memory_web_out, not_8_out);
  // Probe on main_memory_gateway_1_maddress_out_a0_23[20:0]
  LED led_18 (.in(main_memory_gateway_1_memory_oeb_out));
  LED led_19 (.in(or_6_out));
  LED led_20 (.in(n3_to_8_decoder_lvc138_1_p5[2]));
  LED led_21 (.in(or_6_out));
  LED led_22 (.in(main_memory_gateway_1_memory_oeb_out));
  LED led_23 (.in(n3_to_8_decoder_lvc138_1_p5[3]));
  LED led_24 (.in(or_6_out));
  LED led_25 (.in(main_memory_gateway_1_memory_oeb_out));
  LED led_26 (.in(n3_to_8_decoder_lvc138_1_p5[4]));
  LED led_27 (.in(or_6_out));
  LED led_28 (.in(main_memory_gateway_1_memory_oeb_out));
  LED led_29 (.in(n3_to_8_decoder_lvc138_1_p5[5]));
  LED led_30 (.in(or_6_out));
  LED led_31 (.in(main_memory_gateway_1_memory_oeb_out));
  LED led_32 (.in(n3_to_8_decoder_lvc138_1_p5[6]));
  LED led_33 (.in(or_6_out));
  LED led_34 (.in(main_memory_gateway_1_memory_oeb_out));
  LED led_35 (.in(n3_to_8_decoder_lvc138_1_p5[7]));
  RAM #(.trigger("high"), .\type ("nonvolatile"), .enables("line"), .addrWidth(21), .databus("bidir")) ram_1 (
    .addr(main_memory_gateway_1_maddress_out_a0_23[20:0]), .data(main_memory_gateway_1_d_out_right));  // open: we, oe, clk
  SRAM_Chipifier sram_chipifier_2 (
    .WEB(or_6_out), .OEB(main_memory_gateway_1_memory_oeb_out), .CEB(n3_to_8_decoder_lvc138_1_p5[2]));  // open: OE, E, WE
  RAM #(.enables("line"), .databus("bidir"), .\type ("nonvolatile"), .addrWidth(21), .trigger("high")) ram_2 (
    .addr(main_memory_gateway_1_maddress_out_a0_23[20:0]), .data(main_memory_gateway_1_d_out_right));  // open: we, oe, clk
  SRAM_Chipifier sram_chipifier_3 (
    .WEB(main_memory_gateway_1_memory_oeb_out), .OEB(or_6_out), .CEB(n3_to_8_decoder_lvc138_1_p5[3]));  // open: OE, E, WE
  RAM #(.\type ("nonvolatile"), .databus("bidir"), .addrWidth(21), .trigger("high"), .enables("line")) ram_3 (
    .addr(main_memory_gateway_1_maddress_out_a0_23[20:0]), .data(main_memory_gateway_1_d_out_right));  // open: we, oe, clk
  SRAM_Chipifier sram_chipifier_4 (
    .WEB(main_memory_gateway_1_memory_oeb_out), .OEB(or_6_out), .CEB(n3_to_8_decoder_lvc138_1_p5[4]));  // open: OE, E, WE
  RAM #(.addrWidth(21), .trigger("high"), .\type ("nonvolatile"), .databus("bidir"), .enables("line")) ram_4 (
    .addr(main_memory_gateway_1_maddress_out_a0_23[20:0]), .data(main_memory_gateway_1_d_out_right));  // open: we, oe, clk
  SRAM_Chipifier sram_chipifier_5 (
    .WEB(main_memory_gateway_1_memory_oeb_out), .OEB(or_6_out), .CEB(n3_to_8_decoder_lvc138_1_p5[5]));  // open: OE, E, WE
  RAM #(.\type ("nonvolatile"), .databus("bidir"), .addrWidth(21), .trigger("high"), .enables("line")) ram_5 (
    .addr(main_memory_gateway_1_maddress_out_a0_23[20:0]), .data(main_memory_gateway_1_d_out_right));  // open: we, oe, clk
  SRAM_Chipifier sram_chipifier_6 (
    .WEB(main_memory_gateway_1_memory_oeb_out), .OEB(or_6_out), .CEB(n3_to_8_decoder_lvc138_1_p5[6]));  // open: OE, E, WE
  RAM #(.\type ("nonvolatile"), .trigger("high"), .addrWidth(21), .enables("line"), .databus("bidir")) ram_6 (
    .addr(main_memory_gateway_1_maddress_out_a0_23[20:0]), .data(main_memory_gateway_1_d_out_right));  // open: we, oe, clk
  SRAM_Chipifier sram_chipifier_7 (
    .WEB(main_memory_gateway_1_memory_oeb_out), .OEB(or_6_out), .CEB(n3_to_8_decoder_lvc138_1_p5[7]));  // open: OE, E, WE
  // Probe on main_memory_gateway_1_d_out_right
  // Probe on main_memory_gateway_1_d_out_right
  // Helper__W65C816_Timing helper_w65c816_timing_1: pin names not known; wires that end beside it: PHI2, 4'b0110, 4'b0001, 4'b0110, 4'b0100, 4'b0001, 4'b0101, 4'b0001, 4'b0110, 4'b0010, 4'b0110, FST, T1, 4'b0100, 4'b0000, 4'b0111, 4'b0000, 4'b0011, 4'b0111, 4'b0111, 4'b0000, 4'b0011, 4'b0000, T2

  // Notes on the sheet:
  //   Device Channel 0
  //   contents of KERNAL_ROM (hex, n*v repeats v):
  //   16384*0 ad fc ff c9 2b e1 f0 2 0 0 e2 20 a9 a4 8d 12 70 a9 cc ad 12 70 1a 8d 12 70 a9 cc ad 12 70 c9
  //   a5 f0 2 0 0 a2 ef cd 9b ae c 6f ac e 6f a9 ff 8d 0 6f a9 42 8f 0 ff 1 a9 43 8f 1 ff 1 a9 0 48 a9 4
  //   48 a9 1c 48 8 40 41184*ff 18 fb c2 30 a9 ff 1 1b e2 20 a9 0 48 ab c2 20 5c 0 40 0 8b b c2 30 48 da
  //   5a 80 39 8b b c2 30 48 da 5a 80 30 8b b c2 30 48 da 5a 80 27 8b b c2 30 48 da 5a e2 20 a9 0 48 ab ae
  //   c 6f ac e 6f 80 12 8b b c2 30 48 da 5a 80 9 8b b c2 30 48 da 5a 80 0 c2 30 7a fa 68 2b ab 40 7771*ff
  //   5a e1 6f e1 51 e1 48 e1 0 0 3f e1 4*ff 78 e1 0 0 78 e1 78 e1 2b e1 78 e1
  //   32KB_ROM
endmodule

module Device_Bus_Testing (
  input  RESET,
  input  [1:0] MPU_0_DEVICE_CHANNEL,
  input  MPU_0_DEVICE_VALID_B,
  input  [5:0] MPU_0_DEVICE_IDENTIFIER,
  input  [3:0] MPU_0_DEVICE_ADDRESS,
  input  MPU_0_RWB,
  input  [7:0] MPU_0_D_IN,
  input  [7:0] CH_0_D_IN,
  input  [1:0] MPU_1_DEVICE_CHANNEL,
  input  MPU_1_DEVICE_VALID_B,
  input  [5:0] MPU_1_DEVICE_IDENTIFIER,
  input  [3:0] MPU_1_DEVICE_ADDRESS,
  input  MPU_1_RWB,
  input  [7:0] MPU_1_D_IN,
  input  [7:0] CH_1_D_IN,
  input  [1:0] MPU_2_DEVICE_CHANNEL,
  input  MPU_2_DEVICE_VALID,
  input  [5:0] MPU_2_DEVICE_IDENTIFIER,
  input  [3:0] MPU_2_DEVICE_ADDRESS,
  input  FST,
  input  MPU_2_RWB,
  input  SEL_4,
  input  SEL_6,
  input  [7:0] MPU_2_D_IN,
  input  [7:0] CH_2_D_IN,
  input  SEL_0,
  input  SEL_2,
  input  [1:0] MPU_3_DEVICE_CHANNEL,
  input  MPU_3_DEVICE_VALID,
  input  [5:0] MPU_3_DEVICE_IDENTIFIER,
  input  [3:0] MPU_3_DEVICE_ADDRESS,
  input  MPU_3_RWB,
  input  [7:0] MPU_3_D_IN,
  input  [7:0] CH_3_D_IN,
  output [5:0] CH_0_DEVICE_IDENTIFIER,
  output [3:0] CH_0_DEVICE_ADDRESS,
  output CH_0_RWB_B,
  output CH_0_RWB,
  output [7:0] CH_0_D_OUT,
  output [7:0] MPU_0_D_OUT,
  output [5:0] CH_1_DEVICE_IDENTIFIER,
  output [3:0] CH_1_DEVICE_ADDRESS,
  output CH_1_RWB,
  output CH_1_RWB_B,
  output [7:0] CH_1_D_OUT,
  output [7:0] MPU_1_D_OUT,
  output [5:0] CH_2_DEVICE_IDENTIFIER,
  output [3:0] CH_2_DEVICE_ADDRESS,
  output CH_2_RWB,
  output CH_2_RWB_B,
  output [7:0] CH_2_D_OUT,
  output [7:0] MPU_2_D_OUT,
  output [5:0] CH_3_DEVICE_IDENTIFIER,
  output [3:0] CH_3_DEVICE_ADDRESS,
  output CH_3_RWB,
  output CH_3_RWB_B,
  output [7:0] CH_3_D_OUT,
  output [7:0] MPU_3_D_OUT
);

  wire decoder_1_out0, decoder_1_out1, decoder_1_out2, decoder_1_out3,
       device_mpu_gateway_1_channel_device_valid_b, device_mpu_gateway_1_channel_rwb,
       device_strobe_1_channel_0_b, device_strobe_1_channel_1_b, device_strobe_1_channel_2_b,
       device_strobe_1_channel_3_b, FST_t, SEL0, SEL2, SEL4, SEL6;
  wire [1:0] counter_1_q;
  wire [3:0] device_mpu_gateway_1_channel_device_address;
  wire [5:0] device_mpu_gateway_1_channel_device_identifier;
  wire [7:0] device_mpu_gateway_1_channel_d_out;

  Counter #(.width(2), .max('h3)) counter_1 (.Q(counter_1_q), .clk(FST_t));  // open: load, D, count, carry, up, clr
  Clock clock_1 (.out(FST_t));
  not not_1 (SEL4, decoder_1_out0);
  not not_2 (SEL6, decoder_1_out1);
  not not_3 (SEL0, decoder_1_out2);
  not not_4 (SEL2, decoder_1_out3);
  Decoder #(.select(2)) decoder_1 (
    .out0(decoder_1_out0), .out1(decoder_1_out1), .out2(decoder_1_out2), .out3(decoder_1_out3),
    .sel(counter_1_q));  // open: en
  LED led_1 (.in(MPU_0_DEVICE_VALID_B));
  LED led_2 (.in(MPU_1_DEVICE_VALID_B));
  LED led_3 (.in(MPU_2_DEVICE_VALID));
  LED led_4 (.in(MPU_3_DEVICE_VALID));
  Device_MPU_Gateway device_mpu_gateway_1 (
    .MPU_DEVICE_VALID_B(MPU_0_DEVICE_VALID_B), .MPU_0_DEVICE_IDENTIFIER(MPU_0_DEVICE_IDENTIFIER),
    .CHANNEL_DEVICE_IDENTIFIER(device_mpu_gateway_1_channel_device_identifier), .MPU_D_OUT(MPU_0_D_OUT),
    .CHANNEL_DEVICE_ADDRESS(device_mpu_gateway_1_channel_device_address), .MPU_D_IN(MPU_0_D_IN),
    .MPU_RWB(MPU_0_RWB), .CHANNEL_D_IN(device_mpu_gateway_1_channel_d_out),
    .CHANNEL_DEVICE_VALID_B(device_mpu_gateway_1_channel_device_valid_b),
    .CHANNEL_RWB(device_mpu_gateway_1_channel_rwb), .MPU_0_DEVICE_ADDRESS(MPU_0_DEVICE_ADDRESS),
    .CHANNEL_D_OUT(device_mpu_gateway_1_channel_d_out), .SELECTOR_B(SEL4));
  Device_MPU_Gateway device_mpu_gateway_2 (
    .MPU_DEVICE_VALID_B(MPU_1_DEVICE_VALID_B), .MPU_0_DEVICE_IDENTIFIER(MPU_1_DEVICE_IDENTIFIER),
    .CHANNEL_DEVICE_IDENTIFIER(device_mpu_gateway_1_channel_device_identifier), .MPU_D_OUT(MPU_1_D_OUT),
    .CHANNEL_DEVICE_ADDRESS(device_mpu_gateway_1_channel_device_address), .MPU_D_IN(MPU_1_D_IN),
    .MPU_RWB(MPU_1_RWB), .CHANNEL_D_IN(device_mpu_gateway_1_channel_d_out),
    .CHANNEL_DEVICE_VALID_B(device_mpu_gateway_1_channel_device_valid_b),
    .CHANNEL_RWB(device_mpu_gateway_1_channel_rwb), .MPU_0_DEVICE_ADDRESS(MPU_1_DEVICE_ADDRESS),
    .CHANNEL_D_OUT(device_mpu_gateway_1_channel_d_out), .SELECTOR_B(SEL6));
  Device_MPU_Gateway device_mpu_gateway_3 (
    .MPU_DEVICE_VALID_B(MPU_2_DEVICE_VALID), .MPU_0_DEVICE_IDENTIFIER(MPU_2_DEVICE_IDENTIFIER),
    .CHANNEL_DEVICE_IDENTIFIER(device_mpu_gateway_1_channel_device_identifier), .MPU_D_OUT(MPU_2_D_OUT),
    .CHANNEL_DEVICE_ADDRESS(device_mpu_gateway_1_channel_device_address), .MPU_D_IN(MPU_2_D_IN),
    .MPU_RWB(MPU_2_RWB), .CHANNEL_D_IN(device_mpu_gateway_1_channel_d_out),
    .CHANNEL_DEVICE_VALID_B(device_mpu_gateway_1_channel_device_valid_b),
    .CHANNEL_RWB(device_mpu_gateway_1_channel_rwb), .MPU_0_DEVICE_ADDRESS(MPU_2_DEVICE_ADDRESS),
    .CHANNEL_D_OUT(device_mpu_gateway_1_channel_d_out), .SELECTOR_B(SEL0));
  Device_MPU_Gateway device_mpu_gateway_4 (
    .MPU_DEVICE_VALID_B(MPU_3_DEVICE_VALID), .MPU_0_DEVICE_IDENTIFIER(MPU_3_DEVICE_IDENTIFIER),
    .CHANNEL_DEVICE_IDENTIFIER(device_mpu_gateway_1_channel_device_identifier), .MPU_D_OUT(MPU_3_D_OUT),
    .CHANNEL_DEVICE_ADDRESS(device_mpu_gateway_1_channel_device_address), .MPU_D_IN(MPU_3_D_IN),
    .MPU_RWB(MPU_3_RWB), .CHANNEL_D_IN(device_mpu_gateway_1_channel_d_out),
    .CHANNEL_DEVICE_VALID_B(device_mpu_gateway_1_channel_device_valid_b),
    .CHANNEL_RWB(device_mpu_gateway_1_channel_rwb), .MPU_0_DEVICE_ADDRESS(MPU_3_DEVICE_ADDRESS),
    .CHANNEL_D_OUT(device_mpu_gateway_1_channel_d_out), .SELECTOR_B(SEL2));
  Device_Strobe device_strobe_1 (
    .Channel_2_B(device_strobe_1_channel_2_b), .SELECTOR_0_B(SEL4), .CHANNEL_1_NUMBER(MPU_1_DEVICE_CHANNEL),
    .Channel_3_B(device_strobe_1_channel_3_b), .Channel_0_B(device_strobe_1_channel_0_b),
    .Channel_1_B(device_strobe_1_channel_1_b), .RESET(RESET), .CHANNEL_0_NUMBER(MPU_0_DEVICE_CHANNEL),
    .DEVICE_1_VALID_B(MPU_1_DEVICE_VALID_B), .DEVICE_0_VALID_B(MPU_0_DEVICE_VALID_B), .SELECTOR_1_B(SEL6));
  Device_Strobe device_strobe_2 (
    .Channel_2_B(device_strobe_1_channel_2_b), .SELECTOR_0_B(SEL0), .CHANNEL_1_NUMBER(MPU_3_DEVICE_CHANNEL),
    .Channel_3_B(device_strobe_1_channel_3_b), .Channel_0_B(device_strobe_1_channel_0_b),
    .Channel_1_B(device_strobe_1_channel_1_b), .RESET(RESET), .CHANNEL_0_NUMBER(MPU_2_DEVICE_CHANNEL),
    .DEVICE_1_VALID_B(MPU_3_DEVICE_VALID), .DEVICE_0_VALID_B(MPU_2_DEVICE_VALID), .SELECTOR_1_B(SEL2));
  // Probe on device_mpu_gateway_1_channel_d_out
  // Probe on device_mpu_gateway_1_channel_d_out
  // Probe on device_mpu_gateway_1_channel_d_out
  // Probe on device_mpu_gateway_1_channel_d_out
  Device_Channel_Gateway device_channel_gateway_1 (
    .MPU_DEVICE_ADDRESS(device_mpu_gateway_1_channel_device_address),
    .MPU_D_IN(device_mpu_gateway_1_channel_d_out), .CHANNEL_D_IN(CH_0_D_IN),
    .MPU_RWB(device_mpu_gateway_1_channel_rwb), .CHANNEL_RWB(CH_0_RWB_B),
    .CHANNEL_DEVICE_IDENTIFIER(CH_0_DEVICE_IDENTIFIER), .SELECTOR_B(device_strobe_1_channel_0_b),
    .CHANNEL_RWB_B(CH_0_RWB), .CHANNEL_DEVICE_ADDRESS(CH_0_DEVICE_ADDRESS), .FST(FST_t),
    .CHANNEL_D_OUT(CH_0_D_OUT), .MPU_D_OUT(device_mpu_gateway_1_channel_d_out),
    .MPU_DEVICE_VALID_B(device_mpu_gateway_1_channel_device_valid_b),
    .MPU_DEVICE_IDENTIFIER(device_mpu_gateway_1_channel_device_identifier));
  Device_Channel_Gateway device_channel_gateway_2 (
    .MPU_DEVICE_ADDRESS(device_mpu_gateway_1_channel_device_address),
    .MPU_D_IN(device_mpu_gateway_1_channel_d_out), .CHANNEL_D_IN(CH_1_D_IN),
    .MPU_RWB(device_mpu_gateway_1_channel_rwb), .CHANNEL_RWB(CH_1_RWB),
    .CHANNEL_DEVICE_IDENTIFIER(CH_1_DEVICE_IDENTIFIER), .SELECTOR_B(device_strobe_1_channel_1_b),
    .CHANNEL_RWB_B(CH_1_RWB_B), .CHANNEL_DEVICE_ADDRESS(CH_1_DEVICE_ADDRESS), .FST(FST_t),
    .CHANNEL_D_OUT(CH_1_D_OUT), .MPU_D_OUT(device_mpu_gateway_1_channel_d_out),
    .MPU_DEVICE_VALID_B(device_mpu_gateway_1_channel_device_valid_b),
    .MPU_DEVICE_IDENTIFIER(device_mpu_gateway_1_channel_device_identifier));
  Device_Channel_Gateway device_channel_gateway_3 (
    .MPU_DEVICE_ADDRESS(device_mpu_gateway_1_channel_device_address),
    .MPU_D_IN(device_mpu_gateway_1_channel_d_out), .CHANNEL_D_IN(CH_2_D_IN),
    .MPU_RWB(device_mpu_gateway_1_channel_rwb), .CHANNEL_RWB(CH_2_RWB),
    .CHANNEL_DEVICE_IDENTIFIER(CH_2_DEVICE_IDENTIFIER), .SELECTOR_B(device_strobe_1_channel_2_b),
    .CHANNEL_RWB_B(CH_2_RWB_B), .CHANNEL_DEVICE_ADDRESS(CH_2_DEVICE_ADDRESS), .FST(FST_t),
    .CHANNEL_D_OUT(CH_2_D_OUT), .MPU_D_OUT(device_mpu_gateway_1_channel_d_out),
    .MPU_DEVICE_VALID_B(device_mpu_gateway_1_channel_device_valid_b),
    .MPU_DEVICE_IDENTIFIER(device_mpu_gateway_1_channel_device_identifier));
  Device_Channel_Gateway device_channel_gateway_4 (
    .MPU_DEVICE_ADDRESS(device_mpu_gateway_1_channel_device_address),
    .MPU_D_IN(device_mpu_gateway_1_channel_d_out), .CHANNEL_D_IN(CH_3_D_IN),
    .MPU_RWB(device_mpu_gateway_1_channel_rwb), .CHANNEL_RWB(CH_3_RWB),
    .CHANNEL_DEVICE_IDENTIFIER(CH_3_DEVICE_IDENTIFIER), .SELECTOR_B(device_strobe_1_channel_3_b),
    .CHANNEL_RWB_B(CH_3_RWB_B), .CHANNEL_DEVICE_ADDRESS(CH_3_DEVICE_ADDRESS), .FST(FST_t),
    .CHANNEL_D_OUT(CH_3_D_OUT), .MPU_D_OUT(device_mpu_gateway_1_channel_d_out),
    .MPU_DEVICE_VALID_B(device_mpu_gateway_1_channel_device_valid_b),
    .MPU_DEVICE_IDENTIFIER(device_mpu_gateway_1_channel_device_identifier));
endmodule

module SNES_Testing (
  input  [5:0] CHANNEL_DEVICE_IDENTIFIER,
  input  [3:0] CHANNEL_DEVICE_ADDRESS,
  input  CHANNEL_RWB,
  input  CHANNEL_RWB_B,
  input  RESET_B,
  input  [7:0] D_IN,
  output [7:0] D_OUT
);

  wire clock_1_out, CONTROLLER_CLOCK, CONTROLLER_LE, DONE_SHIFTING_B, not_1_out,
       random_snes_signal_1_controller_data, random_snes_signal_2_controller_data,
       random_snes_signal_3_controller_data, random_snes_signal_4_controller_data, SHIFT_IN_CLOCK,
       snes_controller_device_1_counter_reset_b, snes_controller_device_1_device_selected,
       snes_controller_device_1_oe_controller_0_high_b, snes_controller_device_1_oe_controller_0_low_b,
       snes_controller_device_1_oe_controller_1_high_b, snes_controller_device_1_oe_controller_1_low_b,
       snes_controller_device_1_oe_controller_2_high_b, snes_controller_device_1_oe_controller_2_low_b,
       snes_controller_device_1_oe_controller_3_high_b, snes_controller_device_1_oe_controller_3_low_b;
  wire [3:0] counter_1_q;
  wire [7:0] snes_input_board_1_shift_register_out;
  wire [15:0] random_snes_signal_1_value, random_snes_signal_2_value, random_snes_signal_3_value,
       random_snes_signal_4_value;

  not not_1 (not_1_out, CONTROLLER_LE);
  Counter #(.max('hf), .width(4)) counter_1 (
    .Q(counter_1_q), .clk(clock_1_out));  // open: load, D, count, carry, up, clr
  Clock clock_1 (.out(clock_1_out));
  LED led_1 (.in(snes_controller_device_1_device_selected));
  SNES_Controller_Device snes_controller_device_1 (
    .RESET_B(RESET_B), .OE_CONTROLLER_2_HIGH_B(snes_controller_device_1_oe_controller_2_high_b),
    .COUNTER_RESET_B(snes_controller_device_1_counter_reset_b),
    .CHANNEL_DEVICE_IDENTIFIER(CHANNEL_DEVICE_IDENTIFIER),
    .DEVICE_SELECTED(snes_controller_device_1_device_selected), .CHANNEL_RWB_B(CHANNEL_RWB_B),
    .OE_CONTROLLER_3_LOW_B(snes_controller_device_1_oe_controller_3_low_b),
    .CHANNEL_DEVICE_ADDRESS(CHANNEL_DEVICE_ADDRESS),
    .OE_CONTROLLER_1_HIGH_B(snes_controller_device_1_oe_controller_1_high_b),
    .OE_CONTROLLER_1_LOW_B(snes_controller_device_1_oe_controller_1_low_b),
    .SHIFT_REGISTER_IN(snes_input_board_1_shift_register_out), .CHANNEL_RWB(CHANNEL_RWB),
    .OE_CONTROLLER_0_HIGH_B(snes_controller_device_1_oe_controller_0_high_b),
    .OE_CONTROLLER_3_HIGH_B(snes_controller_device_1_oe_controller_3_high_b),
    .LATCH_RESET_B(DONE_SHIFTING_B), .OE_CONTROLLER_0_LOW_B(snes_controller_device_1_oe_controller_0_low_b),
    .D_OUT(D_OUT), .D_IN(D_IN), .OE_CONTROLLER_2_LOW_B(snes_controller_device_1_oe_controller_2_low_b));
  Random_SNES_Signal random_snes_signal_1 (
    .VALUE(random_snes_signal_1_value), .CONTROLLER_DATA(random_snes_signal_1_controller_data),
    .CONTROLLER_CLOCK(CONTROLLER_CLOCK), .TICKY_CLOCK(counter_1_q[0]), .CONTROLLER_LE(not_1_out));
  Random_SNES_Signal random_snes_signal_2 (
    .VALUE(random_snes_signal_2_value), .CONTROLLER_DATA(random_snes_signal_2_controller_data),
    .CONTROLLER_CLOCK(CONTROLLER_CLOCK), .TICKY_CLOCK(counter_1_q[1]), .CONTROLLER_LE(not_1_out));
  Random_SNES_Signal random_snes_signal_3 (
    .VALUE(random_snes_signal_3_value), .CONTROLLER_DATA(random_snes_signal_3_controller_data),
    .CONTROLLER_CLOCK(CONTROLLER_CLOCK), .TICKY_CLOCK(counter_1_q[2]), .CONTROLLER_LE(not_1_out));
  Random_SNES_Signal random_snes_signal_4 (
    .VALUE(random_snes_signal_4_value), .CONTROLLER_DATA(random_snes_signal_4_controller_data),
    .CONTROLLER_CLOCK(CONTROLLER_CLOCK), .TICKY_CLOCK(counter_1_q[3]), .CONTROLLER_LE(not_1_out));
  // Probe on random_snes_signal_1_value
  // Probe on random_snes_signal_2_value
  // Probe on random_snes_signal_3_value
  // Probe on random_snes_signal_4_value
  // Digital_Oscilloscope #(.nState(19)) digital_oscilloscope_1: pin names not known; wires that end beside it: counter_1_q[3], CONTROLLER_LE, CONTROLLER_CLOCK, SHIFT_IN_CLOCK
  SNES_Input_Board snes_input_board_1 (
    .OE_CONTROLLER_2_HIGH_B(snes_controller_device_1_oe_controller_2_high_b),
    .CONTROLLER_LATCH(CONTROLLER_LE),
    .OE_CONTROLLER_0_HIGH_B(snes_controller_device_1_oe_controller_0_high_b),
    .CONTROLLER_CLOCK(CONTROLLER_CLOCK), .CONTROLLER_DATA_1(random_snes_signal_2_controller_data),
    .CONTROLLER_DATA_2(random_snes_signal_3_controller_data),
    .OE_CONTROLLER_2_LOW_B(snes_controller_device_1_oe_controller_2_low_b),
    .OE_CONTROLLER_0_LOW_B(snes_controller_device_1_oe_controller_0_low_b),
    .COUNTER_RESET_B(snes_controller_device_1_counter_reset_b), .DONE_SHIFTING_B(DONE_SHIFTING_B),
    .OE_CONTROLLER_3_HIGH_B(snes_controller_device_1_oe_controller_3_high_b),
    .CONTROLLER_DATA_0(random_snes_signal_1_controller_data),
    .OE_CONTROLLER_1_HIGH_B(snes_controller_device_1_oe_controller_1_high_b),
    .SHIFT_IN_CLOCK(SHIFT_IN_CLOCK), .OE_CONTROLLER_1_LOW_B(snes_controller_device_1_oe_controller_1_low_b),
    .RESET_B(RESET_B), .CONTROLLER_DATA_3(random_snes_signal_4_controller_data),
    .SHIFT_REGISTER_OUT(snes_input_board_1_shift_register_out),
    .OE_CONTROLLER_3_LOW_B(snes_controller_device_1_oe_controller_3_low_b));
  // Probe on snes_input_board_1_shift_register_out
endmodule

module PS2_Testing (
  input  [5:0] CHANNEL_DEVICE_IDENTIFIER,
  input  [3:0] CHANNEL_DEVICE_ADDRESS,
  input  CHANNEL_RWB,
  input  CHANNEL_RWB_B,
  input  [7:0] D_IN,
  input  RESET_B,
  output [7:0] out_7
);

  wire clock_1_out, ps2_input_board_1_ps2_active_0, ps2_input_board_1_ps2_active_1,
       ps2_input_device_1_device_selected, ps2_input_device_1_oe_high_b, ps2_input_device_1_oe_low_b,
       ps2_input_device_1_reset_ps2_b, random_ps2_signal_1_ps2_clock, random_ps2_signal_1_ps2_data,
       random_ps2_signal_2_ps2_clock, random_ps2_signal_2_ps2_data;
  wire [3:0] counter_1_q;
  wire [7:0] ps2_input_board_1_fifo_out, random_ps2_signal_1_value, random_ps2_signal_2_value;

  Clock clock_1 (.out(clock_1_out));
  Counter #(.width(4), .max('hf)) counter_1 (
    .Q(counter_1_q), .clk(clock_1_out));  // open: load, D, count, carry, up, clr
  LED led_1 (.in(ps2_input_device_1_device_selected));
  PS2_Input_Device ps2_input_device_1 (
    .OE_HIGH_B(ps2_input_device_1_oe_high_b), .CHANNEL_RWB_B(CHANNEL_RWB_B),
    .RESET_PS2_B(ps2_input_device_1_reset_ps2_b), .CHANNEL_RWB(CHANNEL_RWB),
    .FIFO_IN(ps2_input_board_1_fifo_out), .DEVICE_SELECTED(ps2_input_device_1_device_selected),
    .D_OUT(out_7), .RESET_B(RESET_B), .CHANNEL_DEVICE_IDENTIFIER(CHANNEL_DEVICE_IDENTIFIER),
    .OE_LOW_B(ps2_input_device_1_oe_low_b), .D_IN(D_IN), .CHANNEL_DEVICE_ADDRESS(CHANNEL_DEVICE_ADDRESS));
  Random_PS2_Signal random_ps2_signal_1 (
    .VALUE(random_ps2_signal_1_value), .PS2_CLOCK(random_ps2_signal_1_ps2_clock),
    .PS2_DATA(random_ps2_signal_1_ps2_data), .GENERATOR_CLOCK(counter_1_q[2]));
  Random_PS2_Signal random_ps2_signal_2 (
    .VALUE(random_ps2_signal_2_value), .PS2_CLOCK(random_ps2_signal_2_ps2_clock),
    .PS2_DATA(random_ps2_signal_2_ps2_data), .GENERATOR_CLOCK(counter_1_q[3]));
  // Probe on random_ps2_signal_1_value
  // Probe on random_ps2_signal_2_value
  PS2_Input_Board ps2_input_board_1 (
    .OE_HIGH_BYTE_B(ps2_input_device_1_oe_high_b), .PS2_DATA_1(random_ps2_signal_2_ps2_data),
    .FIFO_OUT(ps2_input_board_1_fifo_out), .PS2_CLOCK_1(random_ps2_signal_2_ps2_clock),
    .RESET_B(ps2_input_device_1_reset_ps2_b), .PS2_ACTIVE_1(ps2_input_board_1_ps2_active_1),
    .OE_LOW_BYTE_B(ps2_input_device_1_oe_low_b), .PS2_ACTIVE_0(ps2_input_board_1_ps2_active_0),
    .PS2_CLOCK_0(random_ps2_signal_1_ps2_clock), .PS2_DATA_0(random_ps2_signal_1_ps2_data));
  LED led_2 (.in(ps2_input_board_1_ps2_active_0));
  LED led_3 (.in(ps2_input_board_1_ps2_active_1));
endmodule

module Random_PS2_Signal (
  input  GENERATOR_CLOCK,
  output PS2_DATA,
  output PS2_CLOCK,
  output [7:0] VALUE
);

  wire and_1_out, and_2_out, comparator_1_eq, comparator_1_gt, comparator_2_eq, comparator_2_gt,
       comparator_3_eq, comparator_3_lt, comparator_4_gt, comparator_5_eq, comparator_5_gt, counter_1_q,
       n8_bit_parallel_in_shift_lv165_1_p4, not_1_out, not_2_out, not_3_out, not_5_out, or_1_out, or_2_out,
       or_3_out, pull_resistor_6_node;
  wire [3:0] bitadder_1_out;
  wire [4:0] pull_resistor_3_node;
  wire [10:0] pull_resistor_2_node;
  wire [15:0] counter_2_q;

  Counter #(.max('h1), .width(1)) counter_1 (
    .Q(counter_1_q), .clk(GENERATOR_CLOCK), .clr(comparator_5_gt));  // open: load, D, count, carry, up
  Counter #(.max('hffff), .width(16)) counter_2 (
    .Q(counter_2_q), .clk(GENERATOR_CLOCK), .clr(comparator_5_gt));  // open: load, D, count, carry, up
  Comparator #(.width(16)) comparator_1 (
    .a(counter_2_q), .b(16'h1), .gt(comparator_1_gt), .eq(comparator_1_eq));  // open: lt
  Comparator #(.width(16)) comparator_2 (
    .a(counter_2_q), .b(16'h3), .gt(comparator_2_gt), .eq(comparator_2_eq));  // open: lt
  Comparator #(.width(16)) comparator_3 (
    .a(counter_2_q), .b(16'h18), .eq(comparator_3_eq), .lt(comparator_3_lt));  // open: gt
  Comparator #(.width(16)) comparator_4 (.a(counter_2_q), .b(16'h1a), .gt(comparator_4_gt));  // open: eq, lt
  Comparator #(.width(16)) comparator_5 (
    .a(counter_2_q), .b(16'h40), .gt(comparator_5_gt), .eq(comparator_5_eq));  // open: lt
  or or_1 (or_1_out, comparator_2_gt, comparator_2_eq);
  or or_2 (or_2_out, comparator_3_eq, comparator_3_lt);
  and and_1 (and_1_out, or_1_out, or_2_out);
  or or_3 (or_3_out, comparator_4_gt, GENERATOR_CLOCK);
  not not_1 (not_1_out, counter_1_q);
  and and_2 (and_2_out, not_1_out, and_1_out);
  // Random random_1: pin names not known; wires that end beside it: and_2_out, comparator_1_eq
  not not_2 (not_2_out, and_1_out);
  not not_3 (not_3_out, counter_1_q);
  BitAdder bitadder_1 (
    .in0({pull_resistor_2_node[2], pull_resistor_2_node[3], pull_resistor_2_node[4], pull_resistor_2_node[5], pull_resistor_2_node[6], pull_resistor_2_node[7], pull_resistor_2_node[8], pull_resistor_2_node[9]}),
    .out(bitadder_1_out));
  // Probe on bitadder_1_out
  Pull_Resistor pull_resistor_1 (.node(pull_resistor_2_node[10]));
  not not_4 (pull_resistor_2_node[1], bitadder_1_out[0]);
  Pull_Resistor #(.pull(1)) pull_resistor_2 (.node(pull_resistor_2_node[0]));
  Register register_1 (
    .D({pull_resistor_2_node[2], pull_resistor_2_node[3], pull_resistor_2_node[4], pull_resistor_2_node[5], pull_resistor_2_node[6], pull_resistor_2_node[7], pull_resistor_2_node[8], pull_resistor_2_node[9]}),
    .Q(VALUE), .clk(comparator_1_gt));  // open: en, clr
  Pull_Resistor pull_resistor_3 (.node(pull_resistor_3_node));
  not not_5 (not_5_out, comparator_1_eq);
  Pull_Resistor pull_resistor_4 ();  // open: node
  Pull_Resistor pull_resistor_5 ();  // open: node
  Pull_Resistor pull_resistor_6 (.node(pull_resistor_6_node));
  // _8_bit_parallel_in_shift__LV165 8_bit_parallel_in_shift_lv165_1: pin names not known; wires that end beside it: not_5_out, and_2_out, pull_resistor_2_node[10:3], n8_bit_parallel_in_shift_lv165_1_p4, PS2_DATA
  // _8_bit_parallel_in_shift__LV165 8_bit_parallel_in_shift_lv165_2: pin names not known; wires that end beside it: not_5_out, and_2_out, {pull_resistor_2_node[2:0], pull_resistor_3_node}, pull_resistor_6_node, n8_bit_parallel_in_shift_lv165_1_p4
  Pull_Resistor pull_resistor_7 (.node(n8_bit_parallel_in_shift_lv165_1_p4));
  or or_4 (PS2_CLOCK, not_3_out, not_2_out);
  // Digital_Oscilloscope #(.nState(32)) digital_oscilloscope_1: pin names not known; wires that end beside it: or_3_out, PS2_DATA, PS2_CLOCK, comparator_5_eq
endmodule

module Random_SNES_Signal (
  input  CONTROLLER_CLOCK,
  input  TICKY_CLOCK,
  input  CONTROLLER_LE,
  output CONTROLLER_DATA,
  output [15:0] VALUE
);

  wire pull_resistor_1_node;
  wire [4:0] counter_1_q;
  wire [15:0] n16_bit_latch_lvc16373_1_p2;

  Random #(.width(16)) random_1 ();  // open: clk, next, out, clr
  Pull_Resistor pull_resistor_1 (.node(pull_resistor_1_node));
  // _16_bit_Latch__LVC16373 16_bit_latch_lvc16373_1: pin names not known; wires that end beside it: TICKY_CLOCK, n16_bit_latch_lvc16373_1_p2, pull_resistor_1_node, pull_resistor_1_node, n16_bit_latch_lvc16373_1_p2[15:8], CONTROLLER_LE, n16_bit_latch_lvc16373_1_p2[7:0], CONTROLLER_LE, VALUE[15:8], VALUE[7:0]
  Counter #(.width(5), .max('h1f)) counter_1 (
    .Q(counter_1_q), .clk(CONTROLLER_CLOCK), .clr(CONTROLLER_LE));  // open: load, D, count, carry, up
  Multiplexer #(.select(5)) multiplexer_1 (
    .in1(VALUE[15]), .in2(VALUE[14]), .in3(VALUE[13]), .in4(VALUE[12]), .in5(VALUE[11]), .in6(VALUE[10]),
    .in7(VALUE[9]), .in8(VALUE[8]), .in9(VALUE[7]), .in10(VALUE[6]), .in11(VALUE[5]), .in12(VALUE[4]),
    .in13(VALUE[3]), .in14(VALUE[2]), .in15(VALUE[1]), .in16(VALUE[0]), .out(CONTROLLER_DATA),
    .sel(counter_1_q));  // open: in0, in17, in18, in19, in20, in21, in22, in23, in24, in25, in26, in27, in28, in29, in30, in31
endmodule

module SRAM_Chipifier (
  input  OEB,
  input  WEB,
  input  CEB,
  output OE,
  output WE,
  output E
);

  nor nor_1 (OE, OEB, CEB);
  nor nor_2 (WE, WEB, CEB);
  Pull_Resistor #(.pull(1)) pull_resistor_1 (.node(E));
endmodule

module Clock_Detector (
  input  CLOCK,
  input  TICKY_CLOCK,
  output CLOCK_DETECT_B
);

  wire and_1_out, and_2_out, and_3_out, and_4_out, and_5_out, and_6_out, d_ff_1_q, d_ff_1_qn, d_ff_2_q,
       d_ff_3_q, d_ff_4_q, d_ff_5_q, d_ff_6_q, d_ff_7_q, d_ff_8_q, d_ff_9_q, d_ff_10_q, d_ff_11_q, d_ff_12_q,
       d_ff_13_q;

  D_Flip_Flop d_ff_1 (.clk(TICKY_CLOCK), .D(d_ff_1_qn), .Q(d_ff_1_q), .Qn(d_ff_1_qn));  // open: preset, reset
  D_Flip_Flop d_ff_2 (.clk(d_ff_1_q), .D(CLOCK), .Q(d_ff_2_q));  // open: Qn, preset, reset
  D_Flip_Flop d_ff_3 (.clk(d_ff_1_q), .D(d_ff_8_q), .Q(d_ff_3_q));  // open: Qn, preset, reset
  D_Flip_Flop d_ff_4 (.clk(d_ff_1_q), .D(d_ff_9_q), .Q(d_ff_4_q));  // open: Qn, preset, reset
  D_Flip_Flop d_ff_5 (.clk(d_ff_1_q), .D(d_ff_10_q), .Q(d_ff_5_q));  // open: Qn, preset, reset
  D_Flip_Flop d_ff_6 (.clk(d_ff_1_q), .D(d_ff_11_q), .Q(d_ff_6_q));  // open: Qn, preset, reset
  D_Flip_Flop d_ff_7 (.clk(d_ff_1_q), .D(d_ff_12_q), .Q(d_ff_7_q));  // open: Qn, preset, reset
  D_Flip_Flop d_ff_8 (.clk(d_ff_1_q), .D(d_ff_2_q), .Q(d_ff_8_q));  // open: Qn, preset, reset
  D_Flip_Flop d_ff_9 (.clk(d_ff_1_q), .D(d_ff_3_q), .Q(d_ff_9_q));  // open: Qn, preset, reset
  D_Flip_Flop d_ff_10 (.clk(d_ff_1_q), .D(d_ff_4_q), .Q(d_ff_10_q));  // open: Qn, preset, reset
  D_Flip_Flop d_ff_11 (.clk(d_ff_1_q), .D(d_ff_5_q), .Q(d_ff_11_q));  // open: Qn, preset, reset
  D_Flip_Flop d_ff_12 (.clk(d_ff_1_q), .D(d_ff_6_q), .Q(d_ff_12_q));  // open: Qn, preset, reset
  D_Flip_Flop d_ff_13 (.clk(d_ff_1_q), .D(d_ff_7_q), .Q(d_ff_13_q));  // open: Qn, preset, reset
  and and_1 (and_1_out, d_ff_8_q, d_ff_2_q);
  and and_2 (and_2_out, d_ff_9_q, d_ff_3_q);
  and and_3 (and_3_out, d_ff_10_q, d_ff_4_q);
  and and_4 (and_4_out, d_ff_11_q, d_ff_5_q);
  and and_5 (and_5_out, d_ff_12_q, d_ff_6_q);
  and and_6 (and_6_out, d_ff_13_q, d_ff_7_q);
  and and_7 (CLOCK_DETECT_B, and_1_out, and_2_out, and_3_out, and_4_out, and_5_out, and_6_out);
endmodule

module Bidirectional_Monsters (
  input  RWB,
  input  ENABLE_B,
  output READ,
  output WRITE
);

  wire not_1_out, not_2_out;

  and and_1 (READ, RWB, not_1_out);
  not not_1 (not_1_out, ENABLE_B);
  and and_2 (WRITE, not_2_out, not_1_out);
  not not_2 (not_2_out, RWB);
endmodule
